// Logisim project cpu21-riscv.circ as structural Verilog: 26 circuits, main circuit ◇单周期RISC-V
module \单周期RISC_V  (
  input  IR1,
  input  IR2,
  input  IR3,
  output RegWrite,
  output MemWrite,
  output [31:0] PC,
  output [31:0] IR,
  output [31:0] RDin,
  output [31:0] MDin,
  output [31:0] LedData
);

  wire alu_1_equal, and_1_out, and_2_out, and_3_out, Auipc, BGE, Byte, CanBe, CLK, clock_1_out,
       comparator_1_eq, comparator_2_eq, comparator_3_eq, comparator_4_eq, comparator_4_lt, d_ff_2_q, Ecall,
       Geq, Go, halt, IR1_t, IR2_t, IR3_t, IRA, IRB, IRC, JAL, JALR, Less, MemToReg, nand_1_out, nand_2_out,
       not_1_out, not_2_out, not_3_out, not_4_out, or_5_out, or_6_out, S_type, UERT, W1, W2, W3,
       \单周期硬布线控制器_1_alu_src , \单周期硬布线控制器_1_beq , \单周期硬布线控制器_1_bne ;
  wire [1:0] multiplexer_8_out;
  wire [3:0] AluOP;
  wire [4:0] multiplexer_1_out, multiplexer_2_out;
  wire [12:0] CNT_num;
  wire [15:0] \总周期数 ;
  wire [31:0] adder_2_out, adder_3_out, adder_4_out, AluResult, and_4_out, bit_extender_1_out,
       bit_extender_2_out, bit_extender_3_out, bit_extender_4_out, bit_extender_5_out, bit_extender_6_out,
       mips_ram_1_dataout, multiplexer_3_out, multiplexer_4_out, multiplexer_5_out, multiplexer_6_out,
       multiplexer_9_out, multiplexer_10_out, multiplexer_11_out, NextPC, PC_4, regifile_1_r1, shifter_1_out,
       shifter_2_out, shifter_3_out;

  Button \u_继续运行  (.out(Go));
  Button _1 (.out(IRA));
  Button _2 (.out(IRB));
  Button _3 (.out(IRC));
  LED #(.active("true")) led_1 (.in(W1));
  LED #(.active("true")) led_2 (.in(W2));
  LED #(.active("true")) led_3 (.in(W3));
  Hex_Digit_Display hex_digit_display_1 (.value(LedData[31:28]));  // open: dp
  Register #(.width(32), .trigger("rising"), .Select("low")) u_PC (
    .D(NextPC), .en(not_1_out), .Q(PC), .clk(CLK));  // open: clr
  not not_1 (not_1_out, halt);
  Hex_Digit_Display hex_digit_display_2 (.value(LedData[23:20]));  // open: dp
  Hex_Digit_Display hex_digit_display_3 (.value(LedData[27:24]));  // open: dp
  Adder #(.width(32)) adder_1 (.a(PC), .b(32'h4), .out(PC_4));  // open: cin, cout
  Hex_Digit_Display hex_digit_display_4 (.value(LedData[15:12]));  // open: dp
  Hex_Digit_Display hex_digit_display_5 (.value(LedData[19:16]));  // open: dp
  // RiscV_Probe riscv_probe_1: pin names not known; wires that end beside it: IR
  Hex_Digit_Display hex_digit_display_6 (.value(LedData[11:8]));  // open: dp
  Hex_Digit_Display hex_digit_display_7 (.value(LedData[7:4]));  // open: dp
  // Probe on \总周期数 
  ROM #(.addrWidth(10), .dataWidth(32), .Select("high")) rom_1 (.addr(PC[11:2]), .data(IR));
  Hex_Digit_Display hex_digit_display_8 (.value(LedData[3:0]));  // open: dp
  \单周期硬布线控制器  \u_单周期硬布线控制器_1  (
    .Funct({IR[30], IR[25], IR[14:12]}), .OP(IR[6:2]), .ALU_OP(AluOP), .MemToReg(MemToReg),
    .MemWrite(MemWrite), .ALU_SRC(\单周期硬布线控制器_1_alu_src ), .RegWrite(RegWrite), .ecall(Ecall),
    .S_type(S_type), .Jalr(JALR), .Beq(\单周期硬布线控制器_1_beq ), .JAL(JAL), .Bne(\单周期硬布线控制器_1_bne ), .in_3(IR[21]),
    .uret(UERT), .Auipc(Auipc), .Byte(Byte), .BGE(BGE));  // open: RsUsed, RtUsed, CSRRSI, CSRRCI
  // Probe on multiplexer_1_out
  Multiplexer #(.select(1), .width(5), .disabled("Z"), .enable("false")) multiplexer_1 (
    .in0(IR[19:15]), .in1(5'b10001), .out(multiplexer_1_out), .sel(Ecall));
  // Probe on multiplexer_2_out
  Multiplexer #(.select(1), .width(5), .disabled("Z"), .enable("false")) multiplexer_2 (
    .in0(IR[24:20]), .in1(5'b01010), .out(multiplexer_2_out), .sel(Ecall));
  assign bit_extender_1_out = {{20{IR[31]}}, IR[31:20]};  // Bit_Extender bit_extender_1
  assign bit_extender_2_out = {{20{IR[31]}}, {IR[31:25], IR[11:7]}};  // Bit_Extender bit_extender_2
  or or_1 (IR1_t, IR1, IRA);
  Multiplexer #(.select(1), .width(32), .disabled("Z"), .enable("false")) multiplexer_3 (
    .in0(bit_extender_1_out), .in1(bit_extender_2_out), .out(multiplexer_3_out), .sel(S_type));
  assign bit_extender_3_out = {{20{IR[31]}}, {IR[31], IR[7], IR[30:25], IR[11:8]}};  // Bit_Extender bit_extender_3
  Shifter #(.width(32), .shift("ll")) shifter_1 (.in(bit_extender_3_out), .\dist (5'b00001), .out(shifter_1_out));
  assign bit_extender_4_out = {{12{IR[31]}}, {IR[31], IR[19:12], IR[20], IR[30:21]}};  // Bit_Extender bit_extender_4
  Shifter #(.width(32), .shift("ll")) shifter_2 (.in(bit_extender_4_out), .\dist (5'b00001), .out(shifter_2_out));
  not not_2 (not_2_out, halt);
  or or_2 (IR2_t, IR2, IRB);
  Regifile regifile_1 (
    .Din(RDin), .Clk(CLK), .R1(regifile_1_r1), .R2(MDin), .WE(RegWrite), .W_num(IR[11:7]),
    .R1_num(multiplexer_1_out), .R2_num(multiplexer_2_out));
  Adder #(.width(32)) adder_2 (.a(shifter_1_out), .b(PC), .out(adder_2_out));  // open: cin, cout
  Adder #(.width(32)) adder_3 (.a(PC), .b(shifter_2_out), .out(adder_3_out));  // open: cin, cout
  Counter #(.width(16), .max('hffff), .ongoal("wrap"), .trigger("rising"), .behavior("new")) counter_1 (
    .count(not_2_out), .Q(\总周期数 ), .clk(CLK));  // open: load, D, carry, clr, preset, down
  Multiplexer #(.select(1), .width(32), .disabled("Z"), .enable("false")) multiplexer_4 (
    .in0(multiplexer_6_out), .in1(adder_2_out), .out(multiplexer_4_out), .sel(CanBe));
  or or_3 (IR3_t, IR3, IRC);
  Multiplexer #(.select(1), .width(32), .disabled("Z"), .enable("false")) multiplexer_5 (
    .in0(MDin), .in1(multiplexer_3_out), .out(multiplexer_5_out), .sel(\单周期硬布线控制器_1_alu_src ));
  Multiplexer #(.select(1), .width(32), .disabled("Z"), .enable("false")) multiplexer_6 (
    .in0(PC_4), .in1(and_4_out), .out(multiplexer_6_out), .sel(JALR));
  Multiplexer #(.select(1), .width(32), .disabled("Z"), .enable("false")) multiplexer_7 (
    .in0(multiplexer_4_out), .in1(adder_3_out), .out(NextPC), .sel(JAL));
  and and_1 (and_1_out, \单周期硬布线控制器_1_beq , alu_1_equal);
  and and_2 (and_2_out, \单周期硬布线控制器_1_bne , not_3_out);
  not not_3 (not_3_out, alu_1_equal);
  and and_3 (and_3_out, BGE, Geq);
  Comparator #(.width(32), .mode("twosComplement")) comparator_1 (
    .a(regifile_1_r1), .b(32'h22), .eq(comparator_1_eq));  // open: gt, lt
  ALU alu_1 (
    .X(regifile_1_r1), .Y(multiplexer_5_out), .AluOP(AluOP), .Equal(alu_1_equal), .Result(AluResult),
    .out_4(Geq), .out_6(Less));  // open: Result_2
  assign and_4_out = 32'hfffe & AluResult;  // AND_Gate and_4, 32 bits wide
  or or_4 (CanBe, and_1_out, and_2_out, and_3_out);
  not not_4 (not_4_out, nand_1_out);
  nand nand_1 (nand_1_out, comparator_1_eq, Ecall);
  Register #(.width(32), .trigger("rising"), .Select("low")) register_1 (
    .D(MDin), .en(not_4_out), .Q(LedData), .clk(CLK));  // open: clr
  Multiplexer #(.select(1), .width(2), .disabled("Z"), .enable("false")) multiplexer_8 (
    .in0(2'b00), .in1(2'b01), .out(multiplexer_8_out), .sel(Byte));
  MIPS_RAM mips_ram_1 (
    .\字节地址 (AluResult[11:0]), .Din(MDin), .DataOut(mips_ram_1_dataout), .CLK(CLK), .WE(MemWrite),
    .Mode(multiplexer_8_out));
  Multiplexer #(.select(1), .width(32), .disabled("Z"), .enable("false")) multiplexer_9 (
    .in0(AluResult), .in1(mips_ram_1_dataout), .out(multiplexer_9_out), .sel(MemToReg));
  assign bit_extender_5_out = {{31{1'b0}}, Less};  // Bit_Extender bit_extender_5
  D_Flip_Flop #(.trigger("falling"), .Pre_Clr_Positions("ABOVE_BELOW"), .NegatePresetClear("false"), .enable("true"), .NewFFLayout("true")) d_ff_1 (
    .clk(CLK), .D(nand_1_out), .Q(halt), .en(Ecall), .reset(Go));  // open: Qn, preset
  Multiplexer #(.select(1), .width(32), .disabled("Z"), .enable("false")) multiplexer_10 (
    .in0(multiplexer_9_out), .in1(bit_extender_5_out), .out(multiplexer_10_out), .sel(or_6_out));
  assign bit_extender_6_out = {{12{IR[31]}}, IR[31:12]};  // Bit_Extender bit_extender_6
  Shifter #(.width(32), .shift("ll")) shifter_3 (.in(bit_extender_6_out), .\dist (5'b01100), .out(shifter_3_out));
  D_Flip_Flop #(.trigger("high"), .Pre_Clr_Positions("LEGACY"), .NegatePresetClear("false"), .enable("true"), .NewFFLayout("false")) d_ff_2 (.Q(d_ff_2_q));  // open: clk, D, Qn, preset, en, reset
  // Probe on 13'h1
  Comparator #(.width(4), .mode("unsigned")) comparator_2 (
    .a(AluOP), .b(4'b1100), .eq(comparator_2_eq));  // open: gt, lt
  Comparator #(.width(4), .mode("unsigned")) comparator_3 (
    .a(AluOP), .b(4'b1011), .eq(comparator_3_eq));  // open: gt, lt
  Multiplexer #(.select(1), .width(32), .disabled("Z"), .enable("false")) multiplexer_11 (
    .in0(multiplexer_10_out), .in1(PC_4), .out(multiplexer_11_out), .sel(or_5_out));
  or or_5 (or_5_out, JAL, JALR);
  Adder #(.width(32)) adder_4 (.a(shifter_3_out), .b(PC), .out(adder_4_out));  // open: cin, cout
  Comparator #(.width(13), .mode("twosComplement")) comparator_4 (
    .a(CNT_num), .b(13'h1), .eq(comparator_4_eq), .lt(comparator_4_lt));  // open: gt
  Clock #(.highDuration(1), .lowDuration(1)) clock_1 (.out(clock_1_out));
  or or_6 (or_6_out, comparator_2_eq, comparator_3_eq);
  Multiplexer #(.select(1), .width(32), .disabled("Z"), .enable("false")) multiplexer_12 (
    .in0(multiplexer_11_out), .in1(adder_4_out), .out(RDin), .sel(Auipc));
  Counter #(.width(13), .max('h1fff), .ongoal("stay"), .trigger("rising"), .behavior("old")) counter_2 (
    .count(comparator_4_lt), .Q(CNT_num), .clk(clock_1_out));  // open: load, D, carry, clr, preset
  nand nand_2 (nand_2_out, d_ff_2_q, comparator_4_eq);
  assign CLK = nand_2_out ? clock_1_out : 1'bz;  // Controlled_Buffer controlled_buffer_1
  Pull_Resistor #(.pull(1)) pull_resistor_1 (.node(CLK));

  // Other names for the same wires on the sheet: UImm[19:0] = IR[31:12]; R2[31:0] = MDin

  // Notes on the sheet:
  //   中断源
  //   中断等待指示
  //   数码管输出应该用寄存器锁存，否则显示数据只能一闪而过
  //   数码管输出
  //   指令探针
  //   指令存储器
  //   指令字
  //   contents of rom_1 (hex, n*v repeats v):
  //   fff00293 7700493 849493 7748493 900533 2200893 73 1000e13 54c4b3 900533 2200893 73 fffe0e13 fe0e16e3
  //   a00893 73
  //   JAL
  //   JALR
  //   URET
  //   Beq
  //   Bne
  //   MemToReg
  //   MemWrite
  //   AluOP
  //   AluSrcB
  //   RegWrite
  //   为方便自动评测，需要输出PC，IR，寄存器堆写如数据RDin
  //   数据存储器
  //   RAM写使能MemWrite、RAM写入数据MDin等信号
  //   控制位
  //   暂停节拍，不能为0
  //   戳工具置1进入计数暂停模式，ctrl+k时钟自动运行到对应节拍暂停
  //   ctrl+k关闭时钟连续运行，将控制位置零，进入单步调试模式调试
  //   用这个时钟源需要去掉电路中的其他时钟源
  //   可计数暂停的时钟源
endmodule

// 单周期硬布线控制器
module \单周期硬布线控制器  (
  input  [4:0] OP,
  input  [4:0] Funct,
  input  in_3,
  output [3:0] ALU_OP,
  output uret,
  output MemToReg,
  output ecall,
  output MemWrite,
  output ALU_SRC,
  output RegWrite,
  output S_type,
  output Beq,
  output Bne,
  output Jalr,
  output JAL,
  output Auipc,
  output Byte,
  output BGE,
  output RtUsed,
  output CSRRCI,
  output CSRRSI,
  output RsUsed
);

  wire \控制信号自动生成_1_ecall ;

  \运算控制器自动生成  \u_运算控制器自动生成_1  (
    .OP2(OP[0]), .OP3(OP[1]), .OP4(OP[2]), .OP5(OP[3]), .OP6(OP[4]), .F12(Funct[0]), .F13(Funct[1]),
    .F14(Funct[2]), .F25(Funct[3]), .F30(Funct[4]), .S0(ALU_OP[0]), .S1(ALU_OP[1]), .S2(ALU_OP[2]),
    .S3(ALU_OP[3]));
  \控制信号自动生成  \u_控制信号自动生成_1  (
    .OP2(OP[0]), .OP3(OP[1]), .MemToReg(MemToReg), .OP4(OP[2]), .OP5(OP[3]), .OP6(OP[4]), .F12(Funct[0]),
    .MemWrite(MemWrite), .F13(Funct[1]), .F14(Funct[2]), .F25(Funct[3]), .F30(Funct[4]), .ALU_SRC(ALU_SRC),
    .RsUsed(RsUsed), .RtUsed(RtUsed), .RegWrite(RegWrite), .ecall(\控制信号自动生成_1_ecall ), .S_Type(S_type),
    .BEQ(Beq), .BNE(Bne), .JALR(Jalr), .JAL(JAL), .Auipc(Auipc), .Byte(Byte), .BGE(BGE), .CSRRSI(CSRRSI),
    .CSRRCI(CSRRCI));
  and and_1 (uret, in_3, \控制信号自动生成_1_ecall );
  and and_2 (ecall, ~in_3, \控制信号自动生成_1_ecall );  // AND_Gate

  // Other names for the same wires on the sheet: IR21 = in_3; OP_CODE[4:0] = OP

  // Notes on the sheet:
  //   运算器控制器，根据指令生成运算器功能选择信号
  //   控制信号生成，产生数据通路需要的其他控制信号
endmodule

// 运算器控制器
module \运算控制器自动生成  (
  input  OP2,
  input  OP3,
  input  OP4,
  input  OP5,
  input  OP6,
  input  F12,
  input  F13,
  input  F14,
  input  F25,
  input  F30,
  output S0,
  output S1,
  output S2,
  output S3
);

  wire and_1_out, and_2_out, and_3_out, and_4_out, and_5_out, and_6_out, and_7_out, and_8_out, and_9_out,
       and_10_out, and_11_out, and_12_out, and_13_out, and_14_out, and_15_out, and_16_out, and_17_out,
       and_18_out, and_19_out, and_20_out, and_21_out, and_22_out, and_23_out, and_24_out, and_25_out,
       and_26_out, and_27_out, and_28_out, and_29_out, and_30_out, and_31_out, and_32_out, and_33_out,
       and_34_out, and_35_out, and_36_out, and_37_out, and_38_out, and_39_out, not_1_out, not_2_out,
       not_3_out, not_4_out, not_5_out, not_6_out, not_7_out, not_8_out, not_9_out, not_10_out, not_11_out,
       not_12_out, not_13_out, not_14_out, not_15_out, not_16_out, not_17_out, not_18_out, not_19_out,
       not_20_out, not_21_out, not_22_out, not_23_out, not_24_out, not_25_out, not_26_out, not_27_out,
       not_28_out, not_29_out, not_30_out, not_31_out, not_32_out, not_33_out, not_34_out, not_35_out,
       not_36_out, not_37_out, not_38_out, not_39_out, not_40_out, not_41_out, not_42_out, not_43_out,
       not_44_out, not_45_out, not_46_out, not_47_out, not_48_out, not_49_out, not_50_out, not_51_out,
       not_52_out, not_53_out, not_54_out, not_55_out, not_56_out, not_57_out, not_58_out, not_59_out,
       not_60_out, not_61_out, not_62_out, not_63_out, not_64_out, not_65_out, not_66_out, not_67_out,
       not_68_out, not_69_out, not_70_out, not_71_out, not_72_out, not_73_out, not_74_out, not_75_out,
       not_76_out, not_77_out, not_78_out, not_79_out, not_80_out, not_81_out, not_82_out, not_83_out,
       not_84_out, not_85_out, not_86_out, not_87_out, not_88_out, not_89_out, not_90_out, not_91_out,
       not_92_out, not_93_out, not_94_out, not_95_out, not_96_out, not_97_out, not_98_out, not_99_out,
       not_100_out, not_101_out, not_102_out, not_103_out, not_104_out, not_105_out, not_106_out,
       not_107_out, not_108_out, not_109_out, not_110_out, not_111_out, not_112_out, not_113_out,
       not_114_out, not_115_out, not_116_out, not_117_out, not_118_out, not_119_out, not_120_out,
       not_121_out, not_122_out, not_123_out, not_124_out, not_125_out, not_126_out, not_127_out,
       not_128_out, not_129_out, not_130_out, not_131_out, not_132_out, not_133_out, not_134_out,
       not_135_out, not_136_out, not_137_out, not_138_out, not_139_out, not_140_out, not_141_out,
       not_142_out, not_143_out, not_144_out, not_145_out, not_146_out, not_147_out, not_148_out,
       not_149_out, not_150_out, not_151_out, not_152_out, not_153_out, not_154_out, not_155_out,
       not_156_out, not_157_out, not_158_out, not_159_out, not_160_out, not_161_out, not_162_out,
       not_163_out, not_164_out, not_165_out, not_166_out, not_167_out, not_168_out, not_169_out,
       not_170_out, not_171_out, not_172_out, not_173_out, not_174_out, not_175_out, not_176_out,
       not_177_out, not_178_out, not_179_out, not_180_out, not_181_out, not_182_out, not_183_out,
       not_184_out, not_185_out, not_186_out, not_187_out, not_188_out, not_189_out, not_190_out,
       not_191_out, not_192_out, not_193_out, not_194_out, not_195_out, not_196_out, not_197_out,
       not_198_out, not_199_out, not_200_out, not_201_out, not_202_out, not_203_out, not_204_out,
       not_205_out, not_206_out, not_207_out, not_208_out, not_209_out, not_210_out, not_211_out,
       not_212_out, not_213_out, not_214_out, not_215_out, not_216_out, not_217_out, not_218_out,
       not_219_out, not_220_out, not_221_out, not_222_out, not_223_out, not_224_out, not_225_out,
       not_226_out, not_227_out, not_228_out, not_229_out, not_230_out;

  not not_1 (not_1_out, F30);
  not not_2 (not_2_out, F25);
  not not_3 (not_3_out, F14);
  not not_4 (not_4_out, F13);
  not not_5 (not_5_out, F12);
  not not_6 (not_6_out, OP6);
  not not_7 (not_7_out, OP3);
  not not_8 (not_8_out, OP2);
  not not_9 (not_9_out, F30);
  not not_10 (not_10_out, F25);
  not not_11 (not_11_out, OP6);
  not not_12 (not_12_out, OP3);
  not not_13 (not_13_out, OP2);
  not not_14 (not_14_out, F30);
  not not_15 (not_15_out, F25);
  not not_16 (not_16_out, F14);
  not not_17 (not_17_out, F12);
  not not_18 (not_18_out, OP6);
  not not_19 (not_19_out, OP3);
  not not_20 (not_20_out, OP2);
  not not_21 (not_21_out, F14);
  not not_22 (not_22_out, F13);
  not not_23 (not_23_out, F12);
  not not_24 (not_24_out, OP6);
  not not_25 (not_25_out, OP5);
  not not_26 (not_26_out, OP3);
  not not_27 (not_27_out, OP2);
  not not_28 (not_28_out, OP6);
  not not_29 (not_29_out, OP5);
  not not_30 (not_30_out, OP3);
  not not_31 (not_31_out, OP2);
  not not_32 (not_32_out, F13);
  not not_33 (not_33_out, F12);
  not not_34 (not_34_out, OP6);
  not not_35 (not_35_out, OP5);
  not not_36 (not_36_out, OP3);
  not not_37 (not_37_out, OP2);
  not not_38 (not_38_out, F14);
  not not_39 (not_39_out, F12);
  not not_40 (not_40_out, OP6);
  not not_41 (not_41_out, OP5);
  not not_42 (not_42_out, OP3);
  not not_43 (not_43_out, OP2);
  not not_44 (not_44_out, F25);
  not not_45 (not_45_out, F13);
  not not_46 (not_46_out, OP6);
  not not_47 (not_47_out, OP5);
  not not_48 (not_48_out, OP3);
  not not_49 (not_49_out, OP2);
  not not_50 (not_50_out, F30);
  not not_51 (not_51_out, F25);
  not not_52 (not_52_out, F13);
  not not_53 (not_53_out, F12);
  not not_54 (not_54_out, OP6);
  not not_55 (not_55_out, OP3);
  not not_56 (not_56_out, OP2);
  not not_57 (not_57_out, F14);
  not not_58 (not_58_out, F13);
  not not_59 (not_59_out, F12);
  not not_60 (not_60_out, OP6);
  not not_61 (not_61_out, OP4);
  not not_62 (not_62_out, OP3);
  not not_63 (not_63_out, OP2);
  not not_64 (not_64_out, F13);
  not not_65 (not_65_out, OP4);
  not not_66 (not_66_out, OP3);
  not not_67 (not_67_out, OP2);
  not not_68 (not_68_out, F25);
  not not_69 (not_69_out, F14);
  not not_70 (not_70_out, F13);
  not not_71 (not_71_out, F12);
  not not_72 (not_72_out, OP6);
  not not_73 (not_73_out, OP3);
  not not_74 (not_74_out, OP2);
  not not_75 (not_75_out, F30);
  not not_76 (not_76_out, F25);
  not not_77 (not_77_out, OP6);
  not not_78 (not_78_out, OP3);
  not not_79 (not_79_out, OP2);
  not not_80 (not_80_out, F30);
  not not_81 (not_81_out, F25);
  not not_82 (not_82_out, F14);
  not not_83 (not_83_out, F12);
  not not_84 (not_84_out, OP6);
  not not_85 (not_85_out, OP3);
  not not_86 (not_86_out, OP2);
  not not_87 (not_87_out, OP6);
  not not_88 (not_88_out, OP5);
  not not_89 (not_89_out, OP3);
  not not_90 (not_90_out, OP2);
  not not_91 (not_91_out, F14);
  not not_92 (not_92_out, F12);
  not not_93 (not_93_out, OP6);
  not not_94 (not_94_out, OP5);
  not not_95 (not_95_out, OP3);
  not not_96 (not_96_out, OP2);
  not not_97 (not_97_out, F30);
  not not_98 (not_98_out, F25);
  not not_99 (not_99_out, F13);
  not not_100 (not_100_out, OP6);
  not not_101 (not_101_out, OP5);
  not not_102 (not_102_out, OP3);
  not not_103 (not_103_out, OP2);
  not not_104 (not_104_out, F14);
  not not_105 (not_105_out, F13);
  not not_106 (not_106_out, F12);
  not not_107 (not_107_out, OP4);
  not not_108 (not_108_out, OP3);
  not not_109 (not_109_out, OP2);
  not not_110 (not_110_out, F14);
  not not_111 (not_111_out, F13);
  not not_112 (not_112_out, OP4);
  not not_113 (not_113_out, OP3);
  not not_114 (not_114_out, OP2);
  not not_115 (not_115_out, F14);
  not not_116 (not_116_out, F13);
  not not_117 (not_117_out, F12);
  not not_118 (not_118_out, OP4);
  not not_119 (not_119_out, OP3);
  not not_120 (not_120_out, F13);
  not not_121 (not_121_out, OP4);
  not not_122 (not_122_out, OP3);
  not not_123 (not_123_out, OP2);
  not not_124 (not_124_out, F30);
  not not_125 (not_125_out, F25);
  not not_126 (not_126_out, F14);
  not not_127 (not_127_out, F13);
  not not_128 (not_128_out, F12);
  not not_129 (not_129_out, OP6);
  not not_130 (not_130_out, OP3);
  not not_131 (not_131_out, OP2);
  not not_132 (not_132_out, F25);
  not not_133 (not_133_out, F14);
  not not_134 (not_134_out, F13);
  not not_135 (not_135_out, F12);
  not not_136 (not_136_out, OP6);
  not not_137 (not_137_out, OP3);
  not not_138 (not_138_out, OP2);
  not not_139 (not_139_out, F30);
  not not_140 (not_140_out, F25);
  not not_141 (not_141_out, OP6);
  not not_142 (not_142_out, OP3);
  not not_143 (not_143_out, OP2);
  not not_144 (not_144_out, F30);
  not not_145 (not_145_out, F25);
  not not_146 (not_146_out, F14);
  not not_147 (not_147_out, OP6);
  not not_148 (not_148_out, OP3);
  not not_149 (not_149_out, OP2);
  not not_150 (not_150_out, F14);
  not not_151 (not_151_out, F13);
  not not_152 (not_152_out, F12);
  not not_153 (not_153_out, OP6);
  not not_154 (not_154_out, OP5);
  not not_155 (not_155_out, OP3);
  not not_156 (not_156_out, OP2);
  not not_157 (not_157_out, OP6);
  not not_158 (not_158_out, OP5);
  not not_159 (not_159_out, OP3);
  not not_160 (not_160_out, OP2);
  not not_161 (not_161_out, F14);
  not not_162 (not_162_out, F13);
  not not_163 (not_163_out, F12);
  not not_164 (not_164_out, OP4);
  not not_165 (not_165_out, OP3);
  not not_166 (not_166_out, OP2);
  not not_167 (not_167_out, F14);
  not not_168 (not_168_out, F13);
  not not_169 (not_169_out, OP4);
  not not_170 (not_170_out, OP3);
  not not_171 (not_171_out, OP2);
  not not_172 (not_172_out, F14);
  not not_173 (not_173_out, F13);
  not not_174 (not_174_out, F12);
  not not_175 (not_175_out, OP4);
  not not_176 (not_176_out, OP3);
  not not_177 (not_177_out, F14);
  not not_178 (not_178_out, F13);
  not not_179 (not_179_out, F12);
  not not_180 (not_180_out, OP6);
  not not_181 (not_181_out, OP4);
  not not_182 (not_182_out, OP3);
  not not_183 (not_183_out, OP2);
  not not_184 (not_184_out, F30);
  not not_185 (not_185_out, F25);
  not not_186 (not_186_out, F12);
  not not_187 (not_187_out, OP6);
  not not_188 (not_188_out, OP3);
  not not_189 (not_189_out, OP2);
  not not_190 (not_190_out, F30);
  not not_191 (not_191_out, F25);
  not not_192 (not_192_out, F14);
  not not_193 (not_193_out, F12);
  not not_194 (not_194_out, OP6);
  not not_195 (not_195_out, OP3);
  not not_196 (not_196_out, OP2);
  not not_197 (not_197_out, F30);
  not not_198 (not_198_out, F25);
  not not_199 (not_199_out, F14);
  not not_200 (not_200_out, OP6);
  not not_201 (not_201_out, OP3);
  not not_202 (not_202_out, OP2);
  not not_203 (not_203_out, F12);
  not not_204 (not_204_out, OP6);
  not not_205 (not_205_out, OP5);
  not not_206 (not_206_out, OP3);
  not not_207 (not_207_out, OP2);
  not not_208 (not_208_out, F13);
  not not_209 (not_209_out, F12);
  not not_210 (not_210_out, OP6);
  not not_211 (not_211_out, OP5);
  not not_212 (not_212_out, OP3);
  not not_213 (not_213_out, OP2);
  not not_214 (not_214_out, F14);
  not not_215 (not_215_out, F12);
  not not_216 (not_216_out, OP6);
  not not_217 (not_217_out, OP5);
  not not_218 (not_218_out, OP3);
  not not_219 (not_219_out, OP2);
  not not_220 (not_220_out, F30);
  not not_221 (not_221_out, F25);
  not not_222 (not_222_out, F13);
  not not_223 (not_223_out, F12);
  not not_224 (not_224_out, OP6);
  not not_225 (not_225_out, OP3);
  not not_226 (not_226_out, OP2);
  not not_227 (not_227_out, F13);
  not not_228 (not_228_out, OP4);
  not not_229 (not_229_out, OP3);
  not not_230 (not_230_out, OP2);
  and and_1 (and_1_out, not_1_out, not_2_out, not_3_out, not_4_out, not_5_out, not_6_out, OP5, OP4, not_7_out, not_8_out);
  and and_2 (and_2_out, not_9_out, not_10_out, F14, F13, F12, not_11_out, OP5, OP4, not_12_out, not_13_out);
  and and_3 (and_3_out, not_14_out, not_15_out, not_16_out, F13, not_17_out, not_18_out, OP5, OP4, not_19_out, not_20_out);
  and and_4 (and_4_out, not_21_out, not_22_out, not_23_out, not_24_out, not_25_out, OP4, not_26_out, not_27_out);
  and and_5 (and_5_out, F14, F13, F12, not_28_out, not_29_out, OP4, not_30_out, not_31_out);
  and and_6 (and_6_out, F14, not_32_out, not_33_out, not_34_out, not_35_out, OP4, not_36_out, not_37_out);
  and and_7 (and_7_out, not_38_out, F13, not_39_out, not_40_out, not_41_out, OP4, not_42_out, not_43_out);
  and and_8 (and_8_out, F30, not_44_out, F14, not_45_out, F12, not_46_out, not_47_out, OP4, not_48_out, not_49_out);
  and and_9 (and_9_out, not_50_out, not_51_out, F14, not_52_out, not_53_out, not_54_out, OP5, OP4, not_55_out, not_56_out);
  and and_10 (and_10_out, not_57_out, not_58_out, not_59_out, not_60_out, OP5, not_61_out, not_62_out, not_63_out);
  and and_11 (and_11_out, F14, not_64_out, F12, OP6, OP5, not_65_out, not_66_out, not_67_out);
  and and_12 (and_12_out, F30, not_68_out, not_69_out, not_70_out, not_71_out, not_72_out, OP5, OP4, not_73_out, not_74_out);
  and and_13 (and_13_out, not_75_out, not_76_out, F14, F13, F12, not_77_out, OP5, OP4, not_78_out, not_79_out);
  and and_14 (and_14_out, not_80_out, not_81_out, not_82_out, F13, not_83_out, not_84_out, OP5, OP4, not_85_out, not_86_out);
  and and_15 (and_15_out, F14, F13, F12, not_87_out, not_88_out, OP4, not_89_out, not_90_out);
  and and_16 (and_16_out, not_91_out, F13, not_92_out, not_93_out, not_94_out, OP4, not_95_out, not_96_out);
  and and_17 (and_17_out, not_97_out, not_98_out, F14, not_99_out, F12, not_100_out, not_101_out, OP4, not_102_out, not_103_out);
  and and_18 (and_18_out, not_104_out, not_105_out, not_106_out, OP6, OP5, not_107_out, not_108_out, not_109_out);
  and and_19 (and_19_out, not_110_out, not_111_out, F12, OP6, OP5, not_112_out, not_113_out, not_114_out);
  and and_20 (and_20_out, not_115_out, not_116_out, not_117_out, OP6, OP5, not_118_out, not_119_out, OP2);
  and and_21 (and_21_out, F14, not_120_out, F12, OP6, OP5, not_121_out, not_122_out, not_123_out);
  and and_22 (and_22_out, not_124_out, not_125_out, not_126_out, not_127_out, not_128_out, not_129_out, OP5, OP4, not_130_out, not_131_out);
  and and_23 (and_23_out, F30, not_132_out, not_133_out, not_134_out, not_135_out, not_136_out, OP5, OP4, not_137_out, not_138_out);
  and and_24 (and_24_out, not_139_out, not_140_out, F14, F13, F12, not_141_out, OP5, OP4, not_142_out, not_143_out);
  and and_25 (and_25_out, not_144_out, not_145_out, not_146_out, F13, F12, not_147_out, OP5, OP4, not_148_out, not_149_out);
  and and_26 (and_26_out, not_150_out, not_151_out, not_152_out, not_153_out, not_154_out, OP4, not_155_out, not_156_out);
  and and_27 (and_27_out, F14, F13, F12, not_157_out, not_158_out, OP4, not_159_out, not_160_out);
  and and_28 (and_28_out, not_161_out, not_162_out, not_163_out, OP6, OP5, not_164_out, not_165_out, not_166_out);
  and and_29 (and_29_out, not_167_out, not_168_out, F12, OP6, OP5, not_169_out, not_170_out, not_171_out);
  and and_30 (and_30_out, not_172_out, not_173_out, not_174_out, OP6, OP5, not_175_out, not_176_out, OP2);
  and and_31 (and_31_out, not_177_out, not_178_out, not_179_out, not_180_out, OP5, not_181_out, not_182_out, not_183_out);
  and and_32 (and_32_out, not_184_out, not_185_out, F14, F13, not_186_out, not_187_out, OP5, OP4, not_188_out, not_189_out);
  and and_33 (and_33_out, not_190_out, not_191_out, not_192_out, F13, not_193_out, not_194_out, OP5, OP4, not_195_out, not_196_out);
  and and_34 (and_34_out, not_197_out, not_198_out, not_199_out, F13, F12, not_200_out, OP5, OP4, not_201_out, not_202_out);
  and and_35 (and_35_out, F14, F13, not_203_out, not_204_out, not_205_out, OP4, not_206_out, not_207_out);
  and and_36 (and_36_out, F14, not_208_out, not_209_out, not_210_out, not_211_out, OP4, not_212_out, not_213_out);
  and and_37 (and_37_out, not_214_out, F13, not_215_out, not_216_out, not_217_out, OP4, not_218_out, not_219_out);
  and and_38 (and_38_out, not_220_out, not_221_out, F14, not_222_out, not_223_out, not_224_out, OP5, OP4, not_225_out, not_226_out);
  and and_39 (and_39_out, F14, not_227_out, F12, OP6, OP5, not_228_out, not_229_out, not_230_out);
  or or_1 (S0, and_1_out, and_2_out, and_3_out, and_4_out, and_5_out, and_6_out, and_7_out, and_8_out, and_9_out, and_10_out, and_11_out);
  or or_2 (S1, and_12_out, and_13_out, and_14_out, and_15_out, and_16_out, and_17_out, and_18_out, and_19_out, and_20_out, and_21_out);
  or or_3 (S2, and_22_out, and_23_out, and_24_out, and_25_out, and_26_out, and_27_out, and_28_out, and_29_out, and_30_out, and_31_out);
  or or_4 (S3, and_32_out, and_33_out, and_34_out, and_35_out, and_36_out, and_37_out, and_38_out, and_39_out);
endmodule

// 控制信号生成
module \控制信号自动生成  (
  input  OP2,
  input  OP3,
  input  OP4,
  input  OP5,
  input  OP6,
  input  F12,
  input  F13,
  input  F14,
  input  F25,
  input  F30,
  output MemToReg,
  output MemWrite,
  output ALU_SRC,
  output RsUsed,
  output RtUsed,
  output RegWrite,
  output ecall,
  output S_Type,
  output BEQ,
  output BNE,
  output JALR,
  output JAL,
  output Auipc,
  output Byte,
  output BGE,
  output CSRRSI,
  output CSRRCI
);

  wire and_3_out, and_4_out, and_5_out, and_6_out, and_7_out, and_8_out, and_9_out, and_10_out, and_11_out,
       and_12_out, and_13_out, and_14_out, and_15_out, and_16_out, and_17_out, and_18_out, and_19_out,
       and_20_out, and_21_out, and_22_out, and_23_out, and_24_out, and_25_out, and_26_out, and_27_out,
       and_28_out, and_29_out, and_30_out, and_31_out, and_32_out, and_33_out, and_34_out, and_35_out,
       and_36_out, and_37_out, and_38_out, and_39_out, not_1_out, not_2_out, not_3_out, not_4_out, not_5_out,
       not_6_out, not_7_out, not_8_out, not_9_out, not_10_out, not_11_out, not_12_out, not_13_out,
       not_14_out, not_15_out, not_16_out, not_17_out, not_18_out, not_19_out, not_20_out, not_21_out,
       not_22_out, not_23_out, not_24_out, not_25_out, not_26_out, not_27_out, not_28_out, not_29_out,
       not_30_out, not_31_out, not_32_out, not_33_out, not_34_out, not_35_out, not_36_out, not_37_out,
       not_38_out, not_39_out, not_40_out, not_41_out, not_42_out, not_43_out, not_44_out, not_45_out,
       not_46_out, not_47_out, not_48_out, not_49_out, not_50_out, not_51_out, not_52_out, not_53_out,
       not_54_out, not_55_out, not_56_out, not_57_out, not_58_out, not_59_out, not_60_out, not_61_out,
       not_62_out, not_63_out, not_64_out, not_65_out, not_66_out, not_67_out, not_68_out, not_69_out,
       not_70_out, not_71_out, not_72_out, not_73_out, not_74_out, not_75_out, not_76_out, not_77_out,
       not_78_out, not_79_out, not_80_out, not_81_out, not_82_out, not_83_out, not_84_out, not_85_out,
       not_86_out, not_87_out, not_88_out, not_89_out, not_90_out, not_91_out, not_92_out, not_93_out,
       not_94_out, not_95_out, not_96_out, not_97_out, not_98_out, not_99_out, not_100_out, not_101_out,
       not_102_out, not_103_out, not_104_out, not_105_out, not_106_out, not_107_out, not_108_out,
       not_109_out, not_110_out, not_111_out, not_112_out, not_113_out, not_114_out, not_115_out,
       not_116_out, not_117_out, not_118_out, not_119_out, not_120_out, not_121_out, not_122_out,
       not_123_out, not_124_out, not_125_out, not_126_out, not_127_out, not_128_out, not_129_out,
       not_130_out, not_131_out, not_132_out, not_133_out, not_134_out, not_135_out, not_136_out,
       not_137_out, not_138_out, not_139_out, not_140_out, not_141_out, not_142_out, not_143_out,
       not_144_out, not_145_out, not_146_out, not_147_out, not_148_out, not_149_out, not_150_out,
       not_151_out, not_152_out, not_153_out, not_154_out, not_155_out, not_156_out, not_157_out,
       not_158_out, not_159_out, not_160_out, not_161_out, not_162_out, not_163_out, not_164_out,
       not_165_out, not_166_out, not_167_out, not_168_out, not_169_out, not_170_out, not_171_out,
       not_172_out, not_173_out, not_174_out, not_175_out, not_176_out, not_177_out, not_178_out,
       not_179_out, not_180_out, not_181_out, not_182_out, not_183_out, not_184_out, not_185_out,
       not_186_out, not_187_out, not_188_out, not_189_out, not_190_out, not_191_out, not_192_out,
       not_193_out, not_194_out, not_195_out, not_196_out, not_197_out, not_198_out, not_199_out,
       not_200_out, not_201_out, not_202_out, not_203_out, not_204_out, not_205_out, not_206_out,
       not_207_out, not_208_out, not_209_out, not_210_out, not_211_out, not_212_out, not_213_out,
       not_214_out, not_215_out, not_216_out, not_217_out, not_218_out, not_219_out, not_220_out,
       not_221_out, not_222_out, not_223_out, not_224_out, not_225_out, not_226_out, not_227_out,
       not_228_out, not_229_out, not_230_out, not_231_out, not_232_out, not_233_out, not_234_out,
       not_235_out, not_236_out, not_237_out, not_238_out, not_239_out, not_240_out, not_241_out,
       not_242_out, not_243_out, not_244_out, not_245_out, not_246_out, not_247_out, not_248_out,
       not_249_out, not_250_out, not_251_out, not_252_out, not_253_out, not_254_out, not_255_out,
       not_256_out, not_257_out;

  not not_1 (not_1_out, OP2);
  not not_2 (not_2_out, OP3);
  not not_3 (not_3_out, OP4);
  not not_4 (not_4_out, OP5);
  not not_5 (not_5_out, OP6);
  not not_6 (not_6_out, F12);
  not not_7 (not_7_out, F14);
  not not_8 (not_8_out, OP2);
  not not_9 (not_9_out, OP3);
  not not_10 (not_10_out, OP4);
  not not_11 (not_11_out, OP6);
  not not_12 (not_12_out, F12);
  not not_13 (not_13_out, F14);
  not not_14 (not_14_out, OP2);
  not not_15 (not_15_out, OP3);
  not not_16 (not_16_out, OP5);
  not not_17 (not_17_out, OP6);
  not not_18 (not_18_out, F12);
  not not_19 (not_19_out, F14);
  not not_20 (not_20_out, OP2);
  not not_21 (not_21_out, OP3);
  not not_22 (not_22_out, OP4);
  not not_23 (not_23_out, OP6);
  not not_24 (not_24_out, F12);
  not not_25 (not_25_out, F14);
  not not_26 (not_26_out, OP2);
  not not_27 (not_27_out, OP3);
  not not_28 (not_28_out, OP5);
  not not_29 (not_29_out, OP6);
  not not_30 (not_30_out, F12);
  not not_31 (not_31_out, OP2);
  not not_32 (not_32_out, OP3);
  not not_33 (not_33_out, OP5);
  not not_34 (not_34_out, OP6);
  not not_35 (not_35_out, F13);
  not not_36 (not_36_out, F25);
  not not_37 (not_37_out, F30);
  not not_38 (not_38_out, OP2);
  not not_39 (not_39_out, OP3);
  not not_40 (not_40_out, OP5);
  not not_41 (not_41_out, OP6);
  not not_42 (not_42_out, F25);
  not not_43 (not_43_out, OP2);
  not not_44 (not_44_out, OP3);
  not not_45 (not_45_out, OP5);
  not not_46 (not_46_out, OP6);
  not not_47 (not_47_out, OP3);
  not not_48 (not_48_out, OP4);
  not not_49 (not_49_out, F12);
  not not_50 (not_50_out, F13);
  not not_51 (not_51_out, F14);
  not not_52 (not_52_out, OP2);
  not not_53 (not_53_out, OP3);
  not not_54 (not_54_out, OP4);
  not not_55 (not_55_out, OP6);
  not not_56 (not_56_out, F12);
  not not_57 (not_57_out, F14);
  not not_58 (not_58_out, OP2);
  not not_59 (not_59_out, OP3);
  not not_60 (not_60_out, OP4);
  not not_61 (not_61_out, F12);
  not not_62 (not_62_out, F13);
  not not_63 (not_63_out, F14);
  not not_64 (not_64_out, OP2);
  not not_65 (not_65_out, OP3);
  not not_66 (not_66_out, F12);
  not not_67 (not_67_out, F13);
  not not_68 (not_68_out, F14);
  not not_69 (not_69_out, F25);
  not not_70 (not_70_out, F30);
  not not_71 (not_71_out, OP3);
  not not_72 (not_72_out, OP4);
  not not_73 (not_73_out, F12);
  not not_74 (not_74_out, F13);
  not not_75 (not_75_out, F14);
  not not_76 (not_76_out, OP2);
  not not_77 (not_77_out, OP3);
  not not_78 (not_78_out, OP4);
  not not_79 (not_79_out, F13);
  not not_80 (not_80_out, OP2);
  not not_81 (not_81_out, OP3);
  not not_82 (not_82_out, OP5);
  not not_83 (not_83_out, OP6);
  not not_84 (not_84_out, F12);
  not not_85 (not_85_out, OP2);
  not not_86 (not_86_out, OP3);
  not not_87 (not_87_out, OP5);
  not not_88 (not_88_out, OP6);
  not not_89 (not_89_out, F13);
  not not_90 (not_90_out, F25);
  not not_91 (not_91_out, F30);
  not not_92 (not_92_out, OP2);
  not not_93 (not_93_out, OP3);
  not not_94 (not_94_out, OP6);
  not not_95 (not_95_out, F12);
  not not_96 (not_96_out, F13);
  not not_97 (not_97_out, F14);
  not not_98 (not_98_out, F25);
  not not_99 (not_99_out, OP2);
  not not_100 (not_100_out, OP3);
  not not_101 (not_101_out, OP6);
  not not_102 (not_102_out, F12);
  not not_103 (not_103_out, F25);
  not not_104 (not_104_out, F30);
  not not_105 (not_105_out, OP2);
  not not_106 (not_106_out, OP3);
  not not_107 (not_107_out, OP5);
  not not_108 (not_108_out, OP6);
  not not_109 (not_109_out, F25);
  not not_110 (not_110_out, OP2);
  not not_111 (not_111_out, OP3);
  not not_112 (not_112_out, OP5);
  not not_113 (not_113_out, OP6);
  not not_114 (not_114_out, OP2);
  not not_115 (not_115_out, OP3);
  not not_116 (not_116_out, OP6);
  not not_117 (not_117_out, F25);
  not not_118 (not_118_out, F30);
  not not_119 (not_119_out, OP2);
  not not_120 (not_120_out, OP3);
  not not_121 (not_121_out, OP4);
  not not_122 (not_122_out, OP6);
  not not_123 (not_123_out, F12);
  not not_124 (not_124_out, F14);
  not not_125 (not_125_out, OP2);
  not not_126 (not_126_out, OP3);
  not not_127 (not_127_out, OP4);
  not not_128 (not_128_out, F12);
  not not_129 (not_129_out, F13);
  not not_130 (not_130_out, F14);
  not not_131 (not_131_out, OP2);
  not not_132 (not_132_out, OP3);
  not not_133 (not_133_out, OP6);
  not not_134 (not_134_out, F12);
  not not_135 (not_135_out, F13);
  not not_136 (not_136_out, F14);
  not not_137 (not_137_out, F25);
  not not_138 (not_138_out, OP2);
  not not_139 (not_139_out, OP3);
  not not_140 (not_140_out, F12);
  not not_141 (not_141_out, F13);
  not not_142 (not_142_out, F14);
  not not_143 (not_143_out, F25);
  not not_144 (not_144_out, F30);
  not not_145 (not_145_out, OP2);
  not not_146 (not_146_out, OP3);
  not not_147 (not_147_out, OP4);
  not not_148 (not_148_out, F13);
  not not_149 (not_149_out, OP2);
  not not_150 (not_150_out, OP3);
  not not_151 (not_151_out, OP6);
  not not_152 (not_152_out, F12);
  not not_153 (not_153_out, F25);
  not not_154 (not_154_out, F30);
  not not_155 (not_155_out, OP2);
  not not_156 (not_156_out, OP3);
  not not_157 (not_157_out, OP6);
  not not_158 (not_158_out, F25);
  not not_159 (not_159_out, F30);
  not not_160 (not_160_out, OP2);
  not not_161 (not_161_out, OP3);
  not not_162 (not_162_out, OP5);
  not not_163 (not_163_out, OP6);
  not not_164 (not_164_out, F12);
  not not_165 (not_165_out, F14);
  not not_166 (not_166_out, OP2);
  not not_167 (not_167_out, OP3);
  not not_168 (not_168_out, OP6);
  not not_169 (not_169_out, F12);
  not not_170 (not_170_out, F13);
  not not_171 (not_171_out, F14);
  not not_172 (not_172_out, F25);
  not not_173 (not_173_out, OP2);
  not not_174 (not_174_out, OP3);
  not not_175 (not_175_out, OP6);
  not not_176 (not_176_out, F12);
  not not_177 (not_177_out, F25);
  not not_178 (not_178_out, F30);
  not not_179 (not_179_out, OP3);
  not not_180 (not_180_out, OP5);
  not not_181 (not_181_out, OP6);
  not not_182 (not_182_out, F12);
  not not_183 (not_183_out, OP3);
  not not_184 (not_184_out, OP5);
  not not_185 (not_185_out, OP6);
  not not_186 (not_186_out, F13);
  not not_187 (not_187_out, F25);
  not not_188 (not_188_out, F30);
  not not_189 (not_189_out, OP3);
  not not_190 (not_190_out, OP5);
  not not_191 (not_191_out, OP6);
  not not_192 (not_192_out, F25);
  not not_193 (not_193_out, OP3);
  not not_194 (not_194_out, OP5);
  not not_195 (not_195_out, OP6);
  not not_196 (not_196_out, OP2);
  not not_197 (not_197_out, OP3);
  not not_198 (not_198_out, OP6);
  not not_199 (not_199_out, F25);
  not not_200 (not_200_out, F30);
  not not_201 (not_201_out, OP4);
  not not_202 (not_202_out, F12);
  not not_203 (not_203_out, F13);
  not not_204 (not_204_out, F14);
  not not_205 (not_205_out, OP3);
  not not_206 (not_206_out, OP5);
  not not_207 (not_207_out, OP6);
  not not_208 (not_208_out, OP4);
  not not_209 (not_209_out, OP2);
  not not_210 (not_210_out, OP3);
  not not_211 (not_211_out, F12);
  not not_212 (not_212_out, F13);
  not not_213 (not_213_out, F14);
  not not_214 (not_214_out, F25);
  not not_215 (not_215_out, F30);
  not not_216 (not_216_out, OP2);
  not not_217 (not_217_out, OP3);
  not not_218 (not_218_out, OP4);
  not not_219 (not_219_out, OP6);
  not not_220 (not_220_out, F12);
  not not_221 (not_221_out, F14);
  not not_222 (not_222_out, OP2);
  not not_223 (not_223_out, OP3);
  not not_224 (not_224_out, OP4);
  not not_225 (not_225_out, F12);
  not not_226 (not_226_out, F13);
  not not_227 (not_227_out, F14);
  not not_228 (not_228_out, OP2);
  not not_229 (not_229_out, OP3);
  not not_230 (not_230_out, OP4);
  not not_231 (not_231_out, F13);
  not not_232 (not_232_out, F14);
  not not_233 (not_233_out, OP3);
  not not_234 (not_234_out, OP4);
  not not_235 (not_235_out, F12);
  not not_236 (not_236_out, F13);
  not not_237 (not_237_out, F14);
  not not_238 (not_238_out, OP4);
  not not_239 (not_239_out, OP3);
  not not_240 (not_240_out, OP5);
  not not_241 (not_241_out, OP6);
  not not_242 (not_242_out, OP2);
  not not_243 (not_243_out, OP3);
  not not_244 (not_244_out, OP4);
  not not_245 (not_245_out, OP6);
  not not_246 (not_246_out, F12);
  not not_247 (not_247_out, F13);
  not not_248 (not_248_out, F14);
  not not_249 (not_249_out, OP2);
  not not_250 (not_250_out, OP3);
  not not_251 (not_251_out, OP4);
  not not_252 (not_252_out, F13);
  not not_253 (not_253_out, F12);
  not not_254 (not_254_out, OP3);
  not not_255 (not_255_out, OP2);
  not not_256 (not_256_out, OP3);
  not not_257 (not_257_out, OP2);
  and and_1 (MemToReg, not_1_out, not_2_out, not_3_out, not_4_out, not_5_out, not_6_out, F13, not_7_out);
  and and_2 (MemWrite, not_8_out, not_9_out, not_10_out, OP5, not_11_out, not_12_out, not_13_out);
  and and_3 (and_3_out, not_14_out, not_15_out, not_16_out, not_17_out, not_18_out, F13, not_19_out);
  and and_4 (and_4_out, not_20_out, not_21_out, not_22_out, OP5, not_23_out, not_24_out, not_25_out);
  and and_5 (and_5_out, not_26_out, not_27_out, OP4, not_28_out, not_29_out, not_30_out);
  and and_6 (and_6_out, not_31_out, not_32_out, OP4, not_33_out, not_34_out, not_35_out, not_36_out, not_37_out);
  and and_7 (and_7_out, not_38_out, not_39_out, OP4, not_40_out, not_41_out, F14, not_42_out);
  and and_8 (and_8_out, not_43_out, not_44_out, OP4, not_45_out, not_46_out, F13, F14);
  and and_9 (and_9_out, OP2, not_47_out, not_48_out, OP5, OP6, not_49_out, not_50_out, not_51_out);
  and and_10 (and_10_out, not_52_out, not_53_out, not_54_out, not_55_out, not_56_out, F13, not_57_out);
  and and_11 (and_11_out, not_58_out, not_59_out, not_60_out, OP5, not_61_out, not_62_out, not_63_out);
  and and_12 (and_12_out, not_64_out, not_65_out, OP5, not_66_out, not_67_out, not_68_out, not_69_out, not_70_out);
  and and_13 (and_13_out, not_71_out, not_72_out, OP5, OP6, not_73_out, not_74_out, not_75_out);
  and and_14 (and_14_out, not_76_out, not_77_out, not_78_out, OP5, OP6, F12, not_79_out);
  and and_15 (and_15_out, not_80_out, not_81_out, OP4, not_82_out, not_83_out, not_84_out);
  and and_16 (and_16_out, not_85_out, not_86_out, OP4, not_87_out, not_88_out, not_89_out, not_90_out, not_91_out);
  and and_17 (and_17_out, not_92_out, not_93_out, OP4, not_94_out, not_95_out, not_96_out, not_97_out, not_98_out);
  and and_18 (and_18_out, not_99_out, not_100_out, OP4, not_101_out, not_102_out, not_103_out, not_104_out);
  and and_19 (and_19_out, not_105_out, not_106_out, OP4, not_107_out, not_108_out, F14, not_109_out);
  and and_20 (and_20_out, not_110_out, not_111_out, OP4, not_112_out, not_113_out, F13, F14);
  and and_21 (and_21_out, not_114_out, not_115_out, OP4, OP5, not_116_out, F13, not_117_out, not_118_out);
  and and_22 (and_22_out, not_119_out, not_120_out, not_121_out, OP5, not_122_out, not_123_out, not_124_out);
  and and_23 (and_23_out, not_125_out, not_126_out, not_127_out, OP5, not_128_out, not_129_out, not_130_out);
  and and_24 (and_24_out, not_131_out, not_132_out, OP5, not_133_out, not_134_out, not_135_out, not_136_out, not_137_out);
  and and_25 (and_25_out, not_138_out, not_139_out, OP5, not_140_out, not_141_out, not_142_out, not_143_out, not_144_out);
  and and_26 (and_26_out, not_145_out, not_146_out, not_147_out, OP5, OP6, F12, not_148_out);
  and and_27 (and_27_out, not_149_out, not_150_out, OP4, OP5, not_151_out, not_152_out, not_153_out, not_154_out);
  and and_28 (and_28_out, not_155_out, not_156_out, OP4, OP5, not_157_out, F13, not_158_out, not_159_out);
  and and_29 (and_29_out, not_160_out, not_161_out, not_162_out, not_163_out, not_164_out, F13, not_165_out);
  and and_30 (and_30_out, not_166_out, not_167_out, OP4, not_168_out, not_169_out, not_170_out, not_171_out, not_172_out);
  and and_31 (and_31_out, not_173_out, not_174_out, OP4, not_175_out, not_176_out, not_177_out, not_178_out);
  and and_32 (and_32_out, not_179_out, OP4, not_180_out, not_181_out, not_182_out);
  and and_33 (and_33_out, not_183_out, OP4, not_184_out, not_185_out, not_186_out, not_187_out, not_188_out);
  and and_34 (and_34_out, not_189_out, OP4, not_190_out, not_191_out, F14, not_192_out);
  and and_35 (and_35_out, not_193_out, OP4, not_194_out, not_195_out, F13, F14);
  and and_36 (and_36_out, not_196_out, not_197_out, OP4, OP5, not_198_out, F13, not_199_out, not_200_out);
  and and_37 (and_37_out, OP2, not_201_out, OP5, OP6, not_202_out, not_203_out, not_204_out);
  and and_38 (and_38_out, OP2, not_205_out, OP4, not_206_out, not_207_out);
  and and_39 (and_39_out, OP2, OP3, not_208_out, OP5, OP6);
  and and_40 (ecall, not_209_out, not_210_out, OP4, OP5, OP6, not_211_out, not_212_out, not_213_out, not_214_out, not_215_out);
  and and_41 (S_Type, not_216_out, not_217_out, not_218_out, OP5, not_219_out, not_220_out, not_221_out);
  and and_42 (BEQ, not_222_out, not_223_out, not_224_out, OP5, OP6, not_225_out, not_226_out, not_227_out);
  and and_43 (BNE, not_228_out, not_229_out, not_230_out, OP5, OP6, F12, not_231_out, not_232_out);
  and and_44 (JALR, OP2, not_233_out, not_234_out, OP5, OP6, not_235_out, not_236_out, not_237_out);
  and and_45 (JAL, OP2, OP3, not_238_out, OP5, OP6);
  and and_46 (Auipc, OP2, not_239_out, OP4, not_240_out, not_241_out);
  and and_47 (Byte, not_242_out, not_243_out, not_244_out, OP5, not_245_out, not_246_out, not_247_out, not_248_out);
  and and_48 (BGE, not_249_out, not_250_out, not_251_out, OP5, OP6, F12, not_252_out, F14);
  and and_49 (CSRRSI, F14, F13, not_253_out, OP6, OP5, OP4, not_254_out, not_255_out);
  and and_50 (CSRRCI, F14, F13, F12, OP6, OP5, OP4, not_256_out, not_257_out);
  or or_1 (ALU_SRC, and_3_out, and_4_out, and_5_out, and_6_out, and_7_out, and_8_out, and_9_out);
  or or_2 (RtUsed, and_22_out, and_23_out, and_24_out, and_25_out, and_26_out, and_27_out, and_28_out);
  or or_3 (RsUsed, and_10_out, and_11_out, and_12_out, and_13_out, and_14_out, and_15_out, and_16_out, and_17_out, and_18_out, and_19_out, and_20_out, and_21_out);
  or or_4 (RegWrite, and_29_out, and_30_out, and_31_out, and_32_out, and_33_out, and_34_out, and_35_out, and_36_out, and_37_out, and_38_out, and_39_out);
endmodule

// ALU
module ALU (
  input  [31:0] X,
  input  [31:0] Y,
  input  [3:0] AluOP,
  output out_4,
  output Equal,
  output out_6,
  output [31:0] Result,
  output [31:0] Result_2
);

  wire [0:0] comparator_1_lt, comparator_2_lt;
  wire [31:0] adder_1_out, AND_out, divider_1_out, divider_1_rem, multiplier_1_cout, multiplier_1_out,
       NOR_out, OR_out, shifter_1_out, shifter_2_out, shifter_3_out, subtractor_1_out, XOR_out;

  assign AND_out = X & Y;  // AND_Gate AND, 32 bits wide
  assign OR_out = X | Y;  // OR_Gate OR, 32 bits wide
  Shifter #(.width(32), .shift("ll")) shifter_1 (.in(X), .\dist (Y[4:0]), .out(shifter_1_out));
  Shifter #(.width(32), .shift("ar")) shifter_2 (.in(X), .\dist (Y[4:0]), .out(shifter_2_out));
  Shifter #(.width(32), .shift("lr")) shifter_3 (.in(X), .\dist (Y[4:0]), .out(shifter_3_out));
  Multiplier #(.width(32)) multiplier_1 (.a(X), .b(Y), .out(multiplier_1_out), .cout(multiplier_1_cout));  // open: cin
  Divider #(.width(32)) divider_1 (.a(X), .b(Y), .out(divider_1_out), .rem(divider_1_rem));  // open: upper
  Adder #(.width(32)) adder_1 (.a(X), .b(Y), .out(adder_1_out));  // open: cin, cout
  Subtractor #(.width(32)) subtractor_1 (.a(X), .b(Y), .out(subtractor_1_out));  // open: bin, bout
  assign XOR_out = X ^ Y;  // XOR_Gate XOR, 32 bits wide
  assign NOR_out = ~(X | Y);  // NOR_Gate NOR, 32 bits wide
  Comparator #(.width(32), .mode("twosComplement")) comparator_1 (
    .a(X), .b(Y), .eq(Equal), .lt(comparator_1_lt[0]));  // open: gt
  Comparator #(.width(32), .mode("unsigned")) comparator_2 (.a(X), .b(Y), .lt(comparator_2_lt[0]));  // open: gt, eq
  Multiplexer #(.select(4), .width(32), .disabled("Z"), .enable("false")) multiplexer_1 (
    .in0(shifter_1_out), .in1(shifter_2_out), .in2(shifter_3_out), .in3(multiplier_1_out),
    .in4(divider_1_out), .in5(adder_1_out), .in6(subtractor_1_out), .in7(AND_out), .in8(OR_out),
    .in9(XOR_out), .in10(NOR_out), .in11({{31{1'b0}}, comparator_1_lt[0]}),
    .in12({{31{1'b0}}, comparator_2_lt[0]}), .in13({32{1'b0}}), .in14({32{1'b0}}), .in15({32{1'b0}}),
    .out(Result), .sel(AluOP));
  Multiplexer #(.select(4), .width(32), .disabled("Z"), .enable("false")) multiplexer_2 (
    .in0({32{1'b0}}), .in1({32{1'b0}}), .in2({32{1'b0}}), .in3(multiplier_1_cout), .in4(divider_1_rem),
    .in5({32{1'b0}}), .in6({32{1'b0}}), .in7({32{1'b0}}), .in8({32{1'b0}}), .in9({32{1'b0}}),
    .in10({32{1'b0}}), .in11({32{1'b0}}), .in12({32{1'b0}}), .in13({32{1'b0}}), .in14({32{1'b0}}),
    .in15({32{1'b0}}), .out(Result_2), .sel(AluOP));
  Multiplexer #(.select(4), .width(1), .disabled("Z"), .enable("false")) multiplexer_3 (
    .in0(1'b0), .in1(1'b0), .in2(1'b0), .in3(1'b0), .in4(1'b0), .in5(1'b0), .in6(1'b0), .in7(1'b0),
    .in8(1'b0), .in9(1'b0), .in10(1'b0), .in11(comparator_1_lt[0]), .in12(comparator_2_lt[0]), .in13(1'b0),
    .in14(1'b0), .in15(1'b0), .out(out_6), .sel(AluOP));
  not not_1 (out_4, out_6);

  // Other names for the same wires on the sheet: Result2[31:0] = Result_2; S[3:0] = AluOP; tunnel = out_6;
  //   tunnel_t = out_4

  // Notes on the sheet:
  //   不要改变此引脚区域内容，也不要改变ALU封装形式
  //   输入引脚
  //   输出引脚
endmodule

module Regifile (
  input  [31:0] Din,
  input  Clk,
  input  WE,
  input  [4:0] R1_num,
  input  [4:0] W_num,
  input  [4:0] R2_num,
  output [31:0] R1,
  output [31:0] R2
);

  // RegisterFile registerfile_1: pin names not known; wires that end beside it: Din, Clk, WE, W_num, R1_num, R2_num, R1, R2
endmodule

module \理想流水线  (
  output RegWrite,
  output MemWrite,
  output [31:0] IF_PC,
  output [31:0] ID_PC,
  output [31:0] EX_PC,
  output [31:0] M_PC,
  output [31:0] WB_PC,
  output [31:0] RDin,
  output [31:0] MDin,
  output [31:0] LedData
);

  wire alu_1_out_6, and_2_out, and_3_out, and_4_out, Auipc, Beq, Bge, Bne, Byte, CLK, clock_1_out,
       comparator_1_gt, comparator_2_eq, comparator_2_lt, comparator_3_eq, comparator_4_eq, comparator_5_eq,
       d_ff_1_q, Ecall, Equ, ex_mem_1_auipc_2, ex_mem_1_byte_2, ex_mem_1_ecall_2, ex_mem_1_jal_jalr_2,
       ex_mem_1_less_2, ex_mem_1_memtoreg_2, ex_mem_1_regwrite_2, ex_mem_1_shouldhalt_2, ex_mem_1_slt_2, Geq,
       Go, halt, id_ex_1_alusrc_2, id_ex_1_auipc_2, id_ex_1_beq_2, id_ex_1_bge_2, id_ex_1_bne_2,
       id_ex_1_byte_2, id_ex_1_ecall_2, id_ex_1_jal_2, id_ex_1_jalr_2, id_ex_1_memtoreg_2,
       id_ex_1_memwrite_2, id_ex_1_regwrite_2, IR1, IR2, IR3, Jal, Jalr, me_wb_1_ecall_2, me_wb_1_memtoreg_2,
       me_wb_1_shouldhalt_2, nand_1_out, nand_2_out, not_1_out, not_2_out, not_3_out, not_4_out, or_1_out,
       or_2_out, or_3_out, riscv_probe_3_p1, RST, Uret, W1, W2, W3, \单周期硬布线控制器_1_alu_src ,
       \单周期硬布线控制器_1_memtoreg , \单周期硬布线控制器_1_memwrite , \单周期硬布线控制器_1_regwrite , \单周期硬布线控制器_1_s_type ;
  wire [1:0] multiplexer_9_out;
  wire [3:0] id_ex_1_aluop_2, \单周期硬布线控制器_1_alu_op ;
  wire [4:0] ex_mem_1_rd_2, id_ex_1_rd_2, me_wb_1_rd_4, multiplexer_2_out, multiplexer_3_out;
  wire [12:0] CNT_num;
  wire [15:0] \LoadUse次数 , \总周期数 , \插入气泡数 , \无条件分支数 , \条件分支成功数 ;
  wire [31:0] adder_1_out, adder_2_out, adder_3_out, adder_4_out, adder_5_out, alu_1_result, and_1_out,
       bit_extender_1_out, bit_extender_2_out, bit_extender_3_out, bit_extender_4_out, bit_extender_5_out,
       bit_extender_6_out, EX_IR, ex_mem_1_aluresult_2, ex_mem_1_uimm_2, id_ex_1_bimm_2, id_ex_1_imm_2,
       id_ex_1_jimm_2, id_ex_1_r1_2, id_ex_1_r2_2, id_ex_1_uimm_2, ID_IR, IF_IR, me_wb_1_aluresult_2,
       me_wb_1_rd_3, MEM_IR, mips_ram_1_dataout, multiplexer_1_out, multiplexer_4_out, multiplexer_5_out,
       multiplexer_6_out, multiplexer_7_out, multiplexer_8_out, multiplexer_10_out, multiplexer_11_out,
       multiplexer_12_out, regifile_1_r1, regifile_1_r2, shifter_1_out, shifter_2_out, shifter_3_out, WB_IR;

  Button \u_总复位  (.out(RST));
  Button _1 (.out(IR1));
  Button _2 (.out(IR2));
  Button _3 (.out(IR3));
  // Probe on \总周期数 
  // Probe on \总周期数 
  Button \u_继续运行  (.out(Go));
  LED #(.active("true")) led_1 (.in(W1));
  LED #(.active("true")) led_2 (.in(W2));
  LED #(.active("true")) led_3 (.in(W3));
  not not_1 (not_1_out, halt);
  Multiplexer #(.select(1), .width(32), .disabled("Z"), .enable("false")) multiplexer_1 (
    .in0(adder_1_out), .in1(multiplexer_8_out), .out(multiplexer_1_out), .sel(comparator_1_gt));
  Hex_Digit_Display hex_digit_display_1 (.value(LedData[31:28]));  // open: dp
  // Probe on IF_PC[19:0]
  // RiscV_Probe riscv_probe_1: pin names not known; wires that end beside it: IF_IR
  Register #(.width(32), .trigger("rising"), .Select("low")) PC (
    .D(multiplexer_1_out), .en(not_1_out), .Q(IF_PC), .clk(CLK), .clr(riscv_probe_3_p1));
  Hex_Digit_Display hex_digit_display_2 (.value(LedData[23:20]));  // open: dp
  Hex_Digit_Display hex_digit_display_3 (.value(LedData[27:24]));  // open: dp
  // Probe on ID_PC[19:0]
  // RiscV_Probe riscv_probe_2: pin names not known; wires that end beside it: ID_IR
  Hex_Digit_Display hex_digit_display_4 (.value(LedData[19:16]));  // open: dp
  Hex_Digit_Display hex_digit_display_5 (.value(LedData[15:12]));  // open: dp
  // RiscV_Probe riscv_probe_3: pin names not known; wires that end beside it: riscv_probe_3_p1, RST, IF_IR, IF_IR
  ROM #(.addrWidth(10), .dataWidth(32), .Select("high")) rom_1 (.addr(IF_PC[11:2]), .data(IF_IR));
  Adder #(.width(32)) adder_1 (.a(IF_PC), .b(32'h4), .out(adder_1_out));  // open: cin, cout
  Hex_Digit_Display hex_digit_display_6 (.value(LedData[11:8]));  // open: dp
  Hex_Digit_Display hex_digit_display_7 (.value(LedData[7:4]));  // open: dp
  // Probe on EX_PC[19:0]
  // RiscV_Probe riscv_probe_4: pin names not known; wires that end beside it: EX_IR
  Hex_Digit_Display hex_digit_display_8 (.value(LedData[3:0]));  // open: dp
  // IF_ID if_id_1: pin names not known; wires that end beside it: IF_IR, IF_PC, 1'b1, CLK, 1'b0, 1'b0, ID_IR, ID_PC
  // Probe on \总周期数 
  // Probe on M_PC[19:0]
  // RiscV_Probe riscv_probe_5: pin names not known; wires that end beside it: MEM_IR
  Multiplexer #(.select(1), .width(5), .disabled("Z"), .enable("false")) multiplexer_2 (
    .in0(ID_IR[19:15]), .in1(5'b10001), .out(multiplexer_2_out), .sel(Ecall));
  Multiplexer #(.select(1), .width(5), .disabled("Z"), .enable("false")) multiplexer_3 (
    .in0(ID_IR[24:20]), .in1(5'b01010), .out(multiplexer_3_out), .sel(Ecall));
  assign bit_extender_1_out = {{20{ID_IR[31]}}, ID_IR[31:20]};  // Bit_Extender bit_extender_1
  assign bit_extender_2_out = {{20{ID_IR[31]}}, {ID_IR[31:25], ID_IR[11:7]}};  // Bit_Extender bit_extender_2
  // Probe on \总周期数 
  // Probe on \无条件分支数 
  // Probe on \条件分支成功数 
  // Probe on \插入气泡数 
  // Probe on \LoadUse次数 
  \单周期硬布线控制器  \u_单周期硬布线控制器_1  (
    .Funct({ID_IR[30], ID_IR[25], ID_IR[14:12]}), .OP(ID_IR[6:2]), .ALU_OP(\单周期硬布线控制器_1_alu_op ),
    .MemToReg(\单周期硬布线控制器_1_memtoreg ), .MemWrite(\单周期硬布线控制器_1_memwrite ), .ALU_SRC(\单周期硬布线控制器_1_alu_src ),
    .RegWrite(\单周期硬布线控制器_1_regwrite ), .ecall(Ecall), .S_type(\单周期硬布线控制器_1_s_type ), .Jalr(Jalr), .Beq(Beq),
    .JAL(Jal), .Bne(Bne), .in_3(ID_IR[21]), .uret(Uret), .Auipc(Auipc), .Byte(Byte), .BGE(Bge));  // open: RsUsed, RtUsed, CSRRSI, CSRRCI
  // Probe on multiplexer_2_out
  // Probe on multiplexer_3_out
  Multiplexer #(.select(1), .width(32), .disabled("Z"), .enable("false")) multiplexer_4 (
    .in0(bit_extender_1_out), .in1(bit_extender_2_out), .out(multiplexer_4_out), .sel(\单周期硬布线控制器_1_s_type ));
  assign bit_extender_3_out = {{20{ID_IR[31]}}, {ID_IR[31], ID_IR[7], ID_IR[30:25], ID_IR[11:8]}};  // Bit_Extender bit_extender_3
  assign bit_extender_4_out = {{12{ID_IR[31]}}, {ID_IR[31], ID_IR[19:12], ID_IR[20], ID_IR[30:21]}};  // Bit_Extender bit_extender_4
  assign bit_extender_5_out = {{12{ID_IR[31]}}, ID_IR[31:12]};  // Bit_Extender bit_extender_5
  // Probe on IF_PC[11:0]
  // Probe on WB_PC[19:0]
  // RiscV_Probe riscv_probe_6: pin names not known; wires that end beside it: WB_IR
  Shifter #(.width(32), .shift("ll")) shifter_1 (.in(bit_extender_3_out), .\dist (5'b00001), .out(shifter_1_out));
  Shifter #(.width(32), .shift("ll")) shifter_2 (.in(bit_extender_4_out), .\dist (5'b00001), .out(shifter_2_out));
  Shifter #(.width(32), .shift("ll")) shifter_3 (.in(bit_extender_5_out), .\dist (5'b01100), .out(shifter_3_out));
  Comparator #(.width(32), .mode("unsigned")) comparator_1 (
    .a({32{1'b1}}), .b(multiplexer_8_out), .gt(comparator_1_gt));  // open: eq, lt
  // Probe on EX_PC[11:0]
  // Probe on ID_PC[11:0]
  Regifile regifile_1 (
    .Din(RDin), .Clk(CLK), .R1(regifile_1_r1), .R2(regifile_1_r2), .WE(RegWrite), .W_num(me_wb_1_rd_4),
    .R1_num(multiplexer_2_out), .R2_num(multiplexer_3_out));
  Adder #(.width(32)) adder_2 (.a(shifter_1_out), .b(ID_PC), .out(adder_2_out));  // open: cin, cout
  Adder #(.width(32)) adder_3 (.a(ID_PC), .b(shifter_2_out), .out(adder_3_out));  // open: cin, cout
  Adder #(.width(32)) adder_4 (.a(shifter_3_out), .b(IF_PC), .out(adder_4_out));  // open: cin, cout
  // Probe on M_PC[11:0]
  D_Flip_Flop #(.trigger("high"), .Pre_Clr_Positions("LEGACY"), .NegatePresetClear("false"), .enable("true"), .NewFFLayout("false")) d_ff_1 (.Q(d_ff_1_q));  // open: clk, D, Qn, preset, en, reset
  // Probe on 13'ha
  // Probe on WB_PC[11:0]
  Comparator #(.width(13), .mode("twosComplement")) comparator_2 (
    .a(CNT_num), .b(13'ha), .eq(comparator_2_eq), .lt(comparator_2_lt));  // open: gt
  Clock #(.highDuration(1), .lowDuration(1)) clock_1 (.out(clock_1_out));
  ID_EX id_ex_1 (
    .RegWrite(\单周期硬布线控制器_1_regwrite ), .R1(regifile_1_r1), .R2(regifile_1_r2), .rd(ID_IR[11:7]),
    .Imm(multiplexer_4_out), .PC(ID_PC), .RegWrite_2(id_ex_1_regwrite_2), .R1_2(id_ex_1_r1_2),
    .R2_2(id_ex_1_r2_2), .rd_2(id_ex_1_rd_2), .Imm_2(id_ex_1_imm_2), .PC_2(EX_PC), .CLK(CLK),
    .MemToReg(\单周期硬布线控制器_1_memtoreg ), .MemToReg_2(id_ex_1_memtoreg_2), .MemWrite(\单周期硬布线控制器_1_memwrite ),
    .MemWrite_2(id_ex_1_memwrite_2), .AluOP(\单周期硬布线控制器_1_alu_op ), .AluOP_2(id_ex_1_aluop_2), .Bne(Bne),
    .Bne_2(id_ex_1_bne_2), .AluSrc(\单周期硬布线控制器_1_alu_src ), .AluSrc_2(id_ex_1_alusrc_2), .Beq(Beq),
    .Beq_2(id_ex_1_beq_2), .Bge(Bge), .Bge_2(id_ex_1_bge_2), .Auipc(Auipc), .Auipc_2(id_ex_1_auipc_2),
    .Byte(Byte), .Byte_2(id_ex_1_byte_2), .Jalr(Jalr), .Jalr_2(id_ex_1_jalr_2), .Jal(Jal),
    .Jal_2(id_ex_1_jal_2), .BImm(adder_2_out), .BImm_2(id_ex_1_bimm_2), .JImm(adder_3_out),
    .JImm_2(id_ex_1_jimm_2), .UImm(adder_4_out), .UImm_2(id_ex_1_uimm_2), .Ecall(Ecall),
    .Ecall_2(id_ex_1_ecall_2), .IR(ID_IR), .IR_2(EX_IR), .Flush(1'b0), .En(1'b1));  // open: RsFoward, RsFoward_2, RtFoward, RtFoward_2, Uert, Uert_2, PredictJump, PredictJump_2
  or or_1 (or_1_out, id_ex_1_jalr_2, id_ex_1_jal_2);
  nand nand_1 (nand_1_out, d_ff_1_q, comparator_2_eq);
  Counter #(.width(13), .max('h1fff), .ongoal("stay"), .trigger("rising"), .behavior("old")) counter_1 (
    .count(comparator_2_lt), .Q(CNT_num), .clk(clock_1_out));  // open: load, D, carry, clr, preset
  assign CLK = nand_1_out ? clock_1_out : 1'bz;  // Controlled_Buffer controlled_buffer_1
  Multiplexer #(.select(1), .width(32), .disabled("Z"), .enable("false")) multiplexer_5 (
    .in0({32{1'b1}}), .in1(and_1_out), .out(multiplexer_5_out), .sel(id_ex_1_jalr_2));
  Multiplexer #(.select(1), .width(32), .disabled("Z"), .enable("false")) multiplexer_6 (
    .in0(multiplexer_5_out), .in1(id_ex_1_bimm_2), .out(multiplexer_6_out), .sel(or_3_out));
  Pull_Resistor #(.pull(1)) pull_resistor_1 (.node(CLK));
  Comparator #(.width(32), .mode("twosComplement")) comparator_3 (
    .a(id_ex_1_r1_2), .b(32'h22), .eq(comparator_3_eq));  // open: gt, lt
  Multiplexer #(.select(1), .width(32), .disabled("Z"), .enable("false")) multiplexer_7 (
    .in0(id_ex_1_r2_2), .in1(id_ex_1_imm_2), .out(multiplexer_7_out), .sel(id_ex_1_alusrc_2));
  Multiplexer #(.select(1), .width(32), .disabled("Z"), .enable("false")) multiplexer_8 (
    .in0(multiplexer_6_out), .in1(id_ex_1_jimm_2), .out(multiplexer_8_out), .sel(id_ex_1_jal_2));
  Comparator #(.width(4), .mode("unsigned")) comparator_4 (
    .a(id_ex_1_aluop_2), .b(4'b1100), .eq(comparator_4_eq));  // open: gt, lt
  Comparator #(.width(4), .mode("unsigned")) comparator_5 (
    .a(id_ex_1_aluop_2), .b(4'b1011), .eq(comparator_5_eq));  // open: gt, lt
  nand nand_2 (nand_2_out, comparator_3_eq, id_ex_1_ecall_2);
  ALU alu_1 (
    .X(id_ex_1_r1_2), .Y(multiplexer_7_out), .AluOP(id_ex_1_aluop_2), .Equal(Equ), .Result(alu_1_result),
    .out_4(Geq), .out_6(alu_1_out_6));  // open: Result_2
  assign and_1_out = 32'hfffe & alu_1_result;  // AND_Gate and_1, 32 bits wide
  and and_2 (and_2_out, id_ex_1_beq_2, Equ);
  and and_3 (and_3_out, id_ex_1_bne_2, not_2_out);
  not not_2 (not_2_out, Equ);
  and and_4 (and_4_out, id_ex_1_bge_2, Geq);
  or or_2 (or_2_out, comparator_4_eq, comparator_5_eq);
  not not_3 (not_3_out, nand_2_out);
  or or_3 (or_3_out, and_4_out, and_3_out, and_2_out);
  Register #(.width(32), .trigger("rising"), .Select("low")) register_1 (
    .D(id_ex_1_r2_2), .en(not_3_out), .Q(LedData), .clk(CLK));  // open: clr
  EX_MEM ex_mem_1 (
    .AluResult(alu_1_result), .WriteData(id_ex_1_r2_2), .rd(id_ex_1_rd_2),
    .AluResult_2(ex_mem_1_aluresult_2), .WriteData_2(MDin), .rd_2(ex_mem_1_rd_2), .CLK(CLK),
    .RegWrite(id_ex_1_regwrite_2), .RegWrite_2(ex_mem_1_regwrite_2), .MemToReg(id_ex_1_memtoreg_2),
    .MemToReg_2(ex_mem_1_memtoreg_2), .MemWrite(id_ex_1_memwrite_2), .MemWrite_2(MemWrite),
    .Byte(id_ex_1_byte_2), .Byte_2(ex_mem_1_byte_2), .Ecall(id_ex_1_ecall_2), .Ecall_2(ex_mem_1_ecall_2),
    .ShouldHalt(nand_2_out), .ShouldHalt_2(ex_mem_1_shouldhalt_2), .Auipc(id_ex_1_auipc_2),
    .Auipc_2(ex_mem_1_auipc_2), .Less(alu_1_out_6), .Less_2(ex_mem_1_less_2), .Slt(or_2_out),
    .Slt_2(ex_mem_1_slt_2), .Jal_Jalr(or_1_out), .Jal_Jalr_2(ex_mem_1_jal_jalr_2), .PC(EX_PC), .PC_2(M_PC),
    .UImm(id_ex_1_uimm_2), .UImm_2(ex_mem_1_uimm_2), .IR(EX_IR), .IR_2(MEM_IR), .En(1'b1), .Flush(1'b0));  // open: Uert_2, Uert
  assign bit_extender_6_out = {{31{1'b0}}, ex_mem_1_less_2};  // Bit_Extender bit_extender_6
  Adder #(.width(32)) adder_5 (.a(M_PC), .b(32'h4), .out(adder_5_out));  // open: cin, cout
  MIPS_RAM mips_ram_1 (
    .\字节地址 (ex_mem_1_aluresult_2[11:0]), .Din(MDin), .DataOut(mips_ram_1_dataout), .CLK(CLK), .WE(MemWrite),
    .Mode(multiplexer_9_out));
  Multiplexer #(.select(1), .width(2), .disabled("Z"), .enable("false")) multiplexer_9 (
    .in0(2'b00), .in1(2'b01), .out(multiplexer_9_out), .sel(ex_mem_1_byte_2));
  Multiplexer #(.select(1), .width(32), .disabled("Z"), .enable("false")) multiplexer_10 (
    .in0(ex_mem_1_aluresult_2), .in1(bit_extender_6_out), .out(multiplexer_10_out), .sel(ex_mem_1_slt_2));
  Multiplexer #(.select(1), .width(32), .disabled("Z"), .enable("false")) multiplexer_11 (
    .in0(multiplexer_10_out), .in1(adder_5_out), .out(multiplexer_11_out), .sel(ex_mem_1_jal_jalr_2));
  Multiplexer #(.select(1), .width(32), .disabled("Z"), .enable("false")) multiplexer_12 (
    .in0(multiplexer_11_out), .in1(ex_mem_1_uimm_2), .out(multiplexer_12_out), .sel(ex_mem_1_auipc_2));
  ME_WB me_wb_1 (
    .RegWrite(ex_mem_1_regwrite_2), .MemToReg(ex_mem_1_memtoreg_2), .AluResult(multiplexer_12_out),
    .RD(mips_ram_1_dataout), .rd_2(ex_mem_1_rd_2), .RegWrite_2(RegWrite), .MemToReg_2(me_wb_1_memtoreg_2),
    .AluResult_2(me_wb_1_aluresult_2), .RD_3(me_wb_1_rd_3), .rd_4(me_wb_1_rd_4), .CLK(CLK),
    .ShouldHalt(ex_mem_1_shouldhalt_2), .ShouldHalt_2(me_wb_1_shouldhalt_2), .Ecall(ex_mem_1_ecall_2),
    .Ecall_2(me_wb_1_ecall_2), .PC(M_PC), .PC_2(WB_PC), .IR(MEM_IR), .IR_2(WB_IR), .En(1'b1));
  not not_4 (not_4_out, halt);
  Counter #(.width(16), .max('hffff), .ongoal("wrap"), .trigger("rising"), .behavior("new")) counter_2 (
    .count(not_4_out), .Q(\总周期数 ), .clk(CLK));  // open: load, D, carry, clr, preset, down
  Multiplexer #(.select(1), .width(32), .disabled("Z"), .enable("false")) multiplexer_13 (
    .in0(me_wb_1_aluresult_2), .in1(me_wb_1_rd_3), .out(RDin), .sel(me_wb_1_memtoreg_2));
  D_Flip_Flop #(.trigger("falling"), .Pre_Clr_Positions("ABOVE_BELOW"), .NegatePresetClear("false"), .enable("true"), .NewFFLayout("true")) d_ff_2 (
    .clk(CLK), .D(me_wb_1_shouldhalt_2), .Q(halt), .en(me_wb_1_ecall_2), .reset(Go));  // open: Qn, preset

  // Other names for the same wires on the sheet: MEM_PC[31:0] = M_PC; PC[31:0] = IF_PC

  // Notes on the sheet:
  //   中断源
  //   时空图监测，可删除
  //   中断等待指示
  //   指令存储器
  //   数码管输出
  //   指令探针
  //   contents of rom_1 (hex, n*v repeats v):
  //   413 493 913 993 46413 14e493 296913 39e993 842023 942223 1242423 1342623 a00893 493 913 993 73
  //   指令字
  //   JAL
  //   JALR
  //   Beq
  //   Bne
  //   MemToReg
  //   MemWrite
  //   AluOP
  //   AluSrcB
  //   RegWrite
  //   控制位
  //   流水调试日志用
  //   暂停节拍，不能为0
  //   戳工具置1进入计数暂停模式，ctrl+k时钟自动运行到对应节拍暂停
  //   ctrl+k关闭时钟连续运行，将控制位置零，进入单步调试模式调试
  //   用这个时钟源需要去掉电路中的其他时钟源
  //   可计数暂停的时钟源
  //   为方便自动评测，需要输出流水线各段保存的PC值，注意是PC不是PC+4，另外ID段寄存器写入信息，Mem段内存写入信息也要输出
  //   数据存储器
endmodule

module \气泡流水线  (
  output RegWrite,
  output MemWrite,
  output [31:0] IF_PC,
  output [31:0] ID_PC,
  output [31:0] EX_PC,
  output [31:0] M_PC,
  output [31:0] WB_PC,
  output [31:0] RDin,
  output [31:0] MDin,
  output [31:0] LedData
);

  wire alu_1_out_6, and_1_out, and_2_out, and_4_out, and_5_out, and_6_out, and_7_out, and_8_out, and_9_out,
       and_10_out, and_11_out, Auipc, Beq, Bge, Bne, Branch, BranchTaken, Byte, CLK, clock_1_out,
       comparator_2_eq, comparator_2_lt, comparator_3_eq, comparator_4_eq, comparator_5_eq, d_ff_1_q, Ecall,
       Equ, ex_mem_1_auipc_2, ex_mem_1_byte_2, ex_mem_1_ecall_2, ex_mem_1_jal_jalr_2, ex_mem_1_less_2,
       ex_mem_1_memtoreg_2, ex_mem_1_regwrite_2, ex_mem_1_shouldhalt_2, ex_mem_1_slt_2, Flush, Geq, Go, halt,
       id_ex_1_alusrc_2, id_ex_1_auipc_2, id_ex_1_beq_2, id_ex_1_bge_2, id_ex_1_bne_2, id_ex_1_byte_2,
       id_ex_1_ecall_2, id_ex_1_jal_2, id_ex_1_jalr_2, id_ex_1_memtoreg_2, id_ex_1_memwrite_2,
       id_ex_1_regwrite_2, if_id_1_p5, IR1, IR2, IR3, Jal, Jalr, JJump, me_wb_1_ecall_2, me_wb_1_memtoreg_2,
       me_wb_1_shouldhalt_2, nand_1_out, nand_2_out, not_1_out, not_2_out, not_3_out, not_4_out, not_5_out,
       not_6_out, not_7_out, not_8_out, or_1_out, or_3_out, riscv_probe_3_p1, RST, stall, Uret, W1, W2, W3,
       \单周期硬布线控制器_1_alu_src , \单周期硬布线控制器_1_memtoreg , \单周期硬布线控制器_1_memwrite , \单周期硬布线控制器_1_regwrite ,
       \单周期硬布线控制器_1_rsused , \单周期硬布线控制器_1_rtused , \单周期硬布线控制器_1_s_type , \气泡处理逻辑_1_if_id_en ,
       \气泡处理逻辑_1_pc_en ;
  wire [1:0] multiplexer_9_out;
  wire [3:0] id_ex_1_aluop_2, \单周期硬布线控制器_1_alu_op ;
  wire [4:0] ex_mem_1_rd_2, id_ex_1_rd_2, me_wb_1_rd_4, multiplexer_2_out, multiplexer_3_out;
  wire [12:0] CNT_num;
  wire [15:0] \LoadUse次数 , \总周期数 , \插入气泡数 , \无条件分支数 , \条件分支成功数 ;
  wire [31:0] adder_1_out, adder_2_out, adder_3_out, adder_4_out, adder_5_out, alu_1_result, and_3_out,
       bit_extender_1_out, bit_extender_2_out, bit_extender_3_out, bit_extender_4_out, bit_extender_5_out,
       bit_extender_6_out, EX_IR, ex_mem_1_aluresult_2, ex_mem_1_uimm_2, id_ex_1_bimm_2, id_ex_1_imm_2,
       id_ex_1_jimm_2, id_ex_1_r1_2, id_ex_1_r2_2, id_ex_1_uimm_2, ID_IR, IF_IR, me_wb_1_aluresult_2,
       me_wb_1_rd_3, MEM_IR, mips_ram_1_dataout, multiplexer_1_out, multiplexer_4_out, multiplexer_5_out,
       multiplexer_6_out, multiplexer_7_out, multiplexer_8_out, multiplexer_10_out, multiplexer_11_out,
       multiplexer_12_out, regifile_1_r1, regifile_1_r2, shifter_1_out, shifter_2_out, shifter_3_out, WB_IR;

  Button \u_总复位  (.out(RST));
  Button _1 (.out(IR1));
  Button _2 (.out(IR2));
  Button _3 (.out(IR3));
  // Probe on \总周期数 
  // Probe on \总周期数 
  Button \u_继续运行  (.out(Go));
  LED #(.active("true")) led_1 (.in(W1));
  LED #(.active("true")) led_2 (.in(W2));
  LED #(.active("true")) led_3 (.in(W3));
  not not_1 (not_1_out, halt);
  and and_1 (and_1_out, not_1_out, \气泡处理逻辑_1_pc_en );
  Multiplexer #(.select(1), .width(32), .disabled("Z"), .enable("false")) multiplexer_1 (
    .in0(adder_1_out), .in1(multiplexer_7_out), .out(multiplexer_1_out), .sel(BranchTaken));
  Hex_Digit_Display hex_digit_display_1 (.value(LedData[31:28]));  // open: dp
  // Probe on IF_PC[19:0]
  // RiscV_Probe riscv_probe_1: pin names not known; wires that end beside it: IF_IR
  Register #(.width(32), .trigger("rising"), .Select("low")) PC (
    .D(multiplexer_1_out), .en(and_1_out), .Q(IF_PC), .clk(CLK), .clr(riscv_probe_3_p1));
  Hex_Digit_Display hex_digit_display_2 (.value(LedData[23:20]));  // open: dp
  Hex_Digit_Display hex_digit_display_3 (.value(LedData[27:24]));  // open: dp
  // Probe on ID_PC[19:0]
  // RiscV_Probe riscv_probe_2: pin names not known; wires that end beside it: ID_IR
  Hex_Digit_Display hex_digit_display_4 (.value(LedData[15:12]));  // open: dp
  Hex_Digit_Display hex_digit_display_5 (.value(LedData[19:16]));  // open: dp
  // RiscV_Probe riscv_probe_3: pin names not known; wires that end beside it: riscv_probe_3_p1, RST, IF_IR, IF_IR
  Adder #(.width(32)) adder_1 (.a(IF_PC), .b(32'h4), .out(adder_1_out));  // open: cin, cout
  Hex_Digit_Display hex_digit_display_6 (.value(LedData[7:4]));  // open: dp
  Hex_Digit_Display hex_digit_display_7 (.value(LedData[11:8]));  // open: dp
  // Probe on EX_PC[19:0]
  // RiscV_Probe riscv_probe_4: pin names not known; wires that end beside it: EX_IR
  not not_2 (not_2_out, halt);
  and and_2 (and_2_out, not_2_out, \气泡处理逻辑_1_if_id_en );
  ROM #(.addrWidth(10), .dataWidth(32), .Select("high")) rom_1 (.addr(IF_PC[11:2]), .data(IF_IR));
  Hex_Digit_Display hex_digit_display_8 (.value(LedData[3:0]));  // open: dp
  // IF_ID if_id_1: pin names not known; wires that end beside it: IF_IR, IF_PC, and_2_out, CLK, if_id_1_p5, 1'b0, ID_IR, ID_PC
  // Probe on \总周期数 
  // Probe on M_PC[19:0]
  // RiscV_Probe riscv_probe_5: pin names not known; wires that end beside it: MEM_IR
  // Probe on \总周期数 
  // Probe on \无条件分支数 
  // Probe on \条件分支成功数 
  // Probe on \插入气泡数 
  // Probe on \LoadUse次数 
  \单周期硬布线控制器  \u_单周期硬布线控制器_1  (
    .Funct({ID_IR[30], ID_IR[25], ID_IR[14:12]}), .OP(ID_IR[6:2]), .ALU_OP(\单周期硬布线控制器_1_alu_op ),
    .MemToReg(\单周期硬布线控制器_1_memtoreg ), .MemWrite(\单周期硬布线控制器_1_memwrite ), .ALU_SRC(\单周期硬布线控制器_1_alu_src ),
    .RegWrite(\单周期硬布线控制器_1_regwrite ), .ecall(Ecall), .S_type(\单周期硬布线控制器_1_s_type ), .Jalr(Jalr), .Beq(Beq),
    .JAL(Jal), .Bne(Bne), .in_3(ID_IR[21]), .uret(Uret), .Auipc(Auipc), .Byte(Byte), .BGE(Bge),
    .RsUsed(\单周期硬布线控制器_1_rsused ), .RtUsed(\单周期硬布线控制器_1_rtused ));  // open: CSRRSI, CSRRCI
  Multiplexer #(.select(1), .width(5), .disabled("Z"), .enable("false")) multiplexer_2 (
    .in0(ID_IR[19:15]), .in1(5'b10001), .out(multiplexer_2_out), .sel(Ecall));
  // Probe on multiplexer_2_out
  // Probe on multiplexer_3_out
  Multiplexer #(.select(1), .width(5), .disabled("Z"), .enable("false")) multiplexer_3 (
    .in0(ID_IR[24:20]), .in1(5'b01010), .out(multiplexer_3_out), .sel(Ecall));
  assign bit_extender_1_out = {{20{ID_IR[31]}}, ID_IR[31:20]};  // Bit_Extender bit_extender_1
  assign bit_extender_2_out = {{20{ID_IR[31]}}, {ID_IR[31:25], ID_IR[11:7]}};  // Bit_Extender bit_extender_2
  // Probe on IF_PC[11:0]
  // Probe on WB_PC[19:0]
  // RiscV_Probe riscv_probe_6: pin names not known; wires that end beside it: WB_IR
  Multiplexer #(.select(1), .width(32), .disabled("Z"), .enable("false")) multiplexer_4 (
    .in0(bit_extender_1_out), .in1(bit_extender_2_out), .out(multiplexer_4_out), .sel(\单周期硬布线控制器_1_s_type ));
  assign bit_extender_3_out = {{20{ID_IR[31]}}, {ID_IR[31], ID_IR[7], ID_IR[30:25], ID_IR[11:8]}};  // Bit_Extender bit_extender_3
  assign bit_extender_4_out = {{12{ID_IR[31]}}, {ID_IR[31], ID_IR[19:12], ID_IR[20], ID_IR[30:21]}};  // Bit_Extender bit_extender_4
  assign bit_extender_5_out = {{12{ID_IR[31]}}, ID_IR[31:12]};  // Bit_Extender bit_extender_5
  Shifter #(.width(32), .shift("ll")) shifter_1 (.in(bit_extender_5_out), .\dist (5'b01100), .out(shifter_1_out));
  // Probe on ID_PC[11:0]
  // Probe on EX_PC[11:0]
  not not_3 (not_3_out, CLK);
  Regifile regifile_1 (
    .Din(RDin), .Clk(not_3_out), .R1(regifile_1_r1), .R2(regifile_1_r2), .WE(RegWrite), .W_num(me_wb_1_rd_4),
    .R1_num(multiplexer_2_out), .R2_num(multiplexer_3_out));
  // Probe on ID_IR[11:7]
  Shifter #(.width(32), .shift("ll")) shifter_2 (.in(bit_extender_3_out), .\dist (5'b00001), .out(shifter_2_out));
  Shifter #(.width(32), .shift("ll")) shifter_3 (.in(bit_extender_4_out), .\dist (5'b00001), .out(shifter_3_out));
  Adder #(.width(32)) adder_2 (.a(shifter_1_out), .b(ID_PC), .out(adder_2_out));  // open: cin, cout
  Comparator #(.width(32), .mode("unsigned")) comparator_1 (
    .a({32{1'b1}}), .b(multiplexer_7_out), .gt(BranchTaken));  // open: eq, lt
  // Probe on M_PC[11:0]
  D_Flip_Flop #(.trigger("high"), .Pre_Clr_Positions("LEGACY"), .NegatePresetClear("false"), .enable("true"), .NewFFLayout("false")) d_ff_1 (.Q(d_ff_1_q));  // open: clk, D, Qn, preset, en, reset
  // Probe on 13'h16
  Adder #(.width(32)) adder_3 (.a(shifter_2_out), .b(ID_PC), .out(adder_3_out));  // open: cin, cout
  Adder #(.width(32)) adder_4 (.a(ID_PC), .b(shifter_3_out), .out(adder_4_out));  // open: cin, cout
  // Probe on WB_PC[11:0]
  Comparator #(.width(13), .mode("twosComplement")) comparator_2 (
    .a(CNT_num), .b(13'h16), .eq(comparator_2_eq), .lt(comparator_2_lt));  // open: gt
  Clock #(.highDuration(1), .lowDuration(1)) clock_1 (.out(clock_1_out));
  not not_4 (not_4_out, halt);
  ID_EX id_ex_1 (
    .RegWrite(\单周期硬布线控制器_1_regwrite ), .R1(regifile_1_r1), .R2(regifile_1_r2), .rd(ID_IR[11:7]),
    .Imm(multiplexer_4_out), .PC(ID_PC), .RegWrite_2(id_ex_1_regwrite_2), .R1_2(id_ex_1_r1_2),
    .R2_2(id_ex_1_r2_2), .rd_2(id_ex_1_rd_2), .Imm_2(id_ex_1_imm_2), .PC_2(EX_PC), .CLK(CLK),
    .MemToReg(\单周期硬布线控制器_1_memtoreg ), .MemToReg_2(id_ex_1_memtoreg_2), .MemWrite(\单周期硬布线控制器_1_memwrite ),
    .MemWrite_2(id_ex_1_memwrite_2), .AluOP(\单周期硬布线控制器_1_alu_op ), .AluOP_2(id_ex_1_aluop_2), .Bne(Bne),
    .Bne_2(id_ex_1_bne_2), .AluSrc(\单周期硬布线控制器_1_alu_src ), .AluSrc_2(id_ex_1_alusrc_2), .Beq(Beq),
    .Beq_2(id_ex_1_beq_2), .Bge(Bge), .Bge_2(id_ex_1_bge_2), .Auipc(Auipc), .Auipc_2(id_ex_1_auipc_2),
    .Byte(Byte), .Byte_2(id_ex_1_byte_2), .Jalr(Jalr), .Jalr_2(id_ex_1_jalr_2), .Jal(Jal),
    .Jal_2(id_ex_1_jal_2), .BImm(adder_3_out), .BImm_2(id_ex_1_bimm_2), .JImm(adder_4_out),
    .JImm_2(id_ex_1_jimm_2), .UImm(adder_2_out), .UImm_2(id_ex_1_uimm_2), .Ecall(Ecall),
    .Ecall_2(id_ex_1_ecall_2), .IR(ID_IR), .IR_2(EX_IR), .Flush(Flush), .En(not_4_out));  // open: RsFoward, RsFoward_2, RtFoward, RtFoward_2, Uert, Uert_2, PredictJump, PredictJump_2
  nand nand_1 (nand_1_out, d_ff_1_q, comparator_2_eq);
  Counter #(.width(13), .max('h1fff), .ongoal("stay"), .trigger("rising"), .behavior("old")) counter_1 (
    .count(comparator_2_lt), .Q(CNT_num), .clk(clock_1_out));  // open: load, D, carry, clr, preset
  or or_1 (or_1_out, id_ex_1_jalr_2, id_ex_1_jal_2);
  assign CLK = nand_1_out ? clock_1_out : 1'bz;  // Controlled_Buffer controlled_buffer_1
  Multiplexer #(.select(1), .width(32), .disabled("Z"), .enable("false")) multiplexer_5 (
    .in0({32{1'b1}}), .in1(and_3_out), .out(multiplexer_5_out), .sel(id_ex_1_jalr_2));
  or or_2 (JJump, id_ex_1_jal_2, id_ex_1_jalr_2);
  Pull_Resistor #(.pull(1)) pull_resistor_1 (.node(CLK));
  Multiplexer #(.select(1), .width(32), .disabled("Z"), .enable("false")) multiplexer_6 (
    .in0(multiplexer_5_out), .in1(id_ex_1_bimm_2), .out(multiplexer_6_out), .sel(Branch));
  Multiplexer #(.select(1), .width(32), .disabled("Z"), .enable("false")) multiplexer_7 (
    .in0(multiplexer_6_out), .in1(id_ex_1_jimm_2), .out(multiplexer_7_out), .sel(id_ex_1_jal_2));
  Comparator #(.width(4), .mode("unsigned")) comparator_3 (
    .a(id_ex_1_aluop_2), .b(4'b1100), .eq(comparator_3_eq));  // open: gt, lt
  Comparator #(.width(4), .mode("unsigned")) comparator_4 (
    .a(id_ex_1_aluop_2), .b(4'b1011), .eq(comparator_4_eq));  // open: gt, lt
  Comparator #(.width(32), .mode("twosComplement")) comparator_5 (
    .a(id_ex_1_r1_2), .b(32'h22), .eq(comparator_5_eq));  // open: gt, lt
  nand nand_2 (nand_2_out, comparator_5_eq, id_ex_1_ecall_2);
  Multiplexer #(.select(1), .width(32), .disabled("Z"), .enable("false")) multiplexer_8 (
    .in0(id_ex_1_r2_2), .in1(id_ex_1_imm_2), .out(multiplexer_8_out), .sel(id_ex_1_alusrc_2));
  not not_5 (not_5_out, Equ);
  or or_3 (or_3_out, comparator_3_eq, comparator_4_eq);
  ALU alu_1 (
    .X(id_ex_1_r1_2), .Y(multiplexer_8_out), .AluOP(id_ex_1_aluop_2), .Equal(Equ), .Result(alu_1_result),
    .out_4(Geq), .out_6(alu_1_out_6));  // open: Result_2
  assign and_3_out = 32'hfffe & alu_1_result;  // AND_Gate and_3, 32 bits wide
  and and_4 (and_4_out, id_ex_1_beq_2, Equ);
  and and_5 (and_5_out, id_ex_1_bne_2, not_5_out);
  and and_6 (and_6_out, id_ex_1_bge_2, Geq);
  or or_4 (Branch, and_6_out, and_5_out, and_4_out);
  Register #(.width(32), .trigger("rising"), .Select("low")) register_1 (
    .D(id_ex_1_r2_2), .en(not_6_out), .Q(LedData), .clk(CLK));  // open: clr
  not not_6 (not_6_out, nand_2_out);
  not not_7 (not_7_out, halt);
  EX_MEM ex_mem_1 (
    .AluResult(alu_1_result), .WriteData(id_ex_1_r2_2), .rd(id_ex_1_rd_2),
    .AluResult_2(ex_mem_1_aluresult_2), .WriteData_2(MDin), .rd_2(ex_mem_1_rd_2), .CLK(CLK),
    .RegWrite(id_ex_1_regwrite_2), .RegWrite_2(ex_mem_1_regwrite_2), .MemToReg(id_ex_1_memtoreg_2),
    .MemToReg_2(ex_mem_1_memtoreg_2), .MemWrite(id_ex_1_memwrite_2), .MemWrite_2(MemWrite),
    .Byte(id_ex_1_byte_2), .Byte_2(ex_mem_1_byte_2), .Ecall(id_ex_1_ecall_2), .Ecall_2(ex_mem_1_ecall_2),
    .ShouldHalt(nand_2_out), .ShouldHalt_2(ex_mem_1_shouldhalt_2), .Auipc(id_ex_1_auipc_2),
    .Auipc_2(ex_mem_1_auipc_2), .Less(alu_1_out_6), .Less_2(ex_mem_1_less_2), .Slt(or_3_out),
    .Slt_2(ex_mem_1_slt_2), .Jal_Jalr(or_1_out), .Jal_Jalr_2(ex_mem_1_jal_jalr_2), .PC(EX_PC), .PC_2(M_PC),
    .UImm(id_ex_1_uimm_2), .UImm_2(ex_mem_1_uimm_2), .IR(EX_IR), .IR_2(MEM_IR), .En(not_7_out), .Flush(1'b0));  // open: Uert_2, Uert
  assign bit_extender_6_out = {{31{1'b0}}, ex_mem_1_less_2};  // Bit_Extender bit_extender_6
  MIPS_RAM mips_ram_1 (
    .\字节地址 (ex_mem_1_aluresult_2[11:0]), .Din(MDin), .DataOut(mips_ram_1_dataout), .CLK(CLK), .WE(MemWrite),
    .Mode(multiplexer_9_out));
  Multiplexer #(.select(1), .width(2), .disabled("Z"), .enable("false")) multiplexer_9 (
    .in0(2'b00), .in1(2'b01), .out(multiplexer_9_out), .sel(ex_mem_1_byte_2));
  Multiplexer #(.select(1), .width(32), .disabled("Z"), .enable("false")) multiplexer_10 (
    .in0(ex_mem_1_aluresult_2), .in1(bit_extender_6_out), .out(multiplexer_10_out), .sel(ex_mem_1_slt_2));
  Adder #(.width(32)) adder_5 (.a(M_PC), .b(32'h4), .out(adder_5_out));  // open: cin, cout
  Multiplexer #(.select(1), .width(32), .disabled("Z"), .enable("false")) multiplexer_11 (
    .in0(multiplexer_10_out), .in1(adder_5_out), .out(multiplexer_11_out), .sel(ex_mem_1_jal_jalr_2));
  \气泡处理逻辑  \u_气泡处理逻辑_1  (
    .RsUsed(\单周期硬布线控制器_1_rsused ), .rs(multiplexer_2_out), .RtUsed(\单周期硬布线控制器_1_rtused ),
    .rt(multiplexer_3_out), .MEM_RegWrite(ex_mem_1_regwrite_2), .MEM_WriteReg_V(ex_mem_1_rd_2),
    .EX_RegWrite(id_ex_1_regwrite_2), .EX_WriteReg_V(id_ex_1_rd_2), .BranchTaken(BranchTaken), .Stall(stall),
    .PC_EN(\气泡处理逻辑_1_pc_en ), .IF_ID_EN(\气泡处理逻辑_1_if_id_en ), .IF_ID_CLR(if_id_1_p5), .ID_EX_CLR(Flush));  // open: DataHazzard, Flush
  Multiplexer #(.select(1), .width(32), .disabled("Z"), .enable("false")) multiplexer_12 (
    .in0(multiplexer_11_out), .in1(ex_mem_1_uimm_2), .out(multiplexer_12_out), .sel(ex_mem_1_auipc_2));
  not not_8 (not_8_out, halt);
  ME_WB me_wb_1 (
    .RegWrite(ex_mem_1_regwrite_2), .MemToReg(ex_mem_1_memtoreg_2), .AluResult(multiplexer_12_out),
    .RD(mips_ram_1_dataout), .rd_2(ex_mem_1_rd_2), .RegWrite_2(RegWrite), .MemToReg_2(me_wb_1_memtoreg_2),
    .AluResult_2(me_wb_1_aluresult_2), .RD_3(me_wb_1_rd_3), .rd_4(me_wb_1_rd_4), .CLK(CLK),
    .ShouldHalt(ex_mem_1_shouldhalt_2), .ShouldHalt_2(me_wb_1_shouldhalt_2), .Ecall(ex_mem_1_ecall_2),
    .Ecall_2(me_wb_1_ecall_2), .PC(M_PC), .PC_2(WB_PC), .IR(MEM_IR), .IR_2(WB_IR), .En(not_8_out));
  Multiplexer #(.select(1), .width(32), .disabled("Z"), .enable("false")) multiplexer_13 (
    .in0(me_wb_1_aluresult_2), .in1(me_wb_1_rd_3), .out(RDin), .sel(me_wb_1_memtoreg_2));
  D_Flip_Flop #(.trigger("falling"), .Pre_Clr_Positions("ABOVE_BELOW"), .NegatePresetClear("false"), .enable("true"), .NewFFLayout("true")) d_ff_2 (
    .clk(CLK), .D(me_wb_1_shouldhalt_2), .Q(halt), .en(me_wb_1_ecall_2), .reset(Go));  // open: Qn, preset
  and and_7 (and_7_out, ~halt, CLK);  // AND_Gate
  and and_8 (and_8_out, ~halt, CLK);  // AND_Gate
  Counter #(.width(16), .max('hffff), .ongoal("wrap"), .trigger("rising"), .behavior("new")) counter_2 (
    .count(Branch), .Q(\条件分支成功数 ), .clk(and_7_out), .clr(RST));  // open: load, D, carry, preset, down
  Counter #(.width(16), .max('hffff), .ongoal("wrap"), .trigger("rising"), .behavior("new")) counter_3 (
    .count(Flush), .Q(\插入气泡数 ), .clk(and_8_out), .clr(RST));  // open: load, D, carry, preset, down
  Counter #(.width(16), .max('hffff), .ongoal("wrap"), .trigger("rising"), .behavior("new")) counter_4 (
    .count(JJump), .Q(\无条件分支数 ), .clk(and_9_out), .clr(RST));  // open: load, D, carry, preset, down
  and and_9 (and_9_out, ~halt, CLK);  // AND_Gate
  Counter #(.width(16), .max('hffff), .ongoal("wrap"), .trigger("rising"), .behavior("new")) counter_5 (
    .count(CLK), .Q(\总周期数 ), .clk(and_10_out), .clr(RST));  // open: load, D, carry, preset, down
  and and_10 (and_10_out, ~halt, CLK);  // AND_Gate
  Counter #(.width(16), .max('hffff), .ongoal("wrap"), .trigger("rising"), .behavior("new")) counter_6 (
    .count(stall), .Q(\LoadUse次数 ), .clk(and_11_out), .clr(RST));  // open: load, D, carry, preset, down
  and and_11 (and_11_out, ~halt, CLK);  // AND_Gate

  // Other names for the same wires on the sheet: MEM_PC[31:0] = M_PC; PC[31:0] = IF_PC

  // Notes on the sheet:
  //   中断源
  //   时空图监测，可删除
  //   中断等待指示
  //   数码管输出
  //   指令探针
  //   指令存储器
  //   contents of rom_1 (hex, n*v repeats v):
  //   100493 100006f 100493 200913 300993 100006f 100493 200913 300993 100006f 100493 200913 300993
  //   100006f 100493 200913 300993 3ec000ef 100413 100493 1f49493 900533 2200893 73 24d493 48463 fedff06f
  //   900533 2200893 73 100493 249493 900533 2200893 73 48463 fedff06f 100493 1f49493 900533 2200893 73
  //   4034d493 900533 2200893 73 4044d493 900533 2200893 73 4044d493 900533 2200893 73 4044d493 900533
  //   2200893 73 4044d493 900533 2200893 73 4044d493 900533 2200893 73 4044d493 900533 2200893 73 4044d493
  //   900533 2200893 73 100413 1f41993 41f9d993 433 c00913 300b13 140413 f47413 800293 100313 499993
  //   89e9b3 1300533 2200893 73 406282b3 fe0294e3 140413 f00f93 1f47433 1c41413 800293 100313 49d993
  //   89e9b3 1300533 2200893 73 406282b3 fe0294e3 1c45413 406b0b33 b0463 f95ff06f 2b3 fff2c293 829293
  //   ff2e293 500533 2200893 73 fff00413 493 84a023 140413 448493 84a023 140413 448493 84a023 140413
  //   448493 84a023 140413 448493 84a023 140413 448493 84a023 140413 448493 84a023 140413 448493 84a023
  //   140413 448493 84a023 140413 448493 84a023 140413 448493 84a023 140413 448493 84a023 140413 448493
  //   84a023 140413 448493 84a023 140413 448493 84a023 140413 448493 84a023 140413 448493 140413 433
  //   3c00493 42983 4aa03 149a2b3 28663 134a023 1442023 ffc48493 fe9412e3 800533 2200893 73 440413 3c00493
  //   fc9416e3 3200893 73 fff00293 7700493 849493 7748493 900533 2200893 73 1000e13 54c4b3 900533 2200893
  //   73 fffe0e13 fe0e16e3 a00893 73 13 430497 900533 2200893 73 430497 900533 2200893 73 430497 900533
  //   2200893 73 430497 900533 2200893 73 430497 900533 2200893 73 430497 900533 2200893 73 430497 900533
  //   2200893 73 430497 900533 2200893 73 a00893 73 313 2000e13 493 100913 930023 900533 2200893 73
  //   12484b3 130313 fffe0e13 fe0e12e3 800e13 313 32483 900533 2200893 73 430313 fffe0e13 fe0e14e3 a00893
  //   73 f00493 900533 2200893 73 fff48493 fe04d8e3 a00893 73 a00893 73 413 140413 800533 2200893 73
  //   240413 800533 2200893 73 340413 800533 2200893 73 440413 800533 2200893 73 540413 800533 2200893 73
  //   640413 800533 2200893 73 740413 800533 2200893 73 840413 800533 2200893 2200893 73 8067
  //   指令字
  //   JAL
  //   JALR
  //   Beq
  //   Bne
  //   MemToReg
  //   MemWrite
  //   AluOP
  //   AluSrcB
  //   RegWrite
  //   控制位
  //   流水调试日志用
  //   暂停节拍，不能为0
  //   戳工具置1进入计数暂停模式，ctrl+k时钟自动运行到对应节拍暂停
  //   ctrl+k关闭时钟连续运行，将控制位置零，进入单步调试模式调试
  //   可计数暂停的时钟源
  //   为方便自动评测，需要输出流水线各段保存的PC值，注意是PC不是PC+4，另外ID段寄存器写入信息，Mem段内存写入信息也要输出
  //   数据存储器
endmodule
module \重定向流水线  (
  output RegWrite,
  output MemWrite,
  output [31:0] IF_PC,
  output [31:0] ID_PC,
  output [31:0] EX_PC,
  output [31:0] M_PC,
  output [31:0] WB_PC,
  output [31:0] RDin,
  output [31:0] MDin,
  output [31:0] LedData
);

  wire alu_1_out_6, and_1_out, and_2_out, and_4_out, and_5_out, and_6_out, and_7_out, and_8_out, and_9_out,
       and_10_out, and_11_out, Auipc, Beq, Bge, Bne, Branch, BranchTaken, Byte, CLK, clock_1_out,
       comparator_2_eq, comparator_2_lt, comparator_3_eq, comparator_4_eq, comparator_5_eq, d_ff_1_q, Ecall,
       Equ, ex_mem_1_auipc_2, ex_mem_1_byte_2, ex_mem_1_ecall_2, ex_mem_1_jal_jalr_2, ex_mem_1_less_2,
       ex_mem_1_memtoreg_2, ex_mem_1_regwrite_2, ex_mem_1_shouldhalt_2, ex_mem_1_slt_2, Flush, Geq, Go, halt,
       id_ex_1_alusrc_2, id_ex_1_auipc_2, id_ex_1_beq_2, id_ex_1_bge_2, id_ex_1_bne_2, id_ex_1_byte_2,
       id_ex_1_ecall_2, id_ex_1_jal_2, id_ex_1_jalr_2, id_ex_1_memtoreg_2, id_ex_1_memwrite_2,
       id_ex_1_regwrite_2, if_id_1_p5, IR1, IR2, IR3, Jal, Jalr, JJump, me_wb_1_ecall_2, me_wb_1_memtoreg_2,
       me_wb_1_shouldhalt_2, nand_1_out, nand_2_out, not_1_out, not_2_out, not_3_out, not_4_out, not_5_out,
       not_6_out, not_7_out, not_8_out, or_1_out, or_3_out, riscv_probe_3_p1, RST, stall, Uret, W1, W2, W3,
       \单周期硬布线控制器_1_alu_src , \单周期硬布线控制器_1_memtoreg , \单周期硬布线控制器_1_memwrite , \单周期硬布线控制器_1_regwrite ,
       \单周期硬布线控制器_1_rsused , \单周期硬布线控制器_1_rtused , \单周期硬布线控制器_1_s_type , \气泡_重定向处理逻辑_1_if_id_en ,
       \气泡_重定向处理逻辑_1_pc_en ;
  wire [1:0] EX_RsFoward, EX_RtFoward, ID_RsFoward, ID_RtFoward, multiplexer_11_out;
  wire [3:0] id_ex_1_aluop_2, \单周期硬布线控制器_1_alu_op ;
  wire [4:0] ex_mem_1_rd_2, id_ex_1_rd_2, me_wb_1_rd_4, multiplexer_2_out, multiplexer_3_out;
  wire [12:0] CNT_num;
  wire [15:0] \LoadUse次数 , \总周期数 , \插入气泡数 , \无条件分支数 , \条件分支成功数 ;
  wire [31:0] adder_1_out, adder_2_out, adder_3_out, adder_4_out, adder_5_out, alu_1_result, and_3_out,
       bit_extender_1_out, bit_extender_2_out, bit_extender_3_out, bit_extender_4_out, bit_extender_5_out,
       bit_extender_6_out, EX_IR, ex_mem_1_aluresult_2, ex_mem_1_uimm_2, EX_RE_RS, EX_RE_RT, EX_RS, EX_RT,
       id_ex_1_bimm_2, id_ex_1_imm_2, id_ex_1_jimm_2, id_ex_1_uimm_2, ID_IR, IF_IR, me_wb_1_aluresult_2,
       me_wb_1_rd_3, MEM_IR, mips_ram_1_dataout, multiplexer_1_out, multiplexer_4_out, multiplexer_5_out,
       multiplexer_6_out, multiplexer_7_out, multiplexer_8_out, multiplexer_12_out, multiplexer_13_out,
       multiplexer_14_out, regifile_1_r1, regifile_1_r2, shifter_1_out, shifter_2_out, shifter_3_out, WB_IR;

  Button \u_总复位  (.out(RST));
  Button _1 (.out(IR1));
  Button _2 (.out(IR2));
  Button _3 (.out(IR3));
  // Probe on \总周期数 
  // Probe on \总周期数 
  Button \u_继续运行  (.out(Go));
  LED #(.active("true")) led_1 (.in(W1));
  LED #(.active("true")) led_2 (.in(W2));
  LED #(.active("true")) led_3 (.in(W3));
  not not_1 (not_1_out, halt);
  and and_1 (and_1_out, not_1_out, \气泡_重定向处理逻辑_1_pc_en );
  Multiplexer #(.select(1), .width(32), .disabled("Z"), .enable("false")) multiplexer_1 (
    .in0(adder_1_out), .in1(multiplexer_7_out), .out(multiplexer_1_out), .sel(BranchTaken));
  Hex_Digit_Display hex_digit_display_1 (.value(LedData[31:28]));  // open: dp
  // Probe on IF_PC[19:0]
  // RiscV_Probe riscv_probe_1: pin names not known; wires that end beside it: IF_IR
  Register #(.width(32), .trigger("rising"), .Select("low")) PC (
    .D(multiplexer_1_out), .en(and_1_out), .Q(IF_PC), .clk(CLK), .clr(riscv_probe_3_p1));
  Hex_Digit_Display hex_digit_display_2 (.value(LedData[23:20]));  // open: dp
  Hex_Digit_Display hex_digit_display_3 (.value(LedData[27:24]));  // open: dp
  // Probe on ID_PC[19:0]
  // RiscV_Probe riscv_probe_2: pin names not known; wires that end beside it: ID_IR
  Hex_Digit_Display hex_digit_display_4 (.value(LedData[15:12]));  // open: dp
  Hex_Digit_Display hex_digit_display_5 (.value(LedData[19:16]));  // open: dp
  // RiscV_Probe riscv_probe_3: pin names not known; wires that end beside it: riscv_probe_3_p1, RST, IF_IR, IF_IR
  Adder #(.width(32)) adder_1 (.a(IF_PC), .b(32'h4), .out(adder_1_out));  // open: cin, cout
  Hex_Digit_Display hex_digit_display_6 (.value(LedData[7:4]));  // open: dp
  Hex_Digit_Display hex_digit_display_7 (.value(LedData[11:8]));  // open: dp
  // Probe on EX_PC[19:0]
  // RiscV_Probe riscv_probe_4: pin names not known; wires that end beside it: EX_IR
  not not_2 (not_2_out, halt);
  and and_2 (and_2_out, not_2_out, \气泡_重定向处理逻辑_1_if_id_en );
  ROM #(.addrWidth(10), .dataWidth(32), .Select("high")) rom_1 (.addr(IF_PC[11:2]), .data(IF_IR));
  Hex_Digit_Display hex_digit_display_8 (.value(LedData[3:0]));  // open: dp
  // IF_ID if_id_1: pin names not known; wires that end beside it: IF_IR, IF_PC, and_2_out, CLK, if_id_1_p5, 1'b0, ID_IR, ID_PC
  // Probe on \总周期数 
  // Probe on M_PC[19:0]
  // RiscV_Probe riscv_probe_5: pin names not known; wires that end beside it: MEM_IR
  // Probe on \总周期数 
  // Probe on \无条件分支数 
  // Probe on \条件分支成功数 
  // Probe on \插入气泡数 
  // Probe on \LoadUse次数 
  \单周期硬布线控制器  \u_单周期硬布线控制器_1  (
    .Funct({ID_IR[30], ID_IR[25], ID_IR[14:12]}), .OP(ID_IR[6:2]), .ALU_OP(\单周期硬布线控制器_1_alu_op ),
    .MemToReg(\单周期硬布线控制器_1_memtoreg ), .MemWrite(\单周期硬布线控制器_1_memwrite ), .ALU_SRC(\单周期硬布线控制器_1_alu_src ),
    .RegWrite(\单周期硬布线控制器_1_regwrite ), .ecall(Ecall), .S_type(\单周期硬布线控制器_1_s_type ), .Jalr(Jalr), .Beq(Beq),
    .JAL(Jal), .Bne(Bne), .in_3(ID_IR[21]), .uret(Uret), .Auipc(Auipc), .Byte(Byte), .BGE(Bge),
    .RsUsed(\单周期硬布线控制器_1_rsused ), .RtUsed(\单周期硬布线控制器_1_rtused ));  // open: CSRRSI, CSRRCI
  Multiplexer #(.select(1), .width(5), .disabled("Z"), .enable("false")) multiplexer_2 (
    .in0(ID_IR[19:15]), .in1(5'b10001), .out(multiplexer_2_out), .sel(Ecall));
  // Probe on multiplexer_2_out
  Multiplexer #(.select(1), .width(5), .disabled("Z"), .enable("false")) multiplexer_3 (
    .in0(ID_IR[24:20]), .in1(5'b01010), .out(multiplexer_3_out), .sel(Ecall));
  // Probe on multiplexer_3_out
  assign bit_extender_1_out = {{20{ID_IR[31]}}, ID_IR[31:20]};  // Bit_Extender bit_extender_1
  assign bit_extender_2_out = {{20{ID_IR[31]}}, {ID_IR[31:25], ID_IR[11:7]}};  // Bit_Extender bit_extender_2
  // Probe on IF_PC[11:0]
  // Probe on WB_PC[19:0]
  // RiscV_Probe riscv_probe_6: pin names not known; wires that end beside it: WB_IR
  Multiplexer #(.select(1), .width(32), .disabled("Z"), .enable("false")) multiplexer_4 (
    .in0(bit_extender_1_out), .in1(bit_extender_2_out), .out(multiplexer_4_out), .sel(\单周期硬布线控制器_1_s_type ));
  assign bit_extender_3_out = {{20{ID_IR[31]}}, {ID_IR[31], ID_IR[7], ID_IR[30:25], ID_IR[11:8]}};  // Bit_Extender bit_extender_3
  assign bit_extender_4_out = {{12{ID_IR[31]}}, {ID_IR[31], ID_IR[19:12], ID_IR[20], ID_IR[30:21]}};  // Bit_Extender bit_extender_4
  assign bit_extender_5_out = {{12{ID_IR[31]}}, ID_IR[31:12]};  // Bit_Extender bit_extender_5
  Shifter #(.width(32), .shift("ll")) shifter_1 (.in(bit_extender_5_out), .\dist (5'b01100), .out(shifter_1_out));
  // Probe on ID_PC[11:0]
  // Probe on EX_PC[11:0]
  not not_3 (not_3_out, CLK);
  Regifile regifile_1 (
    .Din(RDin), .Clk(not_3_out), .R1(regifile_1_r1), .R2(regifile_1_r2), .WE(RegWrite), .W_num(me_wb_1_rd_4),
    .R1_num(multiplexer_2_out), .R2_num(multiplexer_3_out));
  Shifter #(.width(32), .shift("ll")) shifter_2 (.in(bit_extender_3_out), .\dist (5'b00001), .out(shifter_2_out));
  Shifter #(.width(32), .shift("ll")) shifter_3 (.in(bit_extender_4_out), .\dist (5'b00001), .out(shifter_3_out));
  Adder #(.width(32)) adder_2 (.a(shifter_1_out), .b(ID_PC), .out(adder_2_out));  // open: cin, cout
  Comparator #(.width(32), .mode("unsigned")) comparator_1 (
    .a({32{1'b1}}), .b(multiplexer_7_out), .gt(BranchTaken));  // open: eq, lt
  // Probe on M_PC[11:0]
  D_Flip_Flop #(.trigger("high"), .Pre_Clr_Positions("LEGACY"), .NegatePresetClear("false"), .enable("true"), .NewFFLayout("false")) d_ff_1 (.Q(d_ff_1_q));  // open: clk, D, Qn, preset, en, reset
  // Probe on 13'h16
  Adder #(.width(32)) adder_3 (.a(shifter_2_out), .b(ID_PC), .out(adder_3_out));  // open: cin, cout
  Adder #(.width(32)) adder_4 (.a(ID_PC), .b(shifter_3_out), .out(adder_4_out));  // open: cin, cout
  // Probe on WB_PC[11:0]
  Comparator #(.width(13), .mode("twosComplement")) comparator_2 (
    .a(CNT_num), .b(13'h16), .eq(comparator_2_eq), .lt(comparator_2_lt));  // open: gt
  Clock #(.highDuration(1), .lowDuration(1)) clock_1 (.out(clock_1_out));
  not not_4 (not_4_out, halt);
  ID_EX id_ex_1 (
    .RegWrite(\单周期硬布线控制器_1_regwrite ), .R1(regifile_1_r1), .R2(regifile_1_r2), .rd(ID_IR[11:7]),
    .Imm(multiplexer_4_out), .PC(ID_PC), .RegWrite_2(id_ex_1_regwrite_2), .R1_2(EX_RS), .R2_2(EX_RT),
    .rd_2(id_ex_1_rd_2), .Imm_2(id_ex_1_imm_2), .PC_2(EX_PC), .CLK(CLK), .MemToReg(\单周期硬布线控制器_1_memtoreg ),
    .MemToReg_2(id_ex_1_memtoreg_2), .MemWrite(\单周期硬布线控制器_1_memwrite ), .MemWrite_2(id_ex_1_memwrite_2),
    .AluOP(\单周期硬布线控制器_1_alu_op ), .AluOP_2(id_ex_1_aluop_2), .Bne(Bne), .Bne_2(id_ex_1_bne_2),
    .AluSrc(\单周期硬布线控制器_1_alu_src ), .AluSrc_2(id_ex_1_alusrc_2), .Beq(Beq), .Beq_2(id_ex_1_beq_2), .Bge(Bge),
    .Bge_2(id_ex_1_bge_2), .Auipc(Auipc), .Auipc_2(id_ex_1_auipc_2), .Byte(Byte), .Byte_2(id_ex_1_byte_2),
    .Jalr(Jalr), .Jalr_2(id_ex_1_jalr_2), .Jal(Jal), .Jal_2(id_ex_1_jal_2), .BImm(adder_3_out),
    .BImm_2(id_ex_1_bimm_2), .JImm(adder_4_out), .JImm_2(id_ex_1_jimm_2), .UImm(adder_2_out),
    .UImm_2(id_ex_1_uimm_2), .Ecall(Ecall), .Ecall_2(id_ex_1_ecall_2), .IR(ID_IR), .IR_2(EX_IR),
    .Flush(Flush), .En(not_4_out), .RsFoward(ID_RsFoward), .RsFoward_2(EX_RsFoward), .RtFoward(ID_RtFoward),
    .RtFoward_2(EX_RtFoward));  // open: Uert, Uert_2, PredictJump, PredictJump_2
  nand nand_1 (nand_1_out, d_ff_1_q, comparator_2_eq);
  Counter #(.width(13), .max('h1fff), .ongoal("stay"), .trigger("rising"), .behavior("old")) counter_1 (
    .count(comparator_2_lt), .Q(CNT_num), .clk(clock_1_out));  // open: load, D, carry, clr, preset
  or or_1 (or_1_out, id_ex_1_jalr_2, id_ex_1_jal_2);
  assign CLK = nand_1_out ? clock_1_out : 1'bz;  // Controlled_Buffer controlled_buffer_1
  Multiplexer #(.select(1), .width(32), .disabled("Z"), .enable("false")) multiplexer_5 (
    .in0({32{1'b1}}), .in1(and_3_out), .out(multiplexer_5_out), .sel(id_ex_1_jalr_2));
  or or_2 (JJump, id_ex_1_jal_2, id_ex_1_jalr_2);
  Pull_Resistor #(.pull(1)) pull_resistor_1 (.node(CLK));
  Multiplexer #(.select(1), .width(32), .disabled("Z"), .enable("false")) multiplexer_6 (
    .in0(multiplexer_5_out), .in1(id_ex_1_bimm_2), .out(multiplexer_6_out), .sel(Branch));
  Multiplexer #(.select(1), .width(32), .disabled("Z"), .enable("false")) multiplexer_7 (
    .in0(multiplexer_6_out), .in1(id_ex_1_jimm_2), .out(multiplexer_7_out), .sel(id_ex_1_jal_2));
  Comparator #(.width(4), .mode("unsigned")) comparator_3 (
    .a(id_ex_1_aluop_2), .b(4'b1100), .eq(comparator_3_eq));  // open: gt, lt
  Comparator #(.width(4), .mode("unsigned")) comparator_4 (
    .a(id_ex_1_aluop_2), .b(4'b1011), .eq(comparator_4_eq));  // open: gt, lt
  Comparator #(.width(32), .mode("twosComplement")) comparator_5 (
    .a(EX_RE_RS), .b(32'h22), .eq(comparator_5_eq));  // open: gt, lt
  nand nand_2 (nand_2_out, comparator_5_eq, id_ex_1_ecall_2);
  Multiplexer #(.select(1), .width(32), .disabled("Z"), .enable("false")) multiplexer_8 (
    .in0(EX_RE_RT), .in1(id_ex_1_imm_2), .out(multiplexer_8_out), .sel(id_ex_1_alusrc_2));
  not not_5 (not_5_out, Equ);
  or or_3 (or_3_out, comparator_3_eq, comparator_4_eq);
  ALU alu_1 (
    .X(EX_RE_RS), .Y(multiplexer_8_out), .AluOP(id_ex_1_aluop_2), .Equal(Equ), .Result(alu_1_result),
    .out_4(Geq), .out_6(alu_1_out_6));  // open: Result_2
  assign and_3_out = 32'hfffe & alu_1_result;  // AND_Gate and_3, 32 bits wide
  and and_4 (and_4_out, id_ex_1_beq_2, Equ);
  and and_5 (and_5_out, id_ex_1_bne_2, not_5_out);
  and and_6 (and_6_out, id_ex_1_bge_2, Geq);
  or or_4 (Branch, and_6_out, and_5_out, and_4_out);
  Multiplexer #(.select(2), .width(32), .disabled("Z"), .enable("false")) multiplexer_9 (
    .in0(EX_RS), .in1(RDin), .in2(multiplexer_14_out), .out(EX_RE_RS), .sel(EX_RsFoward));  // open: in3
  Multiplexer #(.select(2), .width(32), .disabled("Z"), .enable("false")) multiplexer_10 (
    .in0(EX_RT), .in1(RDin), .in2(multiplexer_14_out), .out(EX_RE_RT), .sel(EX_RtFoward));  // open: in3
  Register #(.width(32), .trigger("rising"), .Select("low")) register_1 (
    .D(EX_RE_RT), .en(not_6_out), .Q(LedData), .clk(CLK));  // open: clr
  not not_6 (not_6_out, nand_2_out);
  not not_7 (not_7_out, halt);
  EX_MEM ex_mem_1 (
    .AluResult(alu_1_result), .WriteData(EX_RE_RT), .rd(id_ex_1_rd_2), .AluResult_2(ex_mem_1_aluresult_2),
    .WriteData_2(MDin), .rd_2(ex_mem_1_rd_2), .CLK(CLK), .RegWrite(id_ex_1_regwrite_2),
    .RegWrite_2(ex_mem_1_regwrite_2), .MemToReg(id_ex_1_memtoreg_2), .MemToReg_2(ex_mem_1_memtoreg_2),
    .MemWrite(id_ex_1_memwrite_2), .MemWrite_2(MemWrite), .Byte(id_ex_1_byte_2), .Byte_2(ex_mem_1_byte_2),
    .Ecall(id_ex_1_ecall_2), .Ecall_2(ex_mem_1_ecall_2), .ShouldHalt(nand_2_out),
    .ShouldHalt_2(ex_mem_1_shouldhalt_2), .Auipc(id_ex_1_auipc_2), .Auipc_2(ex_mem_1_auipc_2),
    .Less(alu_1_out_6), .Less_2(ex_mem_1_less_2), .Slt(or_3_out), .Slt_2(ex_mem_1_slt_2),
    .Jal_Jalr(or_1_out), .Jal_Jalr_2(ex_mem_1_jal_jalr_2), .PC(EX_PC), .PC_2(M_PC), .UImm(id_ex_1_uimm_2),
    .UImm_2(ex_mem_1_uimm_2), .IR(EX_IR), .IR_2(MEM_IR), .En(not_7_out), .Flush(1'b0));  // open: Uert_2, Uert
  assign bit_extender_6_out = {{31{1'b0}}, ex_mem_1_less_2};  // Bit_Extender bit_extender_6
  MIPS_RAM mips_ram_1 (
    .\字节地址 (ex_mem_1_aluresult_2[11:0]), .Din(MDin), .DataOut(mips_ram_1_dataout), .CLK(CLK), .WE(MemWrite),
    .Mode(multiplexer_11_out));
  Multiplexer #(.select(1), .width(2), .disabled("Z"), .enable("false")) multiplexer_11 (
    .in0(2'b00), .in1(2'b01), .out(multiplexer_11_out), .sel(ex_mem_1_byte_2));
  Multiplexer #(.select(1), .width(32), .disabled("Z"), .enable("false")) multiplexer_12 (
    .in0(ex_mem_1_aluresult_2), .in1(bit_extender_6_out), .out(multiplexer_12_out), .sel(ex_mem_1_slt_2));
  Adder #(.width(32)) adder_5 (.a(M_PC), .b(32'h4), .out(adder_5_out));  // open: cin, cout
  Multiplexer #(.select(1), .width(32), .disabled("Z"), .enable("false")) multiplexer_13 (
    .in0(multiplexer_12_out), .in1(adder_5_out), .out(multiplexer_13_out), .sel(ex_mem_1_jal_jalr_2));
  \气泡_重定向处理逻辑  \u_气泡_重定向处理逻辑_1  (
    .RsUsed(\单周期硬布线控制器_1_rsused ), .rs(multiplexer_2_out), .RtUsed(\单周期硬布线控制器_1_rtused ),
    .rt(multiplexer_3_out), .MEM_RegWrite(ex_mem_1_regwrite_2), .MEM_WriteReg_V(ex_mem_1_rd_2),
    .EX_WriteReg_V(id_ex_1_rd_2), .BranchTaken(BranchTaken), .Stall(stall), .PC_EN(\气泡_重定向处理逻辑_1_pc_en ),
    .IF_ID_EN(\气泡_重定向处理逻辑_1_if_id_en ), .IF_ID_CLR(if_id_1_p5), .ID_EX_CLR(Flush),
    .EX_MemToReg(id_ex_1_memtoreg_2), .EX_RegWrite(id_ex_1_regwrite_2), .RsFoward(ID_RsFoward),
    .RtFoward(ID_RtFoward));  // open: Flush, LoadUse
  Multiplexer #(.select(1), .width(32), .disabled("Z"), .enable("false")) multiplexer_14 (
    .in0(multiplexer_13_out), .in1(ex_mem_1_uimm_2), .out(multiplexer_14_out), .sel(ex_mem_1_auipc_2));
  not not_8 (not_8_out, halt);
  ME_WB me_wb_1 (
    .RegWrite(ex_mem_1_regwrite_2), .MemToReg(ex_mem_1_memtoreg_2), .AluResult(multiplexer_14_out),
    .RD(mips_ram_1_dataout), .rd_2(ex_mem_1_rd_2), .RegWrite_2(RegWrite), .MemToReg_2(me_wb_1_memtoreg_2),
    .AluResult_2(me_wb_1_aluresult_2), .RD_3(me_wb_1_rd_3), .rd_4(me_wb_1_rd_4), .CLK(CLK),
    .ShouldHalt(ex_mem_1_shouldhalt_2), .ShouldHalt_2(me_wb_1_shouldhalt_2), .Ecall(ex_mem_1_ecall_2),
    .Ecall_2(me_wb_1_ecall_2), .PC(M_PC), .PC_2(WB_PC), .IR(MEM_IR), .IR_2(WB_IR), .En(not_8_out));
  Multiplexer #(.select(1), .width(32), .disabled("Z"), .enable("false")) multiplexer_15 (
    .in0(me_wb_1_aluresult_2), .in1(me_wb_1_rd_3), .out(RDin), .sel(me_wb_1_memtoreg_2));
  D_Flip_Flop #(.trigger("falling"), .Pre_Clr_Positions("ABOVE_BELOW"), .NegatePresetClear("false"), .enable("true"), .NewFFLayout("true")) d_ff_2 (
    .clk(CLK), .D(me_wb_1_shouldhalt_2), .Q(halt), .en(me_wb_1_ecall_2), .reset(Go));  // open: Qn, preset
  Counter #(.width(16), .max('hffff), .ongoal("wrap"), .trigger("rising"), .behavior("new")) counter_2 (
    .count(Branch), .Q(\条件分支成功数 ), .clk(and_7_out), .clr(RST));  // open: load, D, carry, preset, down
  and and_7 (and_7_out, ~halt, CLK);  // AND_Gate
  Counter #(.width(16), .max('hffff), .ongoal("wrap"), .trigger("rising"), .behavior("new")) counter_3 (
    .count(Flush), .Q(\插入气泡数 ), .clk(and_8_out), .clr(RST));  // open: load, D, carry, preset, down
  and and_8 (and_8_out, ~halt, CLK);  // AND_Gate
  Counter #(.width(16), .max('hffff), .ongoal("wrap"), .trigger("rising"), .behavior("new")) counter_4 (
    .count(JJump), .Q(\无条件分支数 ), .clk(and_9_out), .clr(RST));  // open: load, D, carry, preset, down
  and and_9 (and_9_out, ~halt, CLK);  // AND_Gate
  Counter #(.width(16), .max('hffff), .ongoal("wrap"), .trigger("rising"), .behavior("new")) counter_5 (
    .count(CLK), .Q(\总周期数 ), .clk(and_10_out), .clr(RST));  // open: load, D, carry, preset, down
  and and_10 (and_10_out, ~halt, CLK);  // AND_Gate
  Counter #(.width(16), .max('hffff), .ongoal("wrap"), .trigger("rising"), .behavior("new")) counter_6 (
    .count(stall), .Q(\LoadUse次数 ), .clk(and_11_out), .clr(RST));  // open: load, D, carry, preset, down
  and and_11 (and_11_out, ~halt, CLK);  // AND_Gate

  // Other names for the same wires on the sheet: MEM_PC[31:0] = M_PC; PC[31:0] = IF_PC

  // Notes on the sheet:
  //   中断源
  //   时空图监测，可删除
  //   中断等待指示
  //   数码管输出
  //   指令探针
  //   指令存储器
  //   contents of rom_1 (hex, n*v repeats v):
  //   100493 100006f 100493 200913 300993 100006f 100493 200913 300993 100006f 100493 200913 300993
  //   100006f 100493 200913 300993 3ec000ef 100413 100493 1f49493 900533 2200893 73 24d493 48463 fedff06f
  //   900533 2200893 73 100493 249493 900533 2200893 73 48463 fedff06f 100493 1f49493 900533 2200893 73
  //   4034d493 900533 2200893 73 4044d493 900533 2200893 73 4044d493 900533 2200893 73 4044d493 900533
  //   2200893 73 4044d493 900533 2200893 73 4044d493 900533 2200893 73 4044d493 900533 2200893 73 4044d493
  //   900533 2200893 73 100413 1f41993 41f9d993 433 c00913 300b13 140413 f47413 800293 100313 499993
  //   89e9b3 1300533 2200893 73 406282b3 fe0294e3 140413 f00f93 1f47433 1c41413 800293 100313 49d993
  //   89e9b3 1300533 2200893 73 406282b3 fe0294e3 1c45413 406b0b33 b0463 f95ff06f 2b3 fff2c293 829293
  //   ff2e293 500533 2200893 73 fff00413 493 84a023 140413 448493 84a023 140413 448493 84a023 140413
  //   448493 84a023 140413 448493 84a023 140413 448493 84a023 140413 448493 84a023 140413 448493 84a023
  //   140413 448493 84a023 140413 448493 84a023 140413 448493 84a023 140413 448493 84a023 140413 448493
  //   84a023 140413 448493 84a023 140413 448493 84a023 140413 448493 84a023 140413 448493 140413 433
  //   3c00493 42983 4aa03 149a2b3 28663 134a023 1442023 ffc48493 fe9412e3 800533 2200893 73 440413 3c00493
  //   fc9416e3 3200893 73 fff00293 7700493 849493 7748493 900533 2200893 73 1000e13 54c4b3 900533 2200893
  //   73 fffe0e13 fe0e16e3 a00893 73 13 430497 900533 2200893 73 430497 900533 2200893 73 430497 900533
  //   2200893 73 430497 900533 2200893 73 430497 900533 2200893 73 430497 900533 2200893 73 430497 900533
  //   2200893 73 430497 900533 2200893 73 a00893 73 313 2000e13 493 100913 930023 900533 2200893 73
  //   12484b3 130313 fffe0e13 fe0e12e3 800e13 313 32483 900533 2200893 73 430313 fffe0e13 fe0e14e3 a00893
  //   73 f00493 900533 2200893 73 fff48493 fe04d8e3 a00893 73 a00893 73 413 140413 800533 2200893 73
  //   240413 800533 2200893 73 340413 800533 2200893 73 440413 800533 2200893 73 540413 800533 2200893 73
  //   640413 800533 2200893 73 740413 800533 2200893 73 840413 800533 2200893 2200893 73 8067
  //   指令字
  //   JAL
  //   JALR
  //   Beq
  //   Bne
  //   MemToReg
  //   MemWrite
  //   AluOP
  //   AluSrcB
  //   RegWrite
  //   控制位
  //   流水调试日志用
  //   暂停节拍，不能为0
  //   戳工具置1进入计数暂停模式，ctrl+k时钟自动运行到对应节拍暂停
  //   ctrl+k关闭时钟连续运行，将控制位置零，进入单步调试模式调试
  //   可计数暂停的时钟源
  //   为方便自动评测，需要输出流水线各段保存的PC值，注意是PC不是PC+4，另外ID段寄存器写入信息，Mem段内存写入信息也要输出
  //   数据存储器
endmodule

module \中断按键参考电路  (
  input  \同步清零信号 ,
  output \与中断屏蔽位与 
);

  wire \_1号中断_out , and_1_out, clock_1_out, d_ff_1_q, or_1_out, or_2_out;

  Clock #(.highDuration(1), .lowDuration(1)) clock_1 (.out(clock_1_out));
  Button \_1号中断  (.out(\_1号中断_out ));
  LED #(.active("true")) \_1号中断等待指示灯  (.in(or_1_out));
  or or_1 (or_1_out, \与中断屏蔽位与 , d_ff_1_q);
  D_Flip_Flop #(.trigger("rising"), .Pre_Clr_Positions("LEGACY"), .NegatePresetClear("false"), .enable("true"), .NewFFLayout("false")) d_ff_1 (
    .clk(\_1号中断_out ), .D(1'b1), .Q(d_ff_1_q), .reset(\与中断屏蔽位与 ));  // open: Qn, preset, en
  or or_2 (or_2_out, d_ff_1_q, \与中断屏蔽位与 );
  and and_1 (and_1_out, or_2_out, ~\同步清零信号 );  // AND_Gate
  D_Flip_Flop #(.trigger("rising"), .Pre_Clr_Positions("LEGACY"), .NegatePresetClear("false"), .enable("true"), .NewFFLayout("false")) IR1 (
    .clk(clock_1_out), .D(and_1_out), .Q(\与中断屏蔽位与 ));  // open: Qn, preset, en, reset

  // Notes on the sheet:
  //   中断信号采样参考电路
  //   Reset 
endmodule

module \单周期_单级中断  (
  input  IR1,
  input  IR2,
  input  IR3,
  output RegWrite,
  output MemWrite,
  output [31:0] PC,
  output [31:0] IR,
  output [31:0] RDin,
  output [31:0] MDin,
  output [31:0] LedData
);

  wire alu_1_equal, and_1_out, and_2_out, and_3_out, and_4_out, and_6_out, and_7_out, and_8_out, Auipc, BGE,
       Byte, CanBe, CLK, clock_1_out, clock_2_out, clock_3_out, clock_4_out, comparator_1_eq,
       comparator_2_eq, comparator_3_eq, comparator_4_eq, comparator_5_eq, comparator_6_eq, comparator_7_eq,
       comparator_7_lt, comparator_8_eq, comparator_9_eq, d_ff_1_q, d_ff_2_q, d_ff_3_q, d_ff_4_q, Ecall, Geq,
       Go, halt, IE, IR1_q, IR1_t, IR2_q, IR2_t, IR3_q, IR3_t, IRA, IRB, IRC, JAL, JALR, Less, MemToReg,
       nand_1_out, nand_2_out, not_1_out, not_2_out, not_3_out, not_4_out, not_5_out, or_1_out, or_2_out,
       or_3_out, or_4_out, or_5_out, or_6_out, or_7_out, or_11_out, or_13_out, or_14_out,
       priority_encoder_1_gs, ResetIR1, ResetIR2, ResetIR3, riscv_probe_1_p1, RST, S_type, UERT, W1, W2, W3,
       \单周期硬布线控制器_1_alu_src , \单周期硬布线控制器_1_beq , \单周期硬布线控制器_1_bne ;
  wire [1:0] IR_Id, multiplexer_11_out, register_1_q;
  wire [3:0] AluOP;
  wire [4:0] multiplexer_1_out, multiplexer_2_out;
  wire [12:0] CNT_num;
  wire [15:0] \总周期数 ;
  wire [31:0] adder_2_out, adder_3_out, adder_4_out, AluResult, and_5_out, bit_extender_1_out,
       bit_extender_2_out, bit_extender_3_out, bit_extender_4_out, bit_extender_5_out, bit_extender_6_out,
       EPC, mips_ram_1_dataout, multiplexer_3_out, multiplexer_4_out, multiplexer_5_out, multiplexer_6_out,
       multiplexer_7_out, multiplexer_8_out, multiplexer_12_out, multiplexer_13_out, multiplexer_14_out,
       NextPC, NextPCWithoutInt, PC_4, regifile_1_r1, shifter_1_out, shifter_2_out, shifter_3_out;

  Button \u_继续运行  (.out(Go));
  Button _1 (.out(IR1_t));
  Button _2 (.out(IR2_t));
  Button _3 (.out(IR3_t));
  LED #(.active("true")) led_1 (.in(W1));
  LED #(.active("true")) led_2 (.in(W2));
  LED #(.active("true")) led_3 (.in(W3));
  Hex_Digit_Display hex_digit_display_1 (.value(LedData[31:28]));  // open: dp
  Comparator #(.width(16), .mode("twosComplement")) comparator_1 (
    .a(16'h23b), .b(\总周期数 ), .eq(comparator_1_eq));  // open: gt, lt
  Comparator #(.width(16), .mode("twosComplement")) comparator_2 (
    .a(\总周期数 ), .b(16'h1), .eq(comparator_2_eq));  // open: gt, lt
  Comparator #(.width(16), .mode("twosComplement")) comparator_3 (
    .a(\总周期数 ), .b(16'h4), .eq(comparator_3_eq));  // open: gt, lt
  Comparator #(.width(16), .mode("twosComplement")) comparator_4 (
    .a(\总周期数 ), .b(16'h7), .eq(comparator_4_eq));  // open: gt, lt
  Clock #(.highDuration(1), .lowDuration(1)) clock_1 (.out(clock_1_out));
  LED #(.active("true")) \_1号中断等待指示灯  (.in(or_1_out));
  or or_1 (or_1_out, IR1_q, d_ff_1_q);
  Clock #(.highDuration(1), .lowDuration(1)) clock_2 (.out(clock_2_out));
  or or_2 (or_2_out, IR2_q, d_ff_2_q);
  LED #(.active("true")) \_2号中断等待指示灯  (.in(or_2_out));
  Clock #(.highDuration(1), .lowDuration(1)) clock_3 (.out(clock_3_out));
  LED #(.active("true")) \_3号中断等待指示灯  (.in(or_3_out));
  or or_3 (or_3_out, IR3_q, d_ff_3_q);
  Hex_Digit_Display hex_digit_display_2 (.value(LedData[27:24]));  // open: dp
  Hex_Digit_Display hex_digit_display_3 (.value(LedData[23:20]));  // open: dp
  or or_4 (or_4_out, comparator_1_eq, comparator_2_eq);
  assign IRA = or_4_out ? ~CLK : 1'bz;  // Controlled_Inverter controlled_inverter_1
  assign IRB = comparator_3_eq ? ~CLK : 1'bz;  // Controlled_Inverter controlled_inverter_2
  assign IRC = comparator_4_eq ? ~CLK : 1'bz;  // Controlled_Inverter controlled_inverter_3
  D_Flip_Flop #(.trigger("rising"), .Pre_Clr_Positions("LEGACY"), .NegatePresetClear("false"), .enable("true"), .NewFFLayout("false")) d_ff_1 (
    .clk(IR1_t), .D(1'b1), .Q(d_ff_1_q), .reset(IR1_q));  // open: Qn, preset, en
  D_Flip_Flop #(.trigger("rising"), .Pre_Clr_Positions("LEGACY"), .NegatePresetClear("false"), .enable("true"), .NewFFLayout("false")) d_ff_2 (
    .clk(IR2_t), .D(1'b1), .Q(d_ff_2_q), .reset(IR2_q));  // open: Qn, preset, en
  D_Flip_Flop #(.trigger("rising"), .Pre_Clr_Positions("LEGACY"), .NegatePresetClear("false"), .enable("true"), .NewFFLayout("false")) d_ff_3 (
    .clk(IR3_t), .D(1'b1), .Q(d_ff_3_q), .reset(IR3_q));  // open: Qn, preset, en
  Hex_Digit_Display hex_digit_display_4 (.value(LedData[15:12]));  // open: dp
  Hex_Digit_Display hex_digit_display_5 (.value(LedData[19:16]));  // open: dp
  Pull_Resistor #(.pull(0)) pull_resistor_1 (.node(IRA));
  Pull_Resistor #(.pull(0)) pull_resistor_2 (.node(IRB));
  Pull_Resistor #(.pull(0)) pull_resistor_3 (.node(IRC));
  not not_1 (not_1_out, halt);
  or or_5 (or_5_out, d_ff_1_q, IR1_q);
  or or_6 (or_6_out, d_ff_2_q, IR2_q);
  or or_7 (or_7_out, d_ff_3_q, IR3_q);
  Hex_Digit_Display hex_digit_display_6 (.value(LedData[7:4]));  // open: dp
  Hex_Digit_Display hex_digit_display_7 (.value(LedData[11:8]));  // open: dp
  // Probe on \总周期数 
  Register #(.width(32), .trigger("rising"), .Select("low")) u_PC (
    .D(NextPC), .en(not_1_out), .Q(PC), .clk(CLK), .clr(riscv_probe_1_p1));
  and and_1 (and_1_out, or_5_out, ~ResetIR1);  // AND_Gate
  and and_2 (and_2_out, or_6_out, ~ResetIR2);  // AND_Gate
  and and_3 (and_3_out, or_7_out, ~ResetIR3);  // AND_Gate
  Hex_Digit_Display hex_digit_display_8 (.value(LedData[3:0]));  // open: dp
  Adder #(.width(32)) adder_1 (.a(PC), .b(32'h4), .out(PC_4));  // open: cin, cout
  D_Flip_Flop #(.trigger("rising"), .Pre_Clr_Positions("LEGACY"), .NegatePresetClear("false"), .enable("true"), .NewFFLayout("false")) u_IR1 (
    .clk(clock_1_out), .D(and_1_out), .Q(IR1_q));  // open: Qn, preset, en, reset
  D_Flip_Flop #(.trigger("rising"), .Pre_Clr_Positions("LEGACY"), .NegatePresetClear("false"), .enable("true"), .NewFFLayout("false")) u_IR2 (
    .clk(clock_2_out), .D(and_2_out), .Q(IR2_q));  // open: Qn, preset, en, reset
  D_Flip_Flop #(.trigger("rising"), .Pre_Clr_Positions("LEGACY"), .NegatePresetClear("false"), .enable("true"), .NewFFLayout("false")) u_IR3 (
    .clk(clock_3_out), .D(and_3_out), .Q(IR3_q));  // open: Qn, preset, en, reset
  // RiscV_Probe riscv_probe_1: pin names not known; wires that end beside it: riscv_probe_1_p1, RST, IR, IR1_t, IR2_t
  ROM #(.addrWidth(10), .dataWidth(32), .Select("high")) rom_1 (.addr(PC[11:2]), .data(IR));
  // OR_Gate or_8 has open pins: in0=IR1, in1=IRA, out=open
  // OR_Gate or_9 has open pins: in0=IR2, in1=IRB, out=open
  \单周期硬布线控制器  \u_单周期硬布线控制器_1  (
    .Funct({IR[30], IR[25], IR[14:12]}), .OP(IR[6:2]), .ALU_OP(AluOP), .MemToReg(MemToReg),
    .MemWrite(MemWrite), .ALU_SRC(\单周期硬布线控制器_1_alu_src ), .RegWrite(RegWrite), .ecall(Ecall),
    .S_type(S_type), .Jalr(JALR), .Beq(\单周期硬布线控制器_1_beq ), .JAL(JAL), .Bne(\单周期硬布线控制器_1_bne ), .in_3(IR[21]),
    .uret(UERT), .Auipc(Auipc), .Byte(Byte), .BGE(BGE));  // open: RsUsed, RtUsed, CSRRSI, CSRRCI
  Multiplexer #(.select(1), .width(5), .disabled("Z"), .enable("false")) multiplexer_1 (
    .in0(IR[19:15]), .in1(5'b10001), .out(multiplexer_1_out), .sel(Ecall));
  Multiplexer #(.select(1), .width(5), .disabled("Z"), .enable("false")) multiplexer_2 (
    .in0(IR[24:20]), .in1(5'b01010), .out(multiplexer_2_out), .sel(Ecall));
  assign bit_extender_1_out = {{20{IR[31]}}, IR[31:20]};  // Bit_Extender bit_extender_1
  assign bit_extender_2_out = {{20{IR[31]}}, {IR[31:25], IR[11:7]}};  // Bit_Extender bit_extender_2
  // Probe on multiplexer_1_out
  // Probe on multiplexer_2_out
  Multiplexer #(.select(1), .width(32), .disabled("Z"), .enable("false")) multiplexer_3 (
    .in0(bit_extender_1_out), .in1(bit_extender_2_out), .out(multiplexer_3_out), .sel(S_type));
  assign bit_extender_3_out = {{20{IR[31]}}, {IR[31], IR[7], IR[30:25], IR[11:8]}};  // Bit_Extender bit_extender_3
  assign bit_extender_4_out = {{12{IR[31]}}, {IR[31], IR[19:12], IR[20], IR[30:21]}};  // Bit_Extender bit_extender_4
  Multiplexer #(.select(2), .width(32), .disabled("Z"), .enable("false")) multiplexer_4 (
    .in0(NextPCWithoutInt), .in1(32'h30ac), .in2(32'h3150), .in3(32'h31f4), .out(multiplexer_4_out),
    .sel(IR_Id));
  Priority_Encoder #(.select(2), .disabled("Z")) priority_encoder_1 (
    .in0(1'b0), .in1(IR1_q), .in2(IR2_q), .in3(IR3_q), .out(IR_Id), .gs(priority_encoder_1_gs));  // open: en_out, en_in
  // OR_Gate or_10 has open pins: in0=IR3, in1=IRC, out=open
  Shifter #(.width(32), .shift("ll")) shifter_1 (.in(bit_extender_3_out), .\dist (5'b00001), .out(shifter_1_out));
  Shifter #(.width(32), .shift("ll")) shifter_2 (.in(bit_extender_4_out), .\dist (5'b00001), .out(shifter_2_out));
  and and_4 (and_4_out, priority_encoder_1_gs, IE);
  not not_2 (not_2_out, and_4_out);
  Register #(.width(32), .trigger("rising"), .Select("low")) u_EPC (
    .D(NextPCWithoutInt), .en(and_4_out), .Q(EPC), .clk(CLK));  // open: clr
  Demultiplexer #(.select(2), .width(1), .tristate("false"), .disabled("Z"), .enable("false")) demultiplexer_1 (
    .out1(ResetIR1), .out2(ResetIR2), .out3(ResetIR3), .in(UERT), .sel(register_1_q));  // open: out0
  Register #(.width(2), .trigger("rising"), .Select("low")) register_1 (
    .D(IR_Id), .en(and_4_out), .Q(register_1_q), .clk(CLK));  // open: clr
  Regifile regifile_1 (
    .Din(RDin), .Clk(CLK), .R1(regifile_1_r1), .R2(MDin), .WE(RegWrite), .W_num(IR[11:7]),
    .R1_num(multiplexer_1_out), .R2_num(multiplexer_2_out));
  Adder #(.width(32)) adder_2 (.a(shifter_1_out), .b(PC), .out(adder_2_out));  // open: cin, cout
  Multiplexer #(.select(1), .width(32), .disabled("Z"), .enable("false")) multiplexer_5 (
    .in0(multiplexer_8_out), .in1(adder_2_out), .out(multiplexer_5_out), .sel(CanBe));
  Adder #(.width(32)) adder_3 (.a(PC), .b(shifter_2_out), .out(adder_3_out));  // open: cin, cout
  Multiplexer #(.select(1), .width(32), .disabled("Z"), .enable("false")) multiplexer_6 (
    .in0(NextPCWithoutInt), .in1(multiplexer_4_out), .out(multiplexer_6_out), .sel(and_4_out));
  Multiplexer #(.select(1), .width(32), .disabled("Z"), .enable("false")) multiplexer_7 (
    .in0(MDin), .in1(multiplexer_3_out), .out(multiplexer_7_out), .sel(\单周期硬布线控制器_1_alu_src ));
  Multiplexer #(.select(1), .width(32), .disabled("Z"), .enable("false")) multiplexer_8 (
    .in0(PC_4), .in1(and_5_out), .out(multiplexer_8_out), .sel(JALR));
  Multiplexer #(.select(1), .width(32), .disabled("Z"), .enable("false")) multiplexer_9 (
    .in0(multiplexer_5_out), .in1(adder_3_out), .out(NextPCWithoutInt), .sel(JAL));
  Multiplexer #(.select(1), .width(32), .disabled("Z"), .enable("false")) multiplexer_10 (
    .in0(multiplexer_6_out), .in1(EPC), .out(NextPC), .sel(UERT));
  Comparator #(.width(16), .mode("twosComplement")) comparator_5 (
    .a(\总周期数 ), .b({16{1'b0}}), .eq(comparator_5_eq));  // open: gt, lt
  not not_3 (not_3_out, alu_1_equal);
  Comparator #(.width(32), .mode("twosComplement")) comparator_6 (
    .a(regifile_1_r1), .b(32'h22), .eq(comparator_6_eq));  // open: gt, lt
  ALU alu_1 (
    .X(regifile_1_r1), .Y(multiplexer_7_out), .AluOP(AluOP), .Equal(alu_1_equal), .Result(AluResult),
    .out_4(Geq), .out_6(Less));  // open: Result_2
  assign and_5_out = 32'hfffe & AluResult;  // AND_Gate and_5, 32 bits wide
  or or_11 (or_11_out, UERT, and_4_out, comparator_5_eq);
  and and_6 (and_6_out, \单周期硬布线控制器_1_beq , alu_1_equal);
  or or_12 (CanBe, and_6_out, and_7_out, and_8_out);
  and and_7 (and_7_out, \单周期硬布线控制器_1_bne , not_3_out);
  and and_8 (and_8_out, BGE, Geq);
  nand nand_1 (nand_1_out, comparator_6_eq, Ecall);
  Register #(.width(1), .trigger("rising"), .Select("low")) u_IE (
    .D(not_2_out), .en(or_11_out), .Q(IE), .clk(CLK));  // open: clr
  Register #(.width(32), .trigger("rising"), .Select("low")) register_2 (
    .D(MDin), .en(not_4_out), .Q(LedData), .clk(CLK));  // open: clr
  not not_4 (not_4_out, nand_1_out);
  not not_5 (not_5_out, halt);
  MIPS_RAM mips_ram_1 (
    .\字节地址 (AluResult[11:0]), .Din(MDin), .DataOut(mips_ram_1_dataout), .CLK(CLK), .WE(MemWrite),
    .Mode(multiplexer_11_out));
  Multiplexer #(.select(1), .width(2), .disabled("Z"), .enable("false")) multiplexer_11 (
    .in0(2'b00), .in1(2'b01), .out(multiplexer_11_out), .sel(Byte));
  Counter #(.width(16), .max('hffff), .ongoal("wrap"), .trigger("rising"), .behavior("new")) counter_1 (
    .count(not_5_out), .Q(\总周期数 ), .clk(CLK));  // open: load, D, carry, clr, preset, down
  D_Flip_Flop #(.trigger("high"), .Pre_Clr_Positions("LEGACY"), .NegatePresetClear("false"), .enable("true"), .NewFFLayout("false")) d_ff_4 (.Q(d_ff_4_q));  // open: clk, D, Qn, preset, en, reset
  // Probe on 13'hc
  Multiplexer #(.select(1), .width(32), .disabled("Z"), .enable("false")) multiplexer_12 (
    .in0(AluResult), .in1(mips_ram_1_dataout), .out(multiplexer_12_out), .sel(MemToReg));
  Comparator #(.width(13), .mode("twosComplement")) comparator_7 (
    .a(CNT_num), .b(13'hc), .eq(comparator_7_eq), .lt(comparator_7_lt));  // open: gt
  Clock #(.highDuration(1), .lowDuration(1)) clock_4 (.out(clock_4_out));
  D_Flip_Flop #(.trigger("falling"), .Pre_Clr_Positions("ABOVE_BELOW"), .NegatePresetClear("false"), .enable("true"), .NewFFLayout("true")) d_ff_5 (
    .clk(CLK), .D(nand_1_out), .Q(halt), .en(Ecall), .reset(Go));  // open: Qn, preset
  Multiplexer #(.select(1), .width(32), .disabled("Z"), .enable("false")) multiplexer_13 (
    .in0(multiplexer_12_out), .in1(bit_extender_5_out), .out(multiplexer_13_out), .sel(or_14_out));
  assign bit_extender_5_out = {{31{1'b0}}, Less};  // Bit_Extender bit_extender_5
  assign bit_extender_6_out = {{12{IR[31]}}, IR[31:12]};  // Bit_Extender bit_extender_6
  Counter #(.width(13), .max('h1fff), .ongoal("stay"), .trigger("rising"), .behavior("old")) counter_2 (
    .count(comparator_7_lt), .Q(CNT_num), .clk(clock_4_out));  // open: load, D, carry, clr, preset
  Comparator #(.width(4), .mode("unsigned")) comparator_8 (
    .a(AluOP), .b(4'b1100), .eq(comparator_8_eq));  // open: gt, lt
  Comparator #(.width(4), .mode("unsigned")) comparator_9 (
    .a(AluOP), .b(4'b1011), .eq(comparator_9_eq));  // open: gt, lt
  Multiplexer #(.select(1), .width(32), .disabled("Z"), .enable("false")) multiplexer_14 (
    .in0(multiplexer_13_out), .in1(PC_4), .out(multiplexer_14_out), .sel(or_13_out));
  or or_13 (or_13_out, JAL, JALR);
  Shifter #(.width(32), .shift("ll")) shifter_3 (.in(bit_extender_6_out), .\dist (5'b01100), .out(shifter_3_out));
  Adder #(.width(32)) adder_4 (.a(shifter_3_out), .b(PC), .out(adder_4_out));  // open: cin, cout
  nand nand_2 (nand_2_out, d_ff_4_q, comparator_7_eq);
  or or_14 (or_14_out, comparator_8_eq, comparator_9_eq);
  Multiplexer #(.select(1), .width(32), .disabled("Z"), .enable("false")) multiplexer_15 (
    .in0(multiplexer_14_out), .in1(adder_4_out), .out(RDin), .sel(Auipc));
  assign CLK = nand_2_out ? clock_4_out : 1'bz;  // Controlled_Buffer controlled_buffer_1
  Pull_Resistor #(.pull(1)) pull_resistor_4 (.node(CLK));

  // Other names for the same wires on the sheet: UImm[19:0] = IR[31:12]; R2[31:0] = MDin

  // Notes on the sheet:
  //   中断源
  //   中断等待指示
  //   总复位信号应将除ROM以外所有存储组件全部清零
  //   单级中断测试信号模拟器
  //   数码管输出
  //   数码管输出应该用寄存器锁存，否则显示数据只能一闪而过
  //   Reset 
  //   Reset 
  //   Reset 
  //   指令存储器
  //   指令探针
  //   contents of rom_1 (hex, n*v repeats v):
  //   7d000113 100413 1f41993 41f9d993 433 c00913 800b13 140413 f47413 800293 100313 499993 89e9b3 1300533
  //   2200893 73 406282b3 fe0294e3 140413 f00f93 1f47433 1c41413 800293 100313 49d993 89e9b3 1300533
  //   2200893 73 406282b3 fe0294e3 1c45413 406b0b33 b0463 f95ff06f 2b3 fff2c293 1029293 fff2e293 500533
  //   2200893 73 f5dff06f 1112023 410113 a12023 410113 812023 410113 1312023 410113 1412023 410113 1512023
  //   410113 1612023 410113 100b13 300a13 100a93 1600433 441413 14469b3 1300533 2200893 73 fe0416e3
  //   415a0a33 fe0a10e3 ffc10113 12b03 ffc10113 12a83 ffc10113 12a03 ffc10113 12983 ffc10113 12403
  //   ffc10113 12503 ffc10113 12883 200073 1112023 410113 a12023 410113 812023 410113 1312023 410113
  //   1412023 410113 1512023 410113 1612023 410113 200b13 300a13 100a93 1600433 441413 14469b3 1300533
  //   2200893 73 fe0416e3 415a0a33 fe0a10e3 ffc10113 12b03 ffc10113 12a83 ffc10113 12a03 ffc10113 12983
  //   ffc10113 12403 ffc10113 12503 ffc10113 12883 200073 1112023 410113 a12023 410113 812023 410113
  //   1312023 410113 1412023 410113 1512023 410113 1612023 410113 300b13 300a13 100a93 1600433 441413
  //   14469b3 1300533 2200893 73 fe0416e3 415a0a33 fe0a10e3 ffc10113 12b03 ffc10113 12a83 ffc10113 12a03
  //   ffc10113 12983 ffc10113 12403 ffc10113 12503 ffc10113 12883 200073
  //   JAL
  //   JALR
  //   URET
  //   指令字
  //   Beq
  //   Bne
  //   MemToReg
  //   MemWrite
  //   AluOP
  //   AluSrcB
  //   RegWrite
  //   为方便自动评测，需要输出PC，IR，寄存器堆写如数据RDin
  //   RAM写使能MemWrite、RAM写入数据MDin等信号
  //   数据存储器
  //   控制位
  //   暂停节拍，不能为0
  //   戳工具置1进入计数暂停模式，ctrl+k时钟自动运行到对应节拍暂停
  //   ctrl+k关闭时钟连续运行，将控制位置零，进入单步调试模式调试
  //   可计数暂停的时钟源
endmodule

module \单周期_多级中断  (
  input  IR1,
  input  IR2,
  input  IR3,
  output RegWrite,
  output MemWrite,
  output [31:0] PC,
  output [31:0] IR,
  output [31:0] RDin,
  output [31:0] MDin,
  output [31:0] LedData
);

  wire alu_1_equal, and_1_out, and_2_out, and_3_out, and_4_out, and_6_out, and_7_out, and_8_out, Auipc, BGE,
       Byte, CanBe, CLK, clock_1_out, clock_2_out, clock_3_out, clock_4_out, comparator_1_eq,
       comparator_2_eq, comparator_3_eq, comparator_4_eq, comparator_5_eq, comparator_6_gt, comparator_7_eq,
       comparator_8_eq, comparator_9_eq, comparator_9_lt, comparator_10_eq, comparator_11_eq, CSRRCI, CSRRSI,
       d_ff_1_q, d_ff_2_q, d_ff_3_q, d_ff_4_q, demultiplexer_2_out1, demultiplexer_2_out2,
       demultiplexer_2_out3, demultiplexer_3_out1, demultiplexer_3_out2, demultiplexer_3_out3, Ecall, Geq,
       Go, halt, IE, IR1_q, IR1_t, IR2_q, IR2_t, IR3_q, IR3_t, IRA, IRB, IRC, JAL, JALR, Less, MemToReg,
       nand_1_out, nand_2_out, not_1_out, not_2_out, not_3_out, not_4_out, not_5_out, or_1_out, or_2_out,
       or_3_out, or_4_out, or_5_out, or_6_out, or_7_out, or_8_out, or_12_out, or_14_out, or_15_out,
       or_16_out, or_17_out, priority_encoder_1_gs, ResetIR1, ResetIR2, ResetIR3, riscv_probe_1_p1, RST,
       S_type, UERT, W1, W2, W3, \单周期硬布线控制器_1_alu_src , \单周期硬布线控制器_1_beq , \单周期硬布线控制器_1_bne ;
  wire [1:0] Cur_IR_Id, EIR_Id, IR_Id, Last_IR_1_q, Last_IR_2_q, Last_IR_3_q, Last_IR_Id, multiplexer_12_out,
       multiplexer_15_out, priority_encoder_1_out;
  wire [3:0] AluOP;
  wire [4:0] multiplexer_1_out, multiplexer_2_out;
  wire [12:0] CNT_num;
  wire [15:0] \总周期数 ;
  wire [31:0] adder_2_out, adder_3_out, adder_4_out, AluResult, and_5_out, bit_extender_1_out,
       bit_extender_2_out, bit_extender_3_out, bit_extender_4_out, bit_extender_5_out, bit_extender_6_out,
       EPC, EPC1_q, EPC2_q, EPC3_q, mips_ram_1_dataout, multiplexer_3_out, multiplexer_5_out,
       multiplexer_6_out, multiplexer_7_out, multiplexer_8_out, multiplexer_9_out, multiplexer_16_out,
       multiplexer_17_out, multiplexer_18_out, NextPC, NextPCWithoutInt, PC_4, regifile_1_r1, shifter_1_out,
       shifter_2_out, shifter_3_out;

  Button \u_继续运行  (.out(Go));
  Button _1 (.out(IR1_t));
  Button _2 (.out(IR2_t));
  Button _3 (.out(IR3_t));
  LED #(.active("true")) led_1 (.in(W1));
  LED #(.active("true")) led_2 (.in(W2));
  LED #(.active("true")) led_3 (.in(W3));
  Hex_Digit_Display hex_digit_display_1 (.value(LedData[31:28]));  // open: dp
  Comparator #(.width(16), .mode("twosComplement")) comparator_1 (
    .a(16'h258), .b(\总周期数 ), .eq(comparator_1_eq));  // open: gt, lt
  Comparator #(.width(16), .mode("twosComplement")) comparator_2 (
    .a(\总周期数 ), .b(16'h1), .eq(comparator_2_eq));  // open: gt, lt
  Comparator #(.width(16), .mode("twosComplement")) comparator_3 (
    .a(\总周期数 ), .b(16'h4), .eq(comparator_3_eq));  // open: gt, lt
  Comparator #(.width(16), .mode("twosComplement")) comparator_4 (
    .a(\总周期数 ), .b(16'h7), .eq(comparator_4_eq));  // open: gt, lt
  or or_1 (or_1_out, comparator_4_eq, comparator_5_eq);
  Comparator #(.width(16), .mode("twosComplement")) comparator_5 (
    .a(\总周期数 ), .b(16'h241), .eq(comparator_5_eq));  // open: gt, lt
  Clock #(.highDuration(1), .lowDuration(1)) clock_1 (.out(clock_1_out));
  or or_2 (or_2_out, IR1_q, d_ff_1_q);
  LED #(.active("true")) \_1号中断等待指示灯  (.in(or_2_out));
  Clock #(.highDuration(1), .lowDuration(1)) clock_2 (.out(clock_2_out));
  or or_3 (or_3_out, IR2_q, d_ff_2_q);
  LED #(.active("true")) \_2号中断等待指示灯  (.in(or_3_out));
  Clock #(.highDuration(1), .lowDuration(1)) clock_3 (.out(clock_3_out));
  LED #(.active("true")) \_3号中断等待指示灯  (.in(or_4_out));
  or or_4 (or_4_out, IR3_q, d_ff_3_q);
  Hex_Digit_Display hex_digit_display_2 (.value(LedData[27:24]));  // open: dp
  Hex_Digit_Display hex_digit_display_3 (.value(LedData[23:20]));  // open: dp
  or or_5 (or_5_out, comparator_1_eq, comparator_2_eq);
  Pull_Resistor #(.pull(0)) pull_resistor_1 (.node(IRA));
  assign IRA = or_5_out ? ~CLK : 1'bz;  // Controlled_Inverter controlled_inverter_1
  Pull_Resistor #(.pull(0)) pull_resistor_2 (.node(IRB));
  assign IRB = comparator_3_eq ? ~CLK : 1'bz;  // Controlled_Inverter controlled_inverter_2
  Pull_Resistor #(.pull(0)) pull_resistor_3 (.node(IRC));
  assign IRC = or_1_out ? ~CLK : 1'bz;  // Controlled_Inverter controlled_inverter_3
  D_Flip_Flop #(.trigger("rising"), .Pre_Clr_Positions("LEGACY"), .NegatePresetClear("false"), .enable("true"), .NewFFLayout("false")) d_ff_1 (
    .clk(IR1_t), .D(1'b1), .Q(d_ff_1_q), .reset(IR1_q));  // open: Qn, preset, en
  D_Flip_Flop #(.trigger("rising"), .Pre_Clr_Positions("LEGACY"), .NegatePresetClear("false"), .enable("true"), .NewFFLayout("false")) d_ff_2 (
    .clk(IR2_t), .D(1'b1), .Q(d_ff_2_q), .reset(IR2_q));  // open: Qn, preset, en
  D_Flip_Flop #(.trigger("rising"), .Pre_Clr_Positions("LEGACY"), .NegatePresetClear("false"), .enable("true"), .NewFFLayout("false")) d_ff_3 (
    .clk(IR3_t), .D(1'b1), .Q(d_ff_3_q), .reset(IR3_q));  // open: Qn, preset, en
  Hex_Digit_Display hex_digit_display_4 (.value(LedData[19:16]));  // open: dp
  Hex_Digit_Display hex_digit_display_5 (.value(LedData[15:12]));  // open: dp
  not not_1 (not_1_out, halt);
  or or_6 (or_6_out, d_ff_1_q, IR1_q);
  or or_7 (or_7_out, d_ff_2_q, IR2_q);
  or or_8 (or_8_out, d_ff_3_q, IR3_q);
  Hex_Digit_Display hex_digit_display_6 (.value(LedData[7:4]));  // open: dp
  Hex_Digit_Display hex_digit_display_7 (.value(LedData[11:8]));  // open: dp
  // Probe on \总周期数 
  Register #(.width(32), .trigger("rising"), .Select("low")) u_PC (
    .D(NextPC), .en(not_1_out), .Q(PC), .clk(CLK), .clr(riscv_probe_1_p1));
  and and_1 (and_1_out, or_6_out, ~ResetIR1);  // AND_Gate
  and and_2 (and_2_out, or_7_out, ~ResetIR2);  // AND_Gate
  and and_3 (and_3_out, or_8_out, ~ResetIR3);  // AND_Gate
  Hex_Digit_Display hex_digit_display_8 (.value(LedData[3:0]));  // open: dp
  Adder #(.width(32)) adder_1 (.a(PC), .b(32'h4), .out(PC_4));  // open: cin, cout
  D_Flip_Flop #(.trigger("rising"), .Pre_Clr_Positions("LEGACY"), .NegatePresetClear("false"), .enable("true"), .NewFFLayout("false")) u_IR1 (
    .clk(clock_1_out), .D(and_1_out), .Q(IR1_q));  // open: Qn, preset, en, reset
  D_Flip_Flop #(.trigger("rising"), .Pre_Clr_Positions("LEGACY"), .NegatePresetClear("false"), .enable("true"), .NewFFLayout("false")) u_IR2 (
    .clk(clock_2_out), .D(and_2_out), .Q(IR2_q));  // open: Qn, preset, en, reset
  D_Flip_Flop #(.trigger("rising"), .Pre_Clr_Positions("LEGACY"), .NegatePresetClear("false"), .enable("true"), .NewFFLayout("false")) u_IR3 (
    .clk(clock_3_out), .D(and_3_out), .Q(IR3_q));  // open: Qn, preset, en, reset
  // RiscV_Probe riscv_probe_1: pin names not known; wires that end beside it: riscv_probe_1_p1, RST, IR, IR1_t, IR2_t
  ROM #(.addrWidth(10), .dataWidth(32), .Select("high")) rom_1 (.addr(PC[11:2]), .data(IR));
  // OR_Gate or_9 has open pins: in0=IR1, in1=IRA, out=open
  Demultiplexer #(.select(2), .width(1), .tristate("false"), .disabled("Z"), .enable("false")) demultiplexer_1 (
    .out1(ResetIR1), .out2(ResetIR2), .out3(ResetIR3), .in(UERT), .sel(Cur_IR_Id));  // open: out0
  // OR_Gate or_10 has open pins: in0=IR2, in1=IRB, out=open
  \单周期硬布线控制器  \u_单周期硬布线控制器_1  (
    .Funct({IR[30], IR[25], IR[14:12]}), .OP(IR[6:2]), .ALU_OP(AluOP), .MemToReg(MemToReg),
    .MemWrite(MemWrite), .ALU_SRC(\单周期硬布线控制器_1_alu_src ), .RegWrite(RegWrite), .ecall(Ecall),
    .S_type(S_type), .Jalr(JALR), .Beq(\单周期硬布线控制器_1_beq ), .JAL(JAL), .Bne(\单周期硬布线控制器_1_bne ), .in_3(IR[21]),
    .uret(UERT), .Auipc(Auipc), .Byte(Byte), .BGE(BGE), .CSRRSI(CSRRSI), .CSRRCI(CSRRCI));  // open: RsUsed, RtUsed
  Multiplexer #(.select(1), .width(5), .disabled("Z"), .enable("false")) multiplexer_1 (
    .in0(IR[19:15]), .in1(5'b10001), .out(multiplexer_1_out), .sel(Ecall));
  Multiplexer #(.select(1), .width(5), .disabled("Z"), .enable("false")) multiplexer_2 (
    .in0(IR[24:20]), .in1(5'b01010), .out(multiplexer_2_out), .sel(Ecall));
  assign bit_extender_1_out = {{20{IR[31]}}, IR[31:20]};  // Bit_Extender bit_extender_1
  assign bit_extender_2_out = {{20{IR[31]}}, {IR[31:25], IR[11:7]}};  // Bit_Extender bit_extender_2
  // Probe on multiplexer_1_out
  // Probe on multiplexer_2_out
  Multiplexer #(.select(1), .width(32), .disabled("Z"), .enable("false")) multiplexer_3 (
    .in0(bit_extender_1_out), .in1(bit_extender_2_out), .out(multiplexer_3_out), .sel(S_type));
  assign bit_extender_3_out = {{20{IR[31]}}, {IR[31], IR[7], IR[30:25], IR[11:8]}};  // Bit_Extender bit_extender_3
  assign bit_extender_4_out = {{12{IR[31]}}, {IR[31], IR[19:12], IR[20], IR[30:21]}};  // Bit_Extender bit_extender_4
  Multiplexer #(.select(1), .width(2), .disabled("Z"), .enable("false")) multiplexer_4 (
    .in0(2'b00), .in1(priority_encoder_1_out), .out(IR_Id), .sel(priority_encoder_1_gs));
  Priority_Encoder #(.select(2), .disabled("Z")) priority_encoder_1 (
    .in0(1'b0), .in1(IR1_q), .in2(IR2_q), .in3(IR3_q), .out(priority_encoder_1_out),
    .gs(priority_encoder_1_gs));  // open: en_out, en_in
  Comparator #(.width(2), .mode("unsigned")) comparator_6 (
    .a(IR_Id), .b(Cur_IR_Id), .gt(comparator_6_gt));  // open: eq, lt
  // OR_Gate or_11 has open pins: in0=IR3, in1=IRC, out=open
  Shifter #(.width(32), .shift("ll")) shifter_1 (.in(bit_extender_3_out), .\dist (5'b00001), .out(shifter_1_out));
  Shifter #(.width(32), .shift("ll")) shifter_2 (.in(bit_extender_4_out), .\dist (5'b00001), .out(shifter_2_out));
  Multiplexer #(.select(2), .width(32), .disabled("Z"), .enable("false")) multiplexer_5 (
    .in0(NextPCWithoutInt), .in1(32'h30ac), .in2(32'h3158), .in3(32'h3204), .out(multiplexer_5_out),
    .sel(IR_Id));
  and and_4 (and_4_out, priority_encoder_1_gs, IE, comparator_6_gt);
  not not_2 (not_2_out, and_4_out);
  Demultiplexer #(.select(2), .width(1), .tristate("false"), .disabled("Z"), .enable("false")) demultiplexer_2 (
    .out1(demultiplexer_2_out1), .out2(demultiplexer_2_out2), .out3(demultiplexer_2_out3), .in(and_4_out),
    .sel(IR_Id));  // open: out0
  Demultiplexer #(.select(2), .width(1), .tristate("false"), .disabled("Z"), .enable("false")) demultiplexer_3 (
    .out1(demultiplexer_3_out1), .out2(demultiplexer_3_out2), .out3(demultiplexer_3_out3), .in(and_4_out),
    .sel(IR_Id));  // open: out0
  Regifile regifile_1 (
    .Din(RDin), .Clk(CLK), .R1(regifile_1_r1), .R2(MDin), .WE(RegWrite), .W_num(IR[11:7]),
    .R1_num(multiplexer_1_out), .R2_num(multiplexer_2_out));
  Adder #(.width(32)) adder_2 (.a(shifter_1_out), .b(PC), .out(adder_2_out));  // open: cin, cout
  Adder #(.width(32)) adder_3 (.a(PC), .b(shifter_2_out), .out(adder_3_out));  // open: cin, cout
  Multiplexer #(.select(1), .width(32), .disabled("Z"), .enable("false")) multiplexer_6 (
    .in0(multiplexer_9_out), .in1(adder_2_out), .out(multiplexer_6_out), .sel(CanBe));
  Multiplexer #(.select(1), .width(32), .disabled("Z"), .enable("false")) multiplexer_7 (
    .in0(NextPCWithoutInt), .in1(multiplexer_5_out), .out(multiplexer_7_out), .sel(and_4_out));
  or or_12 (or_12_out, UERT, and_4_out);
  Multiplexer #(.select(1), .width(32), .disabled("Z"), .enable("false")) multiplexer_8 (
    .in0(MDin), .in1(multiplexer_3_out), .out(multiplexer_8_out), .sel(\单周期硬布线控制器_1_alu_src ));
  Multiplexer #(.select(1), .width(32), .disabled("Z"), .enable("false")) multiplexer_9 (
    .in0(PC_4), .in1(and_5_out), .out(multiplexer_9_out), .sel(JALR));
  Multiplexer #(.select(1), .width(32), .disabled("Z"), .enable("false")) multiplexer_10 (
    .in0(multiplexer_6_out), .in1(adder_3_out), .out(NextPCWithoutInt), .sel(JAL));
  Multiplexer #(.select(1), .width(32), .disabled("Z"), .enable("false")) multiplexer_11 (
    .in0(multiplexer_7_out), .in1(EPC), .out(NextPC), .sel(UERT));
  Comparator #(.width(16), .mode("twosComplement")) comparator_7 (
    .a(\总周期数 ), .b({16{1'b0}}), .eq(comparator_7_eq));  // open: gt, lt
  Register #(.width(32), .trigger("rising"), .Select("low")) EPC1 (
    .D(NextPCWithoutInt), .en(demultiplexer_2_out1), .Q(EPC1_q), .clk(CLK));  // open: clr
  Register #(.width(32), .trigger("rising"), .Select("low")) EPC2 (
    .D(NextPCWithoutInt), .en(demultiplexer_2_out2), .Q(EPC2_q), .clk(CLK));  // open: clr
  Register #(.width(32), .trigger("rising"), .Select("low")) EPC3 (
    .D(NextPCWithoutInt), .en(demultiplexer_2_out3), .Q(EPC3_q), .clk(CLK));  // open: clr
  Register #(.width(2), .trigger("rising"), .Select("low")) Last_IR_1 (
    .D(Last_IR_Id), .en(demultiplexer_3_out1), .Q(Last_IR_1_q), .clk(CLK));  // open: clr
  Register #(.width(2), .trigger("rising"), .Select("low")) Last_IR_2 (
    .D(Last_IR_Id), .en(demultiplexer_3_out2), .Q(Last_IR_2_q), .clk(CLK));  // open: clr
  Register #(.width(2), .trigger("rising"), .Select("low")) Last_IR_3 (
    .D(Last_IR_Id), .en(demultiplexer_3_out3), .Q(Last_IR_3_q), .clk(CLK));  // open: clr
  Multiplexer #(.select(1), .width(2), .disabled("Z"), .enable("false")) multiplexer_12 (
    .in0(IR_Id), .in1(EIR_Id), .out(multiplexer_12_out), .sel(UERT));
  Register #(.width(2), .trigger("rising"), .Select("low")) u_Cur_IR_Id (
    .D(multiplexer_12_out), .en(or_12_out), .Q(Cur_IR_Id), .clk(CLK));  // open: clr
  not not_3 (not_3_out, alu_1_equal);
  Comparator #(.width(32), .mode("twosComplement")) comparator_8 (
    .a(regifile_1_r1), .b(32'h22), .eq(comparator_8_eq));  // open: gt, lt
  ALU alu_1 (
    .X(regifile_1_r1), .Y(multiplexer_8_out), .AluOP(AluOP), .Equal(alu_1_equal), .Result(AluResult),
    .out_4(Geq), .out_6(Less));  // open: Result_2
  assign and_5_out = 32'hfffe & AluResult;  // AND_Gate and_5, 32 bits wide
  Register #(.width(2), .trigger("falling"), .Select("low")) u_Last_IR_Id (
    .D(Cur_IR_Id), .en(and_4_out), .Q(Last_IR_Id), .clk(CLK));  // open: clr
  and and_6 (and_6_out, \单周期硬布线控制器_1_beq , alu_1_equal);
  or or_13 (CanBe, and_6_out, and_7_out, and_8_out);
  and and_7 (and_7_out, \单周期硬布线控制器_1_bne , not_3_out);
  and and_8 (and_8_out, BGE, Geq);
  nand nand_1 (nand_1_out, comparator_8_eq, Ecall);
  or or_14 (or_14_out, CSRRSI, not_2_out);
  or or_15 (or_15_out, UERT, and_4_out, comparator_7_eq, CSRRSI, CSRRCI);
  Multiplexer #(.select(2), .width(32), .disabled("Z"), .enable("false")) multiplexer_13 (
    .in1(EPC1_q), .in2(EPC2_q), .in3(EPC3_q), .out(EPC), .sel(Cur_IR_Id));  // open: in0
  Multiplexer #(.select(2), .width(2), .disabled("Z"), .enable("false")) multiplexer_14 (
    .in1(Last_IR_1_q), .in2(Last_IR_2_q), .in3(Last_IR_3_q), .out(EIR_Id), .sel(Cur_IR_Id));  // open: in0
  Register #(.width(32), .trigger("rising"), .Select("low")) register_1 (
    .D(MDin), .en(not_4_out), .Q(LedData), .clk(CLK));  // open: clr
  not not_4 (not_4_out, nand_1_out);
  not not_5 (not_5_out, halt);
  Register #(.width(1), .trigger("rising"), .Select("low")) u_IE (
    .D(or_14_out), .en(or_15_out), .Q(IE), .clk(CLK));  // open: clr
  MIPS_RAM mips_ram_1 (
    .\字节地址 (AluResult[11:0]), .Din(MDin), .DataOut(mips_ram_1_dataout), .CLK(CLK), .WE(MemWrite),
    .Mode(multiplexer_15_out));
  Multiplexer #(.select(1), .width(2), .disabled("Z"), .enable("false")) multiplexer_15 (
    .in0(2'b00), .in1(2'b01), .out(multiplexer_15_out), .sel(Byte));
  Counter #(.width(16), .max('hffff), .ongoal("wrap"), .trigger("rising"), .behavior("new")) counter_1 (
    .count(not_5_out), .Q(\总周期数 ), .clk(CLK));  // open: load, D, carry, clr, preset, down
  D_Flip_Flop #(.trigger("high"), .Pre_Clr_Positions("LEGACY"), .NegatePresetClear("false"), .enable("true"), .NewFFLayout("false")) d_ff_4 (.Q(d_ff_4_q));  // open: clk, D, Qn, preset, en, reset
  // Probe on 13'h23b
  Multiplexer #(.select(1), .width(32), .disabled("Z"), .enable("false")) multiplexer_16 (
    .in0(AluResult), .in1(mips_ram_1_dataout), .out(multiplexer_16_out), .sel(MemToReg));
  Comparator #(.width(13), .mode("twosComplement")) comparator_9 (
    .a(CNT_num), .b(13'h23b), .eq(comparator_9_eq), .lt(comparator_9_lt));  // open: gt
  Clock #(.highDuration(1), .lowDuration(1)) clock_4 (.out(clock_4_out));
  D_Flip_Flop #(.trigger("falling"), .Pre_Clr_Positions("ABOVE_BELOW"), .NegatePresetClear("false"), .enable("true"), .NewFFLayout("true")) d_ff_5 (
    .clk(CLK), .D(nand_1_out), .Q(halt), .en(Ecall), .reset(Go));  // open: Qn, preset
  Multiplexer #(.select(1), .width(32), .disabled("Z"), .enable("false")) multiplexer_17 (
    .in0(multiplexer_16_out), .in1(bit_extender_5_out), .out(multiplexer_17_out), .sel(or_17_out));
  assign bit_extender_5_out = {{31{1'b0}}, Less};  // Bit_Extender bit_extender_5
  assign bit_extender_6_out = {{12{IR[31]}}, IR[31:12]};  // Bit_Extender bit_extender_6
  Counter #(.width(13), .max('h1fff), .ongoal("stay"), .trigger("rising"), .behavior("old")) counter_2 (
    .count(comparator_9_lt), .Q(CNT_num), .clk(clock_4_out));  // open: load, D, carry, clr, preset
  Comparator #(.width(4), .mode("unsigned")) comparator_10 (
    .a(AluOP), .b(4'b1100), .eq(comparator_10_eq));  // open: gt, lt
  Comparator #(.width(4), .mode("unsigned")) comparator_11 (
    .a(AluOP), .b(4'b1011), .eq(comparator_11_eq));  // open: gt, lt
  Multiplexer #(.select(1), .width(32), .disabled("Z"), .enable("false")) multiplexer_18 (
    .in0(multiplexer_17_out), .in1(PC_4), .out(multiplexer_18_out), .sel(or_16_out));
  or or_16 (or_16_out, JAL, JALR);
  Shifter #(.width(32), .shift("ll")) shifter_3 (.in(bit_extender_6_out), .\dist (5'b01100), .out(shifter_3_out));
  Adder #(.width(32)) adder_4 (.a(shifter_3_out), .b(PC), .out(adder_4_out));  // open: cin, cout
  nand nand_2 (nand_2_out, d_ff_4_q, comparator_9_eq);
  or or_17 (or_17_out, comparator_10_eq, comparator_11_eq);
  Multiplexer #(.select(1), .width(32), .disabled("Z"), .enable("false")) multiplexer_19 (
    .in0(multiplexer_18_out), .in1(adder_4_out), .out(RDin), .sel(Auipc));
  assign CLK = nand_2_out ? clock_4_out : 1'bz;  // Controlled_Buffer controlled_buffer_1
  Pull_Resistor #(.pull(1)) pull_resistor_4 (.node(CLK));

  // Other names for the same wires on the sheet: UImm[19:0] = IR[31:12]; R2[31:0] = MDin

  // Notes on the sheet:
  //   中断源
  //   中断等待指示
  //   总复位信号应将除ROM以外所有存储组件全部清零
  //   多级中断测试信号模拟器
  //   数码管输出
  //   数码管输出应该用寄存器锁存，否则显示数据只能一闪而过
  //   Reset 
  //   Reset 
  //   Reset 
  //   指令存储器
  //   指令探针
  //   contents of rom_1 (hex, n*v repeats v):
  //   7d000113 100413 1f41993 41f9d993 433 c00913 800b13 140413 f47413 800293 100313 499993 89e9b3 1300533
  //   2200893 73 406282b3 fe0294e3 140413 f00f93 1f47433 1c41413 800293 100313 49d993 89e9b3 1300533
  //   2200893 73 406282b3 fe0294e3 1c45413 406b0b33 b0463 f95ff06f 2b3 fff2c293 1029293 fff2e293 500533
  //   2200893 73 f5dff06f 1112023 410113 a12023 410113 812023 410113 1312023 410113 1412023 410113 1512023
  //   410113 1612023 410113 40e073 100b13 300a13 100a93 1600433 441413 14469b3 1300533 2200893 73 fe0416e3
  //   415a0a33 fe0a10e3 40f073 ffc10113 12b03 ffc10113 12a83 ffc10113 12a03 ffc10113 12983 ffc10113 12403
  //   ffc10113 12503 ffc10113 12883 200073 1112023 410113 a12023 410113 812023 410113 1312023 410113
  //   1412023 410113 1512023 410113 1612023 410113 40e073 200b13 300a13 100a93 1600433 441413 14469b3
  //   1300533 2200893 73 fe0416e3 415a0a33 fe0a10e3 40f073 ffc10113 12b03 ffc10113 12a83 ffc10113 12a03
  //   ffc10113 12983 ffc10113 12403 ffc10113 12503 ffc10113 12883 200073 1112023 410113 a12023 410113
  //   812023 410113 1312023 410113 1412023 410113 1512023 410113 1612023 410113 40e073 300b13 300a13
  //   100a93 1600433 441413 14469b3 1300533 2200893 73 fe0416e3 415a0a33 fe0a10e3 40f073 ffc10113 12b03
  //   ffc10113 12a83 ffc10113 12a03 ffc10113 12983 ffc10113 12403 ffc10113 12503 ffc10113 12883 200073
  //   JAL
  //   JALR
  //   URET
  //   指令字
  //   Beq
  //   Bne
  //   MemToReg
  //   MemWrite
  //   AluOP
  //   AluSrcB
  //   RegWrite
  //   为方便自动评测，需要输出PC，IR，寄存器堆写如数据RDin
  //   RAM写使能MemWrite、RAM写入数据MDin等信号
  //   数据存储器
  //   控制位
  //   暂停节拍，不能为0
  //   戳工具置1进入计数暂停模式，ctrl+k时钟自动运行到对应节拍暂停
  //   ctrl+k关闭时钟连续运行，将控制位置零，进入单步调试模式调试
  //   可计数暂停的时钟源
endmodule

module \封装正确性测试  (
);

  wire IR1, IR2, IR3, MemW, RegW;
  wire [31:0] EX_PC, ID_PC, IF_PC, IR, LED, MDin, MDinr, MEM_PC, PC, RDin, RDinr, WB_PC;

  \单周期RISC_V  \u_单周期risc_v_1  (
    .IR1(IR1), .IR2(IR2), .IR3(IR3), .RegWrite(RegW), .MemWrite(MemW), .PC(PC), .IR(IR), .RDin(RDin),
    .MDin(MDin), .LedData(LED));
  \气泡流水线  \u_气泡流水线_1  (
    .RegWrite(RegW), .MemWrite(MemW), .IF_PC(IF_PC), .ID_PC(ID_PC), .EX_PC(EX_PC), .M_PC(MEM_PC),
    .WB_PC(WB_PC), .RDin(RDinr), .MDin(MDinr), .LedData(LED));
  \单周期_单级中断  \u_单周期_单级中断_1  (
    .IR1(IR1), .IR2(IR2), .IR3(IR3), .RegWrite(RegW), .MemWrite(MemW), .PC(PC), .IR(IR), .RDin(RDin),
    .MDin(MDin), .LedData(LED));
  \理想流水线  \u_理想流水线_1  (
    .RegWrite(RegW), .MemWrite(MemW), .IF_PC(IF_PC), .ID_PC(ID_PC), .EX_PC(EX_PC), .M_PC(MEM_PC),
    .WB_PC(WB_PC), .RDin(RDinr), .MDin(MDinr), .LedData(LED));
  \重定向流水线  \u_重定向流水线_1  (
    .RegWrite(RegW), .MemWrite(MemW), .IF_PC(IF_PC), .ID_PC(ID_PC), .EX_PC(EX_PC), .M_PC(MEM_PC),
    .WB_PC(WB_PC), .RDin(RDinr), .MDin(MDinr), .LedData(LED));
  \单周期_多级中断  \u_单周期_多级中断_1  (
    .IR1(IR1), .IR2(IR2), .IR3(IR3), .RegWrite(RegW), .MemWrite(MemW), .PC(PC), .IR(IR), .RDin(RDin),
    .MDin(MDin), .LedData(LED));

  // Notes on the sheet:
  //   单周期封装测试
  //   气泡流水封装测试
  //   单周期+单级中断封装测试
  //   请检查上面封装有无位宽不匹配，引脚标签是否和连接的标签相对应，否则无法在educoder平台上正确测试
  //   理想流水封装测试
  //   重定向流水封装测试
  //   单周期+多级中断封装测试
endmodule

module IF_ID (
  input  PredictJump,
  input  [31:0] IR,
  input  [31:0] PC,
  input  En,
  input  Flush,
  input  CLK,
  output PredictJump_2,
  output [31:0] IR_2,
  output [31:0] PC_2
);

  wire multiplexer_1_out, or_1_out;
  wire [31:0] multiplexer_2_out, multiplexer_3_out;

  or or_1 (or_1_out, En, Flush);
  Multiplexer #(.select(1), .width(1), .disabled("Z"), .enable("false")) multiplexer_1 (
    .in0(PredictJump), .in1(1'b0), .out(multiplexer_1_out), .sel(Flush));
  Multiplexer #(.select(1), .width(32), .disabled("Z"), .enable("false")) multiplexer_2 (
    .in0(IR), .in1({32{1'b0}}), .out(multiplexer_2_out), .sel(Flush));
  Multiplexer #(.select(1), .width(32), .disabled("Z"), .enable("false")) multiplexer_3 (
    .in0(PC), .in1({32{1'b0}}), .out(multiplexer_3_out), .sel(Flush));
  Register #(.width(1), .trigger("rising"), .Select("low")) register_1 (
    .D(multiplexer_1_out), .en(or_1_out), .Q(PredictJump_2), .clk(CLK));  // open: clr
  Register #(.width(32), .trigger("rising"), .Select("low")) register_2 (
    .D(multiplexer_2_out), .en(or_1_out), .Q(IR_2), .clk(CLK));  // open: clr
  Register #(.width(32), .trigger("rising"), .Select("low")) register_3 (
    .D(multiplexer_3_out), .en(or_1_out), .Q(PC_2), .clk(CLK));  // open: clr
endmodule

module ID_EX (
  input  [1:0] RsFoward,
  input  [1:0] RtFoward,
  input  RegWrite,
  input  MemToReg,
  input  MemWrite,
  input  [3:0] AluOP,
  input  Bne,
  input  AluSrc,
  input  Beq,
  input  Bge,
  input  Auipc,
  input  Byte,
  input  Jal,
  input  Jalr,
  input  Ecall,
  input  Uert,
  input  PredictJump,
  input  [31:0] IR,
  input  [31:0] R1,
  input  [31:0] R2,
  input  [4:0] rd,
  input  [31:0] BImm,
  input  [31:0] JImm,
  input  [31:0] UImm,
  input  [31:0] Imm,
  input  [31:0] PC,
  input  Flush,
  input  En,
  input  CLK,
  output [1:0] RsFoward_2,
  output [1:0] RtFoward_2,
  output RegWrite_2,
  output MemToReg_2,
  output MemWrite_2,
  output [3:0] AluOP_2,
  output Bne_2,
  output AluSrc_2,
  output Beq_2,
  output Bge_2,
  output Auipc_2,
  output Byte_2,
  output Jal_2,
  output Jalr_2,
  output Ecall_2,
  output Uert_2,
  output PredictJump_2,
  output [31:0] IR_2,
  output [31:0] R1_2,
  output [31:0] R2_2,
  output [4:0] rd_2,
  output [31:0] BImm_2,
  output [31:0] JImm_2,
  output [31:0] UImm_2,
  output [31:0] Imm_2,
  output [31:0] PC_2
);

  wire multiplexer_3_out, multiplexer_4_out, multiplexer_5_out, multiplexer_7_out, multiplexer_8_out,
       multiplexer_9_out, multiplexer_10_out, multiplexer_11_out, multiplexer_12_out, multiplexer_13_out,
       multiplexer_14_out, multiplexer_15_out, multiplexer_16_out, multiplexer_17_out;
  wire [1:0] multiplexer_1_out, multiplexer_2_out;
  wire [3:0] multiplexer_6_out;
  wire [4:0] multiplexer_21_out;
  wire [31:0] multiplexer_18_out, multiplexer_19_out, multiplexer_20_out, multiplexer_22_out,
       multiplexer_23_out, multiplexer_24_out, multiplexer_25_out, multiplexer_26_out;

  Multiplexer #(.select(1), .width(2), .disabled("Z"), .enable("false")) multiplexer_1 (
    .in0(RsFoward), .in1(2'b00), .out(multiplexer_1_out), .sel(Flush));
  Multiplexer #(.select(1), .width(2), .disabled("Z"), .enable("false")) multiplexer_2 (
    .in0(RtFoward), .in1(2'b00), .out(multiplexer_2_out), .sel(Flush));
  Multiplexer #(.select(1), .width(1), .disabled("Z"), .enable("false")) multiplexer_3 (
    .in0(RegWrite), .in1(1'b0), .out(multiplexer_3_out), .sel(Flush));
  Multiplexer #(.select(1), .width(1), .disabled("Z"), .enable("false")) multiplexer_4 (
    .in0(MemToReg), .in1(1'b0), .out(multiplexer_4_out), .sel(Flush));
  Multiplexer #(.select(1), .width(1), .disabled("Z"), .enable("false")) multiplexer_5 (
    .in0(MemWrite), .in1(1'b0), .out(multiplexer_5_out), .sel(Flush));
  Multiplexer #(.select(1), .width(4), .disabled("Z"), .enable("false")) multiplexer_6 (
    .in0(AluOP), .in1(4'b0000), .out(multiplexer_6_out), .sel(Flush));
  Multiplexer #(.select(1), .width(1), .disabled("Z"), .enable("false")) multiplexer_7 (
    .in0(Bne), .in1(1'b0), .out(multiplexer_7_out), .sel(Flush));
  Multiplexer #(.select(1), .width(1), .disabled("Z"), .enable("false")) multiplexer_8 (
    .in0(AluSrc), .in1(1'b0), .out(multiplexer_8_out), .sel(Flush));
  Multiplexer #(.select(1), .width(1), .disabled("Z"), .enable("false")) multiplexer_9 (
    .in0(Beq), .in1(1'b0), .out(multiplexer_9_out), .sel(Flush));
  Multiplexer #(.select(1), .width(1), .disabled("Z"), .enable("false")) multiplexer_10 (
    .in0(Bge), .in1(1'b0), .out(multiplexer_10_out), .sel(Flush));
  Multiplexer #(.select(1), .width(1), .disabled("Z"), .enable("false")) multiplexer_11 (
    .in0(Auipc), .in1(1'b0), .out(multiplexer_11_out), .sel(Flush));
  Multiplexer #(.select(1), .width(1), .disabled("Z"), .enable("false")) multiplexer_12 (
    .in0(Byte), .in1(1'b0), .out(multiplexer_12_out), .sel(Flush));
  Multiplexer #(.select(1), .width(1), .disabled("Z"), .enable("false")) multiplexer_13 (
    .in0(Jal), .in1(1'b0), .out(multiplexer_13_out), .sel(Flush));
  Multiplexer #(.select(1), .width(1), .disabled("Z"), .enable("false")) multiplexer_14 (
    .in0(Jalr), .in1(1'b0), .out(multiplexer_14_out), .sel(Flush));
  Multiplexer #(.select(1), .width(1), .disabled("Z"), .enable("false")) multiplexer_15 (
    .in0(Ecall), .in1(1'b0), .out(multiplexer_15_out), .sel(Flush));
  Multiplexer #(.select(1), .width(1), .disabled("Z"), .enable("false")) multiplexer_16 (
    .in0(Uert), .in1(1'b0), .out(multiplexer_16_out), .sel(Flush));
  Multiplexer #(.select(1), .width(1), .disabled("Z"), .enable("false")) multiplexer_17 (
    .in0(PredictJump), .in1(1'b0), .out(multiplexer_17_out), .sel(Flush));
  Multiplexer #(.select(1), .width(32), .disabled("Z"), .enable("false")) multiplexer_18 (
    .in0(IR), .in1({32{1'b0}}), .out(multiplexer_18_out), .sel(Flush));
  Multiplexer #(.select(1), .width(32), .disabled("Z"), .enable("false")) multiplexer_19 (
    .in0(R1), .in1({32{1'b0}}), .out(multiplexer_19_out), .sel(Flush));
  Multiplexer #(.select(1), .width(32), .disabled("Z"), .enable("false")) multiplexer_20 (
    .in0(R2), .in1({32{1'b0}}), .out(multiplexer_20_out), .sel(Flush));
  Multiplexer #(.select(1), .width(5), .disabled("Z"), .enable("false")) multiplexer_21 (
    .in0(rd), .in1({5{1'b0}}), .out(multiplexer_21_out), .sel(Flush));
  Multiplexer #(.select(1), .width(32), .disabled("Z"), .enable("false")) multiplexer_22 (
    .in0(BImm), .in1({32{1'b0}}), .out(multiplexer_22_out), .sel(Flush));
  Multiplexer #(.select(1), .width(32), .disabled("Z"), .enable("false")) multiplexer_23 (
    .in0(JImm), .in1({32{1'b0}}), .out(multiplexer_23_out), .sel(Flush));
  Multiplexer #(.select(1), .width(32), .disabled("Z"), .enable("false")) multiplexer_24 (
    .in0(UImm), .in1({32{1'b0}}), .out(multiplexer_24_out), .sel(Flush));
  Multiplexer #(.select(1), .width(32), .disabled("Z"), .enable("false")) multiplexer_25 (
    .in0(Imm), .in1({32{1'b0}}), .out(multiplexer_25_out), .sel(Flush));
  Multiplexer #(.select(1), .width(32), .disabled("Z"), .enable("false")) multiplexer_26 (
    .in0(PC), .in1({32{1'b0}}), .out(multiplexer_26_out), .sel(Flush));
  Register #(.width(2), .trigger("rising"), .Select("low")) u_RsFoward (
    .D(multiplexer_1_out), .en(En), .Q(RsFoward_2), .clk(CLK));  // open: clr
  Register #(.width(2), .trigger("rising"), .Select("low")) register_1 (
    .D(multiplexer_2_out), .en(En), .Q(RtFoward_2), .clk(CLK));  // open: clr
  Register #(.width(1), .trigger("rising"), .Select("low")) u_RegWrite (
    .D(multiplexer_3_out), .en(En), .Q(RegWrite_2), .clk(CLK));  // open: clr
  Register #(.width(1), .trigger("rising"), .Select("low")) register_2 (
    .D(multiplexer_4_out), .en(En), .Q(MemToReg_2), .clk(CLK));  // open: clr
  Register #(.width(1), .trigger("rising"), .Select("low")) register_3 (
    .D(multiplexer_5_out), .en(En), .Q(MemWrite_2), .clk(CLK));  // open: clr
  Register #(.width(4), .trigger("rising"), .Select("low")) register_4 (
    .D(multiplexer_6_out), .en(En), .Q(AluOP_2), .clk(CLK));  // open: clr
  Register #(.width(1), .trigger("rising"), .Select("low")) register_5 (
    .D(multiplexer_7_out), .en(En), .Q(Bne_2), .clk(CLK));  // open: clr
  Register #(.width(1), .trigger("rising"), .Select("low")) register_6 (
    .D(multiplexer_8_out), .en(En), .Q(AluSrc_2), .clk(CLK));  // open: clr
  Register #(.width(1), .trigger("rising"), .Select("low")) register_7 (
    .D(multiplexer_9_out), .en(En), .Q(Beq_2), .clk(CLK));  // open: clr
  Register #(.width(1), .trigger("rising"), .Select("low")) register_8 (
    .D(multiplexer_10_out), .en(En), .Q(Bge_2), .clk(CLK));  // open: clr
  Register #(.width(1), .trigger("rising"), .Select("low")) register_9 (
    .D(multiplexer_11_out), .en(En), .Q(Auipc_2), .clk(CLK));  // open: clr
  Register #(.width(1), .trigger("rising"), .Select("low")) register_10 (
    .D(multiplexer_12_out), .en(En), .Q(Byte_2), .clk(CLK));  // open: clr
  Register #(.width(1), .trigger("rising"), .Select("low")) register_11 (
    .D(multiplexer_13_out), .en(En), .Q(Jal_2), .clk(CLK));  // open: clr
  Register #(.width(1), .trigger("rising"), .Select("low")) register_12 (
    .D(multiplexer_14_out), .en(En), .Q(Jalr_2), .clk(CLK));  // open: clr
  Register #(.width(1), .trigger("rising"), .Select("low")) register_13 (
    .D(multiplexer_15_out), .en(En), .Q(Ecall_2), .clk(CLK));  // open: clr
  Register #(.width(1), .trigger("rising"), .Select("low")) register_14 (
    .D(multiplexer_16_out), .en(En), .Q(Uert_2), .clk(CLK));  // open: clr
  Register #(.width(1), .trigger("rising"), .Select("low")) register_15 (
    .D(multiplexer_17_out), .en(En), .Q(PredictJump_2), .clk(CLK));  // open: clr
  Register #(.width(32), .trigger("rising"), .Select("low")) register_16 (
    .D(multiplexer_18_out), .en(En), .Q(IR_2), .clk(CLK));  // open: clr
  Register #(.width(32), .trigger("rising"), .Select("low")) register_17 (
    .D(multiplexer_19_out), .en(En), .Q(R1_2), .clk(CLK));  // open: clr
  Register #(.width(32), .trigger("rising"), .Select("low")) register_18 (
    .D(multiplexer_20_out), .en(En), .Q(R2_2), .clk(CLK));  // open: clr
  Register #(.width(5), .trigger("rising"), .Select("low")) register_19 (
    .D(multiplexer_21_out), .en(En), .Q(rd_2), .clk(CLK));  // open: clr
  Register #(.width(32), .trigger("rising"), .Select("low")) register_20 (
    .D(multiplexer_22_out), .en(En), .Q(BImm_2), .clk(CLK));  // open: clr
  Register #(.width(32), .trigger("rising"), .Select("low")) register_21 (
    .D(multiplexer_23_out), .en(En), .Q(JImm_2), .clk(CLK));  // open: clr
  Register #(.width(32), .trigger("rising"), .Select("low")) register_22 (
    .D(multiplexer_24_out), .en(En), .Q(UImm_2), .clk(CLK));  // open: clr
  Register #(.width(32), .trigger("rising"), .Select("low")) register_23 (
    .D(multiplexer_25_out), .en(En), .Q(Imm_2), .clk(CLK));  // open: clr
  Register #(.width(32), .trigger("rising"), .Select("low")) register_24 (
    .D(multiplexer_26_out), .en(En), .Q(PC_2), .clk(CLK));  // open: clr
endmodule

module EX_MEM (
  input  RegWrite,
  input  MemToReg,
  input  MemWrite,
  input  Byte,
  input  Ecall,
  input  ShouldHalt,
  input  Auipc,
  input  Less,
  input  Slt,
  input  Jal_Jalr,
  input  Uert,
  input  [31:0] UImm,
  input  [31:0] PC,
  input  [31:0] AluResult,
  input  [31:0] IR,
  input  [31:0] WriteData,
  input  [4:0] rd,
  input  Flush,
  input  En,
  input  CLK,
  output RegWrite_2,
  output MemToReg_2,
  output MemWrite_2,
  output Byte_2,
  output Ecall_2,
  output ShouldHalt_2,
  output Auipc_2,
  output Less_2,
  output Slt_2,
  output Jal_Jalr_2,
  output Uert_2,
  output [31:0] UImm_2,
  output [31:0] PC_2,
  output [31:0] AluResult_2,
  output [31:0] IR_2,
  output [31:0] WriteData_2,
  output [4:0] rd_2
);

  wire multiplexer_1_out, multiplexer_2_out, multiplexer_3_out, multiplexer_4_out, multiplexer_5_out,
       multiplexer_6_out, multiplexer_7_out, multiplexer_8_out, multiplexer_9_out, multiplexer_10_out,
       multiplexer_11_out;
  wire [4:0] multiplexer_17_out;
  wire [31:0] multiplexer_12_out, multiplexer_13_out, multiplexer_14_out, multiplexer_15_out,
       multiplexer_16_out;

  Multiplexer #(.select(1), .width(1), .disabled("Z"), .enable("false")) multiplexer_1 (
    .in0(RegWrite), .in1(1'b0), .out(multiplexer_1_out), .sel(Flush));
  Multiplexer #(.select(1), .width(1), .disabled("Z"), .enable("false")) multiplexer_2 (
    .in0(MemToReg), .in1(1'b0), .out(multiplexer_2_out), .sel(Flush));
  Multiplexer #(.select(1), .width(1), .disabled("Z"), .enable("false")) multiplexer_3 (
    .in0(MemWrite), .in1(1'b0), .out(multiplexer_3_out), .sel(Flush));
  Multiplexer #(.select(1), .width(1), .disabled("Z"), .enable("false")) multiplexer_4 (
    .in0(Byte), .in1(1'b0), .out(multiplexer_4_out), .sel(Flush));
  Multiplexer #(.select(1), .width(1), .disabled("Z"), .enable("false")) multiplexer_5 (
    .in0(Ecall), .in1(1'b0), .out(multiplexer_5_out), .sel(Flush));
  Multiplexer #(.select(1), .width(1), .disabled("Z"), .enable("false")) multiplexer_6 (
    .in0(ShouldHalt), .in1(1'b0), .out(multiplexer_6_out), .sel(Flush));
  Multiplexer #(.select(1), .width(1), .disabled("Z"), .enable("false")) multiplexer_7 (
    .in0(Auipc), .in1(1'b0), .out(multiplexer_7_out), .sel(Flush));
  Multiplexer #(.select(1), .width(1), .disabled("Z"), .enable("false")) multiplexer_8 (
    .in0(Less), .in1(1'b0), .out(multiplexer_8_out), .sel(Flush));
  Multiplexer #(.select(1), .width(1), .disabled("Z"), .enable("false")) multiplexer_9 (
    .in0(Slt), .in1(1'b0), .out(multiplexer_9_out), .sel(Flush));
  Multiplexer #(.select(1), .width(1), .disabled("Z"), .enable("false")) multiplexer_10 (
    .in0(Jal_Jalr), .in1(1'b0), .out(multiplexer_10_out), .sel(Flush));
  Multiplexer #(.select(1), .width(1), .disabled("Z"), .enable("false")) multiplexer_11 (
    .in0(Uert), .in1(1'b0), .out(multiplexer_11_out), .sel(Flush));
  Multiplexer #(.select(1), .width(32), .disabled("Z"), .enable("false")) multiplexer_12 (
    .in0(UImm), .in1({32{1'b0}}), .out(multiplexer_12_out), .sel(Flush));
  Multiplexer #(.select(1), .width(32), .disabled("Z"), .enable("false")) multiplexer_13 (
    .in0(PC), .in1({32{1'b0}}), .out(multiplexer_13_out), .sel(Flush));
  Multiplexer #(.select(1), .width(32), .disabled("Z"), .enable("false")) multiplexer_14 (
    .in0(AluResult), .in1({32{1'b0}}), .out(multiplexer_14_out), .sel(Flush));
  Multiplexer #(.select(1), .width(32), .disabled("Z"), .enable("false")) multiplexer_15 (
    .in0(IR), .in1({32{1'b0}}), .out(multiplexer_15_out), .sel(Flush));
  Multiplexer #(.select(1), .width(32), .disabled("Z"), .enable("false")) multiplexer_16 (
    .in0(WriteData), .in1({32{1'b0}}), .out(multiplexer_16_out), .sel(Flush));
  Multiplexer #(.select(1), .width(5), .disabled("Z"), .enable("false")) multiplexer_17 (
    .in0(rd), .in1({5{1'b0}}), .out(multiplexer_17_out), .sel(Flush));
  Register #(.width(1), .trigger("rising"), .Select("low")) u_RegWrite (
    .D(multiplexer_1_out), .en(En), .Q(RegWrite_2), .clk(CLK));  // open: clr
  Register #(.width(1), .trigger("rising"), .Select("low")) register_1 (
    .D(multiplexer_2_out), .en(En), .Q(MemToReg_2), .clk(CLK));  // open: clr
  Register #(.width(1), .trigger("rising"), .Select("low")) register_2 (
    .D(multiplexer_3_out), .en(En), .Q(MemWrite_2), .clk(CLK));  // open: clr
  Register #(.width(1), .trigger("rising"), .Select("low")) register_3 (
    .D(multiplexer_4_out), .en(En), .Q(Byte_2), .clk(CLK));  // open: clr
  Register #(.width(1), .trigger("rising"), .Select("low")) u_Ecall (
    .D(multiplexer_5_out), .en(En), .Q(Ecall_2), .clk(CLK));  // open: clr
  Register #(.width(1), .trigger("rising"), .Select("low")) u_ShouldHalt (
    .D(multiplexer_6_out), .en(En), .Q(ShouldHalt_2), .clk(CLK));  // open: clr
  Register #(.width(1), .trigger("rising"), .Select("low")) u_Auipc (
    .D(multiplexer_7_out), .en(En), .Q(Auipc_2), .clk(CLK));  // open: clr
  Register #(.width(1), .trigger("rising"), .Select("low")) u_Less (
    .D(multiplexer_8_out), .en(En), .Q(Less_2), .clk(CLK));  // open: clr
  Register #(.width(1), .trigger("rising"), .Select("low")) u_Slt (
    .D(multiplexer_9_out), .en(En), .Q(Slt_2), .clk(CLK));  // open: clr
  Register #(.width(1), .trigger("rising"), .Select("low")) u_Jal_Jalr (
    .D(multiplexer_10_out), .en(En), .Q(Jal_Jalr_2), .clk(CLK));  // open: clr
  Register #(.width(1), .trigger("rising"), .Select("low")) u_Uert (
    .D(multiplexer_11_out), .en(En), .Q(Uert_2), .clk(CLK));  // open: clr
  Register #(.width(32), .trigger("rising"), .Select("low")) register_4 (
    .D(multiplexer_12_out), .en(En), .Q(UImm_2), .clk(CLK));  // open: clr
  Register #(.width(32), .trigger("rising"), .Select("low")) register_5 (
    .D(multiplexer_13_out), .en(En), .Q(PC_2), .clk(CLK));  // open: clr
  Register #(.width(32), .trigger("rising"), .Select("low")) register_6 (
    .D(multiplexer_14_out), .en(En), .Q(AluResult_2), .clk(CLK));  // open: clr
  Register #(.width(32), .trigger("rising"), .Select("low")) register_7 (
    .D(multiplexer_15_out), .en(En), .Q(IR_2), .clk(CLK));  // open: clr
  Register #(.width(32), .trigger("rising"), .Select("low")) register_8 (
    .D(multiplexer_16_out), .en(En), .Q(WriteData_2), .clk(CLK));  // open: clr
  Register #(.width(5), .trigger("rising"), .Select("low")) register_9 (
    .D(multiplexer_17_out), .en(En), .Q(rd_2), .clk(CLK));  // open: clr
endmodule

module ME_WB (
  input  RegWrite,
  input  MemToReg,
  input  Ecall,
  input  ShouldHalt,
  input  [31:0] IR,
  input  [31:0] PC,
  input  [31:0] AluResult,
  input  [31:0] RD,
  input  [4:0] rd_2,
  input  En,
  input  CLK,
  output RegWrite_2,
  output MemToReg_2,
  output Ecall_2,
  output ShouldHalt_2,
  output [31:0] IR_2,
  output [31:0] PC_2,
  output [31:0] AluResult_2,
  output [31:0] RD_3,
  output [4:0] rd_4
);

  Register #(.width(1), .trigger("rising"), .Select("low")) u_RegWrite (
    .D(RegWrite), .en(En), .Q(RegWrite_2), .clk(CLK));  // open: clr
  Register #(.width(1), .trigger("rising"), .Select("low")) register_1 (
    .D(MemToReg), .en(En), .Q(MemToReg_2), .clk(CLK));  // open: clr
  Register #(.width(1), .trigger("rising"), .Select("low")) u_Ecall (
    .D(Ecall), .en(En), .Q(Ecall_2), .clk(CLK));  // open: clr
  Register #(.width(1), .trigger("rising"), .Select("low")) u_ShouldHalt (
    .D(ShouldHalt), .en(En), .Q(ShouldHalt_2), .clk(CLK));  // open: clr
  Register #(.width(32), .trigger("rising"), .Select("low")) register_2 (
    .D(IR), .en(En), .Q(IR_2), .clk(CLK));  // open: clr
  Register #(.width(32), .trigger("rising"), .Select("low")) register_3 (
    .D(PC), .en(En), .Q(PC_2), .clk(CLK));  // open: clr
  Register #(.width(32), .trigger("rising"), .Select("low")) register_4 (
    .D(AluResult), .en(En), .Q(AluResult_2), .clk(CLK));  // open: clr
  Register #(.width(32), .trigger("rising"), .Select("low")) register_5 (
    .D(RD), .en(En), .Q(RD_3), .clk(CLK));  // open: clr
  Register #(.width(5), .trigger("rising"), .Select("low")) register_6 (
    .D(rd_2), .en(En), .Q(rd_4), .clk(CLK));  // open: clr
endmodule

module MIPS_RAM (
  input  [11:0] \字节地址 ,
  input  [31:0] Din,
  input  CLK,
  input  WE,
  input  [1:0] Mode,
  output [31:0] DataOut
);

  wire and_1_out, and_2_out, and_3_out, and_4_out, multiplexer_3_out, multiplexer_5_out, multiplexer_6_out,
       multiplexer_8_out, not_1_out, not_2_out, not_3_out, not_4_out;
  wire [7:0] controlled_buffer_1_out, controlled_buffer_2_out, controlled_buffer_6_out,
       controlled_buffer_8_out, controlled_buffer_11_out, demultiplexer_1_out0, demultiplexer_1_out0_2,
       demultiplexer_1_out0_3, demultiplexer_1_out0_4, demultiplexer_1_out1, demultiplexer_1_out1_2,
       demultiplexer_1_out1_3, demultiplexer_1_out1_4, demultiplexer_1_out2, demultiplexer_1_out2_2,
       demultiplexer_1_out2_3, demultiplexer_1_out2_4, multiplexer_1_out, multiplexer_2_out,
       multiplexer_4_out, multiplexer_7_out, ram_1_data, ram_2_data, ram_3_data, ram_4_data, \计数器_q ;
  wire [15:0] controlled_buffer_5_out;

  Multiplexer #(.select(2), .width(8), .disabled("Z"), .enable("false")) multiplexer_1 (
    .in0(demultiplexer_1_out0_4), .in1(demultiplexer_1_out1), .in2(demultiplexer_1_out2_2),
    .out(multiplexer_1_out), .sel(Mode));  // open: in3
  Demultiplexer #(.select(2), .width(32), .tristate("false"), .disabled("Z"), .enable("false")) demultiplexer_1 (
    .out0({demultiplexer_1_out0_4, demultiplexer_1_out0_3, demultiplexer_1_out0_2, demultiplexer_1_out0}),
    .out1({demultiplexer_1_out1_4, demultiplexer_1_out1_3, demultiplexer_1_out1_2, demultiplexer_1_out1}),
    .out2({demultiplexer_1_out2_4, demultiplexer_1_out2_3, demultiplexer_1_out2_2, demultiplexer_1_out2}),
    .in(Din), .sel(Mode));  // open: out3
  assign controlled_buffer_1_out = multiplexer_3_out ? ram_1_data : 8'bz;  // Controlled_Buffer controlled_buffer_1
  RAM #(.addrWidth(10), .dataWidth(8), .bus("separate"), .Select("high")) ram_1 (
    .addr(\字节地址 [11:2]), .din(multiplexer_1_out), .data(ram_1_data), .str(WE), .sel(multiplexer_3_out),
    .clk(CLK), .ld(1'b1));  // open: clr
  assign controlled_buffer_2_out = multiplexer_3_out ? ram_1_data : 8'bz;  // Controlled_Buffer controlled_buffer_2
  assign controlled_buffer_5_out[15:8] = multiplexer_3_out ? ram_1_data : 8'bz;  // Controlled_Buffer controlled_buffer_3
  Multiplexer #(.select(2), .width(8), .disabled("Z"), .enable("false")) multiplexer_2 (
    .in0(demultiplexer_1_out0_3), .in1(demultiplexer_1_out1), .in2(demultiplexer_1_out2),
    .out(multiplexer_2_out), .sel(Mode));  // open: in3
  Multiplexer #(.select(2), .width(1), .disabled("Z"), .enable("false")) multiplexer_3 (
    .in0(1'b1), .in1(and_1_out), .in2(\字节地址 [1]), .out(multiplexer_3_out), .sel(Mode));  // open: in3
  and and_1 (and_1_out, \字节地址 [0], \字节地址 [1]);
  assign controlled_buffer_1_out = multiplexer_5_out ? ram_2_data : 8'bz;  // Controlled_Buffer controlled_buffer_4
  assign controlled_buffer_5_out[7:0] = multiplexer_5_out ? ram_2_data : 8'bz;  // Controlled_Buffer controlled_buffer_5
  RAM #(.addrWidth(10), .dataWidth(8), .bus("separate"), .Select("high")) ram_2 (
    .addr(\字节地址 [11:2]), .din(multiplexer_2_out), .data(ram_2_data), .str(WE), .sel(multiplexer_5_out),
    .clk(CLK), .ld(1'b1));  // open: clr
  and and_2 (and_2_out, not_1_out, \字节地址 [1]);
  not not_1 (not_1_out, \字节地址 [0]);
  assign controlled_buffer_6_out = multiplexer_5_out ? ram_2_data : 8'bz;  // Controlled_Buffer controlled_buffer_6
  Multiplexer #(.select(2), .width(8), .disabled("Z"), .enable("false")) multiplexer_4 (
    .in0(demultiplexer_1_out0_2), .in1(demultiplexer_1_out1), .in2(demultiplexer_1_out2_2),
    .out(multiplexer_4_out), .sel(Mode));  // open: in3
  Multiplexer #(.select(2), .width(1), .disabled("Z"), .enable("false")) multiplexer_5 (
    .in0(1'b1), .in1(and_2_out), .in2(\字节地址 [1]), .out(multiplexer_5_out), .sel(Mode));  // open: in3
  // Probe on DataOut
  Multiplexer #(.select(2), .width(1), .disabled("Z"), .enable("false")) multiplexer_6 (
    .in0(1'b1), .in1(and_3_out), .in2(not_2_out), .out(multiplexer_6_out), .sel(Mode));  // open: in3
  and and_3 (and_3_out, \字节地址 [0], not_2_out);
  not not_2 (not_2_out, \字节地址 [1]);
  assign controlled_buffer_5_out[15:8] = multiplexer_6_out ? ram_3_data : 8'bz;  // Controlled_Buffer controlled_buffer_7
  assign controlled_buffer_8_out = multiplexer_6_out ? ram_3_data : 8'bz;  // Controlled_Buffer controlled_buffer_8
  assign controlled_buffer_1_out = multiplexer_6_out ? ram_3_data : 8'bz;  // Controlled_Buffer controlled_buffer_9
  RAM #(.addrWidth(10), .dataWidth(8), .bus("separate"), .Select("high")) ram_3 (
    .addr(\字节地址 [11:2]), .din(multiplexer_4_out), .data(ram_3_data), .str(WE), .sel(multiplexer_6_out),
    .clk(CLK), .ld(1'b1));  // open: clr
  Multiplexer #(.select(2), .width(8), .disabled("Z"), .enable("false")) multiplexer_7 (
    .in0(demultiplexer_1_out0), .in1(demultiplexer_1_out1), .in2(demultiplexer_1_out2),
    .out(multiplexer_7_out), .sel(Mode));  // open: in3
  Multiplexer #(.select(2), .width(1), .disabled("Z"), .enable("false")) multiplexer_8 (
    .in0(1'b1), .in1(and_4_out), .in2(not_4_out), .out(multiplexer_8_out), .sel(Mode));  // open: in3
  and and_4 (and_4_out, not_3_out, not_4_out);
  not not_3 (not_3_out, \字节地址 [0]);
  not not_4 (not_4_out, \字节地址 [1]);
  Counter #(.width(8), .max('hff), .ongoal("wrap"), .trigger("rising"), .behavior("old")) \u_计数器  (
    .Q(\计数器_q ), .clk(CLK));  // open: load, D, count, carry, clr, preset
  // Probe on \计数器_q 
  assign controlled_buffer_1_out = multiplexer_8_out ? ram_4_data : 8'bz;  // Controlled_Buffer controlled_buffer_10
  assign controlled_buffer_11_out = multiplexer_8_out ? ram_4_data : 8'bz;  // Controlled_Buffer controlled_buffer_11
  assign controlled_buffer_5_out[7:0] = multiplexer_8_out ? ram_4_data : 8'bz;  // Controlled_Buffer controlled_buffer_12
  RAM #(.addrWidth(10), .dataWidth(8), .bus("separate"), .Select("high")) ram_4 (
    .addr(\字节地址 [11:2]), .din(multiplexer_7_out), .data(ram_4_data), .str(WE), .sel(multiplexer_8_out),
    .clk(CLK), .ld(1'b1));  // open: clr
  Multiplexer #(.select(2), .width(32), .disabled("Z"), .enable("false")) multiplexer_9 (
    .in0({controlled_buffer_2_out, controlled_buffer_6_out, controlled_buffer_8_out, controlled_buffer_11_out}),
    .in1({{24{1'b0}}, controlled_buffer_1_out}), .in2({{16{1'b0}}, controlled_buffer_5_out}),
    .in3({32{1'b0}}), .out(DataOut), .sel(Mode));

  // Other names for the same wires on the sheet: Dout[31:0] = DataOut; ADDR[9:0] = \字节地址 [11:2]

  // Notes on the sheet:
  //   输入引脚区
  //   请勿增改引脚，请勿修改子电路封装
  //   电路功能：利用下图中给定的RAM器件实现既既可以按照字节，也可以按照半字，也可以按照32位字访问的MIPS存储器
  //   请在下方利用上方输入输出引脚的隧道信号构建电路，ctrl+d复制选择部件
  //   输出引脚区
  //   为方便测试，注意Dout应一直输出数据，所有数据位不得悬空，所有RAM芯片ld控制端悬空即可
endmodule

module \气泡处理逻辑  (
  input  RsUsed,
  input  [4:0] rs,
  input  RtUsed,
  input  [4:0] rt,
  input  MEM_RegWrite,
  input  [4:0] MEM_WriteReg_V,
  input  EX_RegWrite,
  input  [4:0] EX_WriteReg_V,
  input  BranchTaken,
  output DataHazzard,
  output Stall,
  output PC_EN,
  output IF_ID_EN,
  output IF_ID_CLR,
  output ID_EX_CLR,
  output Flush
);

  wire and_1_out, and_2_out, and_3_out, and_4_out, and_5_out, and_6_out, and_7_out, and_8_out,
       comparator_1_eq, comparator_2_eq, comparator_3_eq, comparator_4_eq, comparator_5_eq, comparator_6_eq,
       not_1_out, not_2_out, Rs_out, Rt_out;

  Comparator #(.width(5), .mode("twosComplement")) comparator_1 (
    .a(rs), .b({5{1'b0}}), .eq(comparator_1_eq));  // open: gt, lt
  Comparator #(.width(5), .mode("twosComplement")) comparator_2 (
    .a(rt), .b({5{1'b0}}), .eq(comparator_2_eq));  // open: gt, lt
  Comparator #(.width(5), .mode("twosComplement")) comparator_3 (
    .a(MEM_WriteReg_V), .b(rt), .eq(comparator_3_eq));  // open: gt, lt
  Comparator #(.width(5), .mode("twosComplement")) comparator_4 (
    .a(MEM_WriteReg_V), .b(rs), .eq(comparator_4_eq));  // open: gt, lt
  Comparator #(.width(5), .mode("twosComplement")) comparator_5 (
    .a(EX_WriteReg_V), .b(rt), .eq(comparator_5_eq));  // open: gt, lt
  Comparator #(.width(5), .mode("twosComplement")) comparator_6 (
    .a(EX_WriteReg_V), .b(rs), .eq(comparator_6_eq));  // open: gt, lt
  not not_1 (not_1_out, comparator_1_eq);
  not not_2 (not_2_out, comparator_2_eq);
  and and_1 (and_1_out, RsUsed, not_1_out);
  and and_2 (and_2_out, RtUsed, not_2_out);
  and and_3 (and_3_out, MEM_RegWrite, comparator_3_eq);
  and and_4 (and_4_out, MEM_RegWrite, comparator_4_eq);
  and and_5 (and_5_out, EX_RegWrite, comparator_5_eq);
  and and_6 (and_6_out, EX_RegWrite, comparator_6_eq);
  or u_Rt (Rt_out, and_3_out, and_5_out);
  or u_Rs (Rs_out, and_4_out, and_6_out);
  and and_7 (and_7_out, and_2_out, Rt_out);
  and and_8 (and_8_out, and_1_out, Rs_out);
  or or_1 (DataHazzard, and_7_out, and_8_out);
  not not_3 (IF_ID_EN, DataHazzard);
  or or_2 (Flush, BranchTaken, DataHazzard);

  assign ID_EX_CLR = Flush;
  assign IF_ID_CLR = BranchTaken;
  assign PC_EN = IF_ID_EN;
  assign Stall = DataHazzard;
endmodule

module \气泡_重定向处理逻辑  (
  input  RsUsed,
  input  [4:0] rs,
  input  RtUsed,
  input  [4:0] rt,
  input  EX_RegWrite,
  input  [4:0] MEM_WriteReg_V,
  input  MEM_RegWrite,
  input  [4:0] EX_WriteReg_V,
  input  EX_MemToReg,
  input  BranchTaken,
  output [1:0] RsFoward,
  output [1:0] RtFoward,
  output LoadUse,
  output Stall,
  output PC_EN,
  output IF_ID_EN,
  output IF_ID_CLR,
  output ID_EX_CLR,
  output Flush
);

  wire and_3_out, and_4_out, and_5_out, and_6_out, and_7_out, and_8_out, and_9_out, and_10_out, and_11_out,
       and_12_out, comparator_1_eq, comparator_2_eq, not_1_out, not_2_out, or_1_out, rs__EX_reg, rs__MEM_reg,
       RsUsed__rs__0, rt__EX_reg, rt__MEM_reg, RtUsed__rt__0;
  wire [1:0] multiplexer_1_out, multiplexer_2_out;

  Comparator #(.width(5), .mode("twosComplement")) comparator_1 (
    .a(rs), .b({5{1'b0}}), .eq(comparator_1_eq));  // open: gt, lt
  Comparator #(.width(5), .mode("twosComplement")) comparator_2 (
    .a(rt), .b({5{1'b0}}), .eq(comparator_2_eq));  // open: gt, lt
  Comparator #(.width(5), .mode("twosComplement")) comparator_3 (
    .a(MEM_WriteReg_V), .b(rt), .eq(rt__MEM_reg));  // open: gt, lt
  Comparator #(.width(5), .mode("twosComplement")) comparator_4 (
    .a(MEM_WriteReg_V), .b(rs), .eq(rs__MEM_reg));  // open: gt, lt
  Comparator #(.width(5), .mode("twosComplement")) comparator_5 (
    .a(EX_WriteReg_V), .b(rt), .eq(rt__EX_reg));  // open: gt, lt
  Comparator #(.width(5), .mode("twosComplement")) comparator_6 (
    .a(EX_WriteReg_V), .b(rs), .eq(rs__EX_reg));  // open: gt, lt
  not not_1 (not_1_out, comparator_1_eq);
  not not_2 (not_2_out, comparator_2_eq);
  and and_1 (RsUsed__rs__0, RsUsed, not_1_out);
  and and_2 (RtUsed__rt__0, RtUsed, not_2_out);
  and and_3 (and_3_out, rs__EX_reg, EX_RegWrite);
  and and_4 (and_4_out, rs__MEM_reg, MEM_RegWrite);
  and and_5 (and_5_out, rt__EX_reg, EX_RegWrite);
  and and_6 (and_6_out, rt__MEM_reg, MEM_RegWrite);
  and and_7 (and_7_out, RsUsed__rs__0, rs__EX_reg);
  and and_8 (and_8_out, RtUsed__rt__0, rt__EX_reg);
  and and_9 (and_9_out, RsUsed__rs__0, and_3_out);
  and and_10 (and_10_out, RsUsed__rs__0, and_4_out);
  and and_11 (and_11_out, RtUsed__rt__0, and_5_out);
  and and_12 (and_12_out, RtUsed__rt__0, and_6_out);
  or or_1 (or_1_out, and_7_out, and_8_out);
  and and_13 (LoadUse, or_1_out, EX_MemToReg);
  Multiplexer #(.select(1), .width(2), .disabled("Z"), .enable("false")) multiplexer_1 (
    .in0(2'b00), .in1(2'b01), .out(multiplexer_1_out), .sel(and_10_out));
  Multiplexer #(.select(1), .width(2), .disabled("Z"), .enable("false")) multiplexer_2 (
    .in0(2'b00), .in1(2'b01), .out(multiplexer_2_out), .sel(and_12_out));
  not not_3 (IF_ID_EN, LoadUse);
  or or_2 (Flush, BranchTaken, LoadUse);
  Multiplexer #(.select(1), .width(2), .disabled("Z"), .enable("false")) multiplexer_3 (
    .in0(multiplexer_1_out), .in1(2'b10), .out(RsFoward), .sel(and_9_out));
  Multiplexer #(.select(1), .width(2), .disabled("Z"), .enable("false")) multiplexer_4 (
    .in0(multiplexer_2_out), .in1(2'b10), .out(RtFoward), .sel(and_11_out));

  assign ID_EX_CLR = Flush;
  assign IF_ID_CLR = BranchTaken;
  assign PC_EN = IF_ID_EN;
  assign Stall = LoadUse;
endmodule
module \重定向中断流水线  (
  input  IR1,
  input  IR2,
  input  IR3,
  output RegWrite,
  output MemWrite,
  output [31:0] IF_PC,
  output [31:0] ID_PC,
  output [31:0] EX_PC,
  output [31:0] M_PC,
  output [31:0] WB_PC,
  output [31:0] RDin,
  output [31:0] MDin,
  output [31:0] LedData
);

  wire alu_1_out_6, and_1_out, and_2_out, and_3_out, and_4_out, and_5_out, and_8_out, and_9_out, and_10_out,
       and_11_out, and_12_out, and_13_out, and_14_out, and_15_out, and_16_out, and_17_out, Auipc, Beq, Bge,
       Bne, Branch, BranchTaken, button_1_out, button_2_out, button_3_out, Byte, CLK, clock_1_out,
       clock_2_out, clock_3_out, clock_4_out, comparator_1_gt, comparator_2_eq, comparator_2_lt,
       comparator_3_eq, comparator_4_eq, comparator_5_eq, comparator_6_eq, comparator_7_eq, comparator_8_eq,
       comparator_9_eq, comparator_10_eq, CSIR1, CSIR2, CSIR3, d_ff_1_q, d_ff_2_q, d_ff_3_q, d_ff_4_q, Ecall,
       Equ, EX_Flush, ex_mem_1_auipc_2, ex_mem_1_byte_2, ex_mem_1_ecall_2, ex_mem_1_jal_jalr_2,
       ex_mem_1_less_2, ex_mem_1_memtoreg_2, ex_mem_1_regwrite_2, ex_mem_1_shouldhalt_2, ex_mem_1_slt_2,
       EX_Uert, Flush, Geq, Go, halt, id_ex_1_alusrc_2, id_ex_1_auipc_2, id_ex_1_beq_2, id_ex_1_bge_2,
       id_ex_1_bne_2, id_ex_1_byte_2, id_ex_1_ecall_2, id_ex_1_jal_2, id_ex_1_jalr_2, id_ex_1_memtoreg_2,
       id_ex_1_memwrite_2, id_ex_1_regwrite_2, IE, if_id_1_p5, Inte, IR1_q, IR1_t, IR2_q, IR2_t, IR3_q,
       IR3_t, IRA, IRB, IRC, Jal, Jalr, JJump, ME_Uert, me_wb_1_ecall_2, me_wb_1_memtoreg_2,
       me_wb_1_shouldhalt_2, nand_1_out, nand_2_out, not_1_out, not_2_out, not_3_out, not_4_out, not_5_out,
       not_6_out, not_7_out, not_8_out, not_9_out, or_1_out, or_2_out, or_3_out, or_4_out, or_5_out,
       or_6_out, or_8_out, or_10_out, or_12_out, or_13_out, or_14_out, priority_encoder_1_gs, ResetIR1,
       ResetIR2, ResetIR3, riscv_probe_3_p1, RST, stall, Uert, W1, W2, W3, \单周期硬布线控制器_1_alu_src ,
       \单周期硬布线控制器_1_memtoreg , \单周期硬布线控制器_1_memwrite , \单周期硬布线控制器_1_regwrite , \单周期硬布线控制器_1_rsused ,
       \单周期硬布线控制器_1_rtused , \单周期硬布线控制器_1_s_type , \气泡_重定向处理逻辑_1_if_id_en , \气泡_重定向处理逻辑_1_pc_en ;
  wire [1:0] EX_RsFoward, EX_RtFoward, ID_RsFoward, ID_RtFoward, IR_Id, multiplexer_14_out, register_1_q;
  wire [3:0] id_ex_1_aluop_2, \单周期硬布线控制器_1_alu_op ;
  wire [4:0] ex_mem_1_rd_2, id_ex_1_rd_2, me_wb_1_rd_4, multiplexer_2_out, multiplexer_3_out;
  wire [12:0] CNT_num;
  wire [15:0] \LoadUse次数 , \总周期数 , \插入气泡数 , \无条件分支数 , \条件分支成功数 ;
  wire [31:0] adder_1_out, adder_2_out, adder_3_out, adder_4_out, adder_5_out, alu_1_result, and_7_out,
       bit_extender_1_out, bit_extender_2_out, bit_extender_3_out, bit_extender_4_out, bit_extender_5_out,
       bit_extender_6_out, EPC, EX_IR, ex_mem_1_aluresult_2, ex_mem_1_uimm_2, EX_RE_RS, EX_RE_RT, EX_RS,
       EX_RT, id_ex_1_bimm_2, id_ex_1_imm_2, id_ex_1_jimm_2, id_ex_1_uimm_2, ID_IR, IF_IR,
       me_wb_1_aluresult_2, me_wb_1_rd_3, MEM_IR, mips_ram_1_dataout, multiplexer_4_out, multiplexer_5_out,
       multiplexer_6_out, multiplexer_7_out, multiplexer_8_out, multiplexer_9_out, multiplexer_10_out,
       multiplexer_15_out, multiplexer_16_out, multiplexer_17_out, NextPC, NextPCWithoutInt, regifile_1_r1,
       regifile_1_r2, shifter_1_out, shifter_2_out, shifter_3_out, WB_IR;

  Button \u_总复位  (.out(RST));
  Button _1 (.out(IR1_t));
  Button _2 (.out(IR2_t));
  Button _3 (.out(IR3_t));
  // Probe on \总周期数 
  // Probe on \总周期数 
  Button \u_继续运行  (.out(Go));
  LED #(.active("true")) led_1 (.in(W1));
  LED #(.active("true")) led_2 (.in(W2));
  LED #(.active("true")) led_3 (.in(W3));
  not not_1 (not_1_out, halt);
  and and_1 (and_1_out, not_1_out, \气泡_重定向处理逻辑_1_pc_en );
  Multiplexer #(.select(1), .width(32), .disabled("Z"), .enable("false")) multiplexer_1 (
    .in0(adder_1_out), .in1(multiplexer_8_out), .out(NextPCWithoutInt), .sel(comparator_1_gt));
  Hex_Digit_Display hex_digit_display_1 (.value(LedData[31:28]));  // open: dp
  // Probe on IF_PC[19:0]
  // RiscV_Probe riscv_probe_1: pin names not known; wires that end beside it: IF_IR
  Register #(.width(32), .trigger("rising"), .Select("low")) PC (
    .D(NextPC), .en(and_1_out), .Q(IF_PC), .clk(CLK), .clr(riscv_probe_3_p1));
  Hex_Digit_Display hex_digit_display_2 (.value(LedData[27:24]));  // open: dp
  Hex_Digit_Display hex_digit_display_3 (.value(LedData[23:20]));  // open: dp
  // Probe on ID_PC[19:0]
  // RiscV_Probe riscv_probe_2: pin names not known; wires that end beside it: ID_IR
  Hex_Digit_Display hex_digit_display_4 (.value(LedData[19:16]));  // open: dp
  Hex_Digit_Display hex_digit_display_5 (.value(LedData[15:12]));  // open: dp
  // RiscV_Probe riscv_probe_3: pin names not known; wires that end beside it: riscv_probe_3_p1, RST, IF_IR, IF_IR
  Adder #(.width(32)) adder_1 (.a(IF_PC), .b(32'h4), .out(adder_1_out));  // open: cin, cout
  Button button_1 (.out(button_1_out));
  Hex_Digit_Display hex_digit_display_6 (.value(LedData[7:4]));  // open: dp
  Hex_Digit_Display hex_digit_display_7 (.value(LedData[11:8]));  // open: dp
  // Probe on EX_PC[19:0]
  // RiscV_Probe riscv_probe_4: pin names not known; wires that end beside it: EX_IR
  not not_2 (not_2_out, halt);
  and and_2 (and_2_out, not_2_out, \气泡_重定向处理逻辑_1_if_id_en );
  ROM #(.addrWidth(10), .dataWidth(32), .Select("high")) rom_1 (.addr(IF_PC[11:2]), .data(IF_IR));
  Clock #(.highDuration(1), .lowDuration(1)) clock_1 (.out(clock_1_out));
  LED #(.active("true")) \_1号中断等待指示灯  (.in(or_1_out));
  or or_1 (or_1_out, IR1_q, d_ff_1_q);
  Clock #(.highDuration(1), .lowDuration(1)) clock_2 (.out(clock_2_out));
  Button button_2 (.out(button_2_out));
  LED #(.active("true")) \_2号中断等待指示灯  (.in(or_2_out));
  or or_2 (or_2_out, IR2_q, d_ff_2_q);
  Clock #(.highDuration(1), .lowDuration(1)) clock_3 (.out(clock_3_out));
  Button button_3 (.out(button_3_out));
  LED #(.active("true")) \_3号中断等待指示灯  (.in(or_3_out));
  or or_3 (or_3_out, IR3_q, d_ff_3_q);
  Hex_Digit_Display hex_digit_display_8 (.value(LedData[3:0]));  // open: dp
  // IF_ID if_id_1: pin names not known; wires that end beside it: IF_IR, IF_PC, and_2_out, CLK, if_id_1_p5, 1'b0, ID_IR, ID_PC
  D_Flip_Flop #(.trigger("rising"), .Pre_Clr_Positions("LEGACY"), .NegatePresetClear("false"), .enable("true"), .NewFFLayout("false")) d_ff_1 (
    .clk(button_1_out), .D(1'b1), .Q(d_ff_1_q), .reset(IR1_q));  // open: Qn, preset, en
  D_Flip_Flop #(.trigger("rising"), .Pre_Clr_Positions("LEGACY"), .NegatePresetClear("false"), .enable("true"), .NewFFLayout("false")) d_ff_2 (
    .clk(button_2_out), .D(1'b1), .Q(d_ff_2_q), .reset(IR2_q));  // open: Qn, preset, en
  D_Flip_Flop #(.trigger("rising"), .Pre_Clr_Positions("LEGACY"), .NegatePresetClear("false"), .enable("true"), .NewFFLayout("false")) d_ff_3 (
    .clk(button_3_out), .D(1'b1), .Q(d_ff_3_q), .reset(IR3_q));  // open: Qn, preset, en
  // Probe on \总周期数 
  // Probe on M_PC[19:0]
  // RiscV_Probe riscv_probe_5: pin names not known; wires that end beside it: MEM_IR
  or or_4 (or_4_out, d_ff_1_q, IR1_q);
  or or_5 (or_5_out, d_ff_2_q, IR2_q);
  or or_6 (or_6_out, d_ff_3_q, IR3_q);
  // Probe on \总周期数 
  // Probe on \无条件分支数 
  // Probe on \条件分支成功数 
  // Probe on \插入气泡数 
  // Probe on \LoadUse次数 
  \单周期硬布线控制器  \u_单周期硬布线控制器_1  (
    .Funct({ID_IR[30], ID_IR[25], ID_IR[14:12]}), .OP(ID_IR[6:2]), .ALU_OP(\单周期硬布线控制器_1_alu_op ),
    .MemToReg(\单周期硬布线控制器_1_memtoreg ), .MemWrite(\单周期硬布线控制器_1_memwrite ), .ALU_SRC(\单周期硬布线控制器_1_alu_src ),
    .RegWrite(\单周期硬布线控制器_1_regwrite ), .ecall(Ecall), .S_type(\单周期硬布线控制器_1_s_type ), .Jalr(Jalr), .Beq(Beq),
    .JAL(Jal), .Bne(Bne), .in_3(ID_IR[21]), .uret(Uert), .Auipc(Auipc), .Byte(Byte), .BGE(Bge),
    .RsUsed(\单周期硬布线控制器_1_rsused ), .RtUsed(\单周期硬布线控制器_1_rtused ));  // open: CSRRSI, CSRRCI
  Multiplexer #(.select(1), .width(5), .disabled("Z"), .enable("false")) multiplexer_2 (
    .in0(ID_IR[19:15]), .in1(5'b10001), .out(multiplexer_2_out), .sel(Ecall));
  // Probe on multiplexer_2_out
  Multiplexer #(.select(1), .width(5), .disabled("Z"), .enable("false")) multiplexer_3 (
    .in0(ID_IR[24:20]), .in1(5'b01010), .out(multiplexer_3_out), .sel(Ecall));
  // Probe on multiplexer_3_out
  assign bit_extender_1_out = {{20{ID_IR[31]}}, ID_IR[31:20]};  // Bit_Extender bit_extender_1
  assign bit_extender_2_out = {{20{ID_IR[31]}}, {ID_IR[31:25], ID_IR[11:7]}};  // Bit_Extender bit_extender_2
  and and_3 (and_3_out, or_4_out, ~ResetIR1);  // AND_Gate
  and and_4 (and_4_out, or_5_out, ~ResetIR2);  // AND_Gate
  and and_5 (and_5_out, or_6_out, ~ResetIR3);  // AND_Gate
  // Probe on IF_PC[11:0]
  // Probe on WB_PC[19:0]
  // RiscV_Probe riscv_probe_6: pin names not known; wires that end beside it: WB_IR
  Multiplexer #(.select(1), .width(32), .disabled("Z"), .enable("false")) multiplexer_4 (
    .in0(bit_extender_1_out), .in1(bit_extender_2_out), .out(multiplexer_4_out), .sel(\单周期硬布线控制器_1_s_type ));
  assign bit_extender_3_out = {{20{ID_IR[31]}}, {ID_IR[31], ID_IR[7], ID_IR[30:25], ID_IR[11:8]}};  // Bit_Extender bit_extender_3
  assign bit_extender_4_out = {{12{ID_IR[31]}}, {ID_IR[31], ID_IR[19:12], ID_IR[20], ID_IR[30:21]}};  // Bit_Extender bit_extender_4
  assign bit_extender_5_out = {{12{ID_IR[31]}}, ID_IR[31:12]};  // Bit_Extender bit_extender_5
  Shifter #(.width(32), .shift("ll")) shifter_1 (.in(bit_extender_5_out), .\dist (5'b01100), .out(shifter_1_out));
  D_Flip_Flop #(.trigger("rising"), .Pre_Clr_Positions("LEGACY"), .NegatePresetClear("false"), .enable("true"), .NewFFLayout("false")) u_IR1 (
    .clk(clock_1_out), .D(and_3_out), .Q(IR1_q));  // open: Qn, preset, en, reset
  D_Flip_Flop #(.trigger("rising"), .Pre_Clr_Positions("LEGACY"), .NegatePresetClear("false"), .enable("true"), .NewFFLayout("false")) u_IR2 (
    .clk(clock_2_out), .D(and_4_out), .Q(IR2_q));  // open: Qn, preset, en, reset
  D_Flip_Flop #(.trigger("rising"), .Pre_Clr_Positions("LEGACY"), .NegatePresetClear("false"), .enable("true"), .NewFFLayout("false")) u_IR3 (
    .clk(clock_3_out), .D(and_5_out), .Q(IR3_q));  // open: Qn, preset, en, reset
  // Probe on ID_PC[11:0]
  // Probe on EX_PC[11:0]
  not not_3 (not_3_out, CLK);
  Regifile regifile_1 (
    .Din(RDin), .Clk(not_3_out), .R1(regifile_1_r1), .R2(regifile_1_r2), .WE(RegWrite), .W_num(me_wb_1_rd_4),
    .R1_num(multiplexer_2_out), .R2_num(multiplexer_3_out));
  Shifter #(.width(32), .shift("ll")) shifter_2 (.in(bit_extender_3_out), .\dist (5'b00001), .out(shifter_2_out));
  Shifter #(.width(32), .shift("ll")) shifter_3 (.in(bit_extender_4_out), .\dist (5'b00001), .out(shifter_3_out));
  Adder #(.width(32)) adder_2 (.a(shifter_1_out), .b(ID_PC), .out(adder_2_out));  // open: cin, cout
  Comparator #(.width(32), .mode("unsigned")) comparator_1 (
    .a({32{1'b1}}), .b(multiplexer_8_out), .gt(comparator_1_gt));  // open: eq, lt
  // Probe on M_PC[11:0]
  D_Flip_Flop #(.trigger("high"), .Pre_Clr_Positions("LEGACY"), .NegatePresetClear("false"), .enable("true"), .NewFFLayout("false")) d_ff_4 (.Q(d_ff_4_q));  // open: clk, D, Qn, preset, en, reset
  // Probe on 13'h16
  Adder #(.width(32)) adder_3 (.a(shifter_2_out), .b(ID_PC), .out(adder_3_out));  // open: cin, cout
  Adder #(.width(32)) adder_4 (.a(ID_PC), .b(shifter_3_out), .out(adder_4_out));  // open: cin, cout
  // Probe on WB_PC[11:0]
  Comparator #(.width(13), .mode("twosComplement")) comparator_2 (
    .a(CNT_num), .b(13'h16), .eq(comparator_2_eq), .lt(comparator_2_lt));  // open: gt
  Clock #(.highDuration(1), .lowDuration(1)) clock_4 (.out(clock_4_out));
  not not_4 (not_4_out, halt);
  ID_EX id_ex_1 (
    .RegWrite(\单周期硬布线控制器_1_regwrite ), .R1(regifile_1_r1), .R2(regifile_1_r2), .rd(ID_IR[11:7]),
    .Imm(multiplexer_4_out), .PC(ID_PC), .RegWrite_2(id_ex_1_regwrite_2), .R1_2(EX_RS), .R2_2(EX_RT),
    .rd_2(id_ex_1_rd_2), .Imm_2(id_ex_1_imm_2), .PC_2(EX_PC), .CLK(CLK), .MemToReg(\单周期硬布线控制器_1_memtoreg ),
    .MemToReg_2(id_ex_1_memtoreg_2), .MemWrite(\单周期硬布线控制器_1_memwrite ), .MemWrite_2(id_ex_1_memwrite_2),
    .AluOP(\单周期硬布线控制器_1_alu_op ), .AluOP_2(id_ex_1_aluop_2), .Bne(Bne), .Bne_2(id_ex_1_bne_2),
    .AluSrc(\单周期硬布线控制器_1_alu_src ), .AluSrc_2(id_ex_1_alusrc_2), .Beq(Beq), .Beq_2(id_ex_1_beq_2), .Bge(Bge),
    .Bge_2(id_ex_1_bge_2), .Auipc(Auipc), .Auipc_2(id_ex_1_auipc_2), .Byte(Byte), .Byte_2(id_ex_1_byte_2),
    .Jalr(Jalr), .Jalr_2(id_ex_1_jalr_2), .Jal(Jal), .Jal_2(id_ex_1_jal_2), .BImm(adder_3_out),
    .BImm_2(id_ex_1_bimm_2), .JImm(adder_4_out), .JImm_2(id_ex_1_jimm_2), .UImm(adder_2_out),
    .UImm_2(id_ex_1_uimm_2), .Ecall(Ecall), .Ecall_2(id_ex_1_ecall_2), .IR(ID_IR), .IR_2(EX_IR),
    .Flush(Flush), .En(not_4_out), .RsFoward(ID_RsFoward), .RsFoward_2(EX_RsFoward), .RtFoward(ID_RtFoward),
    .RtFoward_2(EX_RtFoward), .Uert(Uert), .Uert_2(EX_Uert));  // open: PredictJump, PredictJump_2
  or or_7 (BranchTaken, Inte, comparator_1_gt, EX_Uert);
  nand nand_1 (nand_1_out, d_ff_4_q, comparator_2_eq);
  Counter #(.width(13), .max('h1fff), .ongoal("stay"), .trigger("rising"), .behavior("old")) counter_1 (
    .count(comparator_2_lt), .Q(CNT_num), .clk(clock_4_out));  // open: load, D, carry, clr, preset
  or or_8 (or_8_out, id_ex_1_jalr_2, id_ex_1_jal_2);
  Multiplexer #(.select(2), .width(32), .disabled("Z"), .enable("false")) multiplexer_5 (
    .in0(NextPCWithoutInt), .in1(32'h30ac), .in2(32'h3150), .in3(32'h31f4), .out(multiplexer_5_out),
    .sel(IR_Id));
  Priority_Encoder #(.select(2), .disabled("Z")) priority_encoder_1 (
    .in0(1'b0), .in1(IR1_q), .in2(IR2_q), .in3(IR3_q), .out(IR_Id), .gs(priority_encoder_1_gs));  // open: en_out, en_in
  assign CLK = nand_1_out ? clock_4_out : 1'bz;  // Controlled_Buffer controlled_buffer_1
  Multiplexer #(.select(1), .width(32), .disabled("Z"), .enable("false")) multiplexer_6 (
    .in0({32{1'b1}}), .in1(and_7_out), .out(multiplexer_6_out), .sel(id_ex_1_jalr_2));
  or or_9 (JJump, id_ex_1_jal_2, id_ex_1_jalr_2);
  and and_6 (Inte, priority_encoder_1_gs, IE);
  not not_5 (not_5_out, Inte);
  Demultiplexer #(.select(2), .width(1), .tristate("false"), .disabled("Z"), .enable("false")) demultiplexer_1 (
    .out1(ResetIR1), .out2(ResetIR2), .out3(ResetIR3), .in(EX_Uert), .sel(register_1_q));  // open: out0
  Register #(.width(2), .trigger("rising"), .Select("low")) register_1 (
    .D(IR_Id), .en(Inte), .Q(register_1_q), .clk(CLK));  // open: clr
  Pull_Resistor #(.pull(1)) pull_resistor_1 (.node(CLK));
  Multiplexer #(.select(1), .width(32), .disabled("Z"), .enable("false")) multiplexer_7 (
    .in0(multiplexer_6_out), .in1(id_ex_1_bimm_2), .out(multiplexer_7_out), .sel(Branch));
  Multiplexer #(.select(1), .width(32), .disabled("Z"), .enable("false")) multiplexer_8 (
    .in0(multiplexer_7_out), .in1(id_ex_1_jimm_2), .out(multiplexer_8_out), .sel(id_ex_1_jal_2));
  Multiplexer #(.select(1), .width(32), .disabled("Z"), .enable("false")) multiplexer_9 (
    .in0(NextPCWithoutInt), .in1(multiplexer_5_out), .out(multiplexer_9_out), .sel(Inte));
  Comparator #(.width(4), .mode("unsigned")) comparator_3 (
    .a(id_ex_1_aluop_2), .b(4'b1100), .eq(comparator_3_eq));  // open: gt, lt
  Comparator #(.width(4), .mode("unsigned")) comparator_4 (
    .a(id_ex_1_aluop_2), .b(4'b1011), .eq(comparator_4_eq));  // open: gt, lt
  Comparator #(.width(32), .mode("twosComplement")) comparator_5 (
    .a(EX_RE_RS), .b(32'h22), .eq(comparator_5_eq));  // open: gt, lt
  nand nand_2 (nand_2_out, comparator_5_eq, id_ex_1_ecall_2);
  Multiplexer #(.select(1), .width(32), .disabled("Z"), .enable("false")) multiplexer_10 (
    .in0(EX_RE_RT), .in1(id_ex_1_imm_2), .out(multiplexer_10_out), .sel(id_ex_1_alusrc_2));
  not not_6 (not_6_out, Equ);
  Multiplexer #(.select(1), .width(32), .disabled("Z"), .enable("false")) multiplexer_11 (
    .in0(multiplexer_9_out), .in1(EPC), .out(NextPC), .sel(EX_Uert));
  Comparator #(.width(16), .mode("twosComplement")) comparator_6 (
    .a(\总周期数 ), .b({16{1'b0}}), .eq(comparator_6_eq));  // open: gt, lt
  or or_10 (or_10_out, comparator_3_eq, comparator_4_eq);
  ALU alu_1 (
    .X(EX_RE_RS), .Y(multiplexer_10_out), .AluOP(id_ex_1_aluop_2), .Equal(Equ), .Result(alu_1_result),
    .out_4(Geq), .out_6(alu_1_out_6));  // open: Result_2
  assign and_7_out = 32'hfffe & alu_1_result;  // AND_Gate and_7, 32 bits wide
  and and_8 (and_8_out, id_ex_1_beq_2, Equ);
  and and_9 (and_9_out, id_ex_1_bne_2, not_6_out);
  and and_10 (and_10_out, id_ex_1_bge_2, Geq);
  or or_11 (Branch, and_10_out, and_9_out, and_8_out);
  or or_12 (or_12_out, EX_Uert, Inte, comparator_6_eq);
  and and_11 (and_11_out, Inte, ~ME_Uert);  // AND_Gate
  Multiplexer #(.select(2), .width(32), .disabled("Z"), .enable("false")) multiplexer_12 (
    .in0(EX_RS), .in1(RDin), .in2(multiplexer_17_out), .out(EX_RE_RS), .sel(EX_RsFoward));  // open: in3
  Multiplexer #(.select(2), .width(32), .disabled("Z"), .enable("false")) multiplexer_13 (
    .in0(EX_RT), .in1(RDin), .in2(multiplexer_17_out), .out(EX_RE_RT), .sel(EX_RtFoward));  // open: in3
  Register #(.width(32), .trigger("rising"), .Select("low")) register_2 (
    .D(EX_RE_RT), .en(not_7_out), .Q(LedData), .clk(CLK));  // open: clr
  not not_7 (not_7_out, nand_2_out);
  not not_8 (not_8_out, halt);
  Register #(.width(1), .trigger("rising"), .Select("low")) u_IE (
    .D(not_5_out), .en(or_12_out), .Q(IE), .clk(CLK));  // open: clr
  Register #(.width(32), .trigger("rising"), .Select("low")) u_EPC (
    .D(EX_PC), .en(and_11_out), .Q(EPC), .clk(CLK));  // open: clr
  EX_MEM ex_mem_1 (
    .AluResult(alu_1_result), .WriteData(EX_RE_RT), .rd(id_ex_1_rd_2), .AluResult_2(ex_mem_1_aluresult_2),
    .WriteData_2(MDin), .rd_2(ex_mem_1_rd_2), .CLK(CLK), .RegWrite(id_ex_1_regwrite_2),
    .RegWrite_2(ex_mem_1_regwrite_2), .MemToReg(id_ex_1_memtoreg_2), .MemToReg_2(ex_mem_1_memtoreg_2),
    .MemWrite(id_ex_1_memwrite_2), .MemWrite_2(MemWrite), .Byte(id_ex_1_byte_2), .Byte_2(ex_mem_1_byte_2),
    .Ecall(id_ex_1_ecall_2), .Ecall_2(ex_mem_1_ecall_2), .ShouldHalt(nand_2_out),
    .ShouldHalt_2(ex_mem_1_shouldhalt_2), .Auipc(id_ex_1_auipc_2), .Auipc_2(ex_mem_1_auipc_2),
    .Less(alu_1_out_6), .Less_2(ex_mem_1_less_2), .Slt(or_10_out), .Slt_2(ex_mem_1_slt_2),
    .Jal_Jalr(or_8_out), .Jal_Jalr_2(ex_mem_1_jal_jalr_2), .PC(EX_PC), .PC_2(M_PC), .UImm(id_ex_1_uimm_2),
    .UImm_2(ex_mem_1_uimm_2), .IR(EX_IR), .IR_2(MEM_IR), .En(not_8_out), .Flush(EX_Flush), .Uert_2(ME_Uert),
    .Uert(EX_Uert));
  assign bit_extender_6_out = {{31{1'b0}}, ex_mem_1_less_2};  // Bit_Extender bit_extender_6
  or or_13 (or_13_out, Inte, and_12_out);
  and and_12 (and_12_out, CLK, EX_Flush);
  MIPS_RAM mips_ram_1 (
    .\字节地址 (ex_mem_1_aluresult_2[11:0]), .Din(MDin), .DataOut(mips_ram_1_dataout), .CLK(CLK), .WE(MemWrite),
    .Mode(multiplexer_14_out));
  Multiplexer #(.select(1), .width(2), .disabled("Z"), .enable("false")) multiplexer_14 (
    .in0(2'b00), .in1(2'b01), .out(multiplexer_14_out), .sel(ex_mem_1_byte_2));
  Multiplexer #(.select(1), .width(32), .disabled("Z"), .enable("false")) multiplexer_15 (
    .in0(ex_mem_1_aluresult_2), .in1(bit_extender_6_out), .out(multiplexer_15_out), .sel(ex_mem_1_slt_2));
  Adder #(.width(32)) adder_5 (.a(M_PC), .b(32'h4), .out(adder_5_out));  // open: cin, cout
  Comparator #(.width(16), .mode("twosComplement")) comparator_7 (
    .a(16'h23b), .b(\总周期数 ), .eq(comparator_7_eq));  // open: gt, lt
  Comparator #(.width(16), .mode("twosComplement")) comparator_8 (
    .a(\总周期数 ), .b(16'h1), .eq(comparator_8_eq));  // open: gt, lt
  Comparator #(.width(16), .mode("twosComplement")) comparator_9 (
    .a(\总周期数 ), .b(16'h4), .eq(comparator_9_eq));  // open: gt, lt
  Comparator #(.width(16), .mode("twosComplement")) comparator_10 (
    .a(\总周期数 ), .b(16'h7), .eq(comparator_10_eq));  // open: gt, lt
  T_Flip_Flop #(.trigger("rising"), .Pre_Clr_Positions("ABOVE_BELOW"), .NegatePresetClear("false"), .enable("false"), .NewFFLayout("true")) t_ff_1 (
    .clk(or_13_out), .T(1'b1), .Q(EX_Flush));  // open: Qn, preset, reset
  Multiplexer #(.select(1), .width(32), .disabled("Z"), .enable("false")) multiplexer_16 (
    .in0(multiplexer_15_out), .in1(adder_5_out), .out(multiplexer_16_out), .sel(ex_mem_1_jal_jalr_2));
  or or_14 (or_14_out, comparator_7_eq, comparator_8_eq);
  Pull_Resistor #(.pull(0)) pull_resistor_2 (.node(IRA));
  assign IRA = or_14_out ? ~CLK : 1'bz;  // Controlled_Inverter controlled_inverter_1
  Pull_Resistor #(.pull(0)) pull_resistor_3 (.node(IRB));
  assign IRB = comparator_9_eq ? ~CLK : 1'bz;  // Controlled_Inverter controlled_inverter_2
  Pull_Resistor #(.pull(0)) pull_resistor_4 (.node(IRC));
  assign IRC = comparator_10_eq ? ~CLK : 1'bz;  // Controlled_Inverter controlled_inverter_3
  \气泡_重定向处理逻辑  \u_气泡_重定向处理逻辑_1  (
    .RsUsed(\单周期硬布线控制器_1_rsused ), .rs(multiplexer_2_out), .RtUsed(\单周期硬布线控制器_1_rtused ),
    .rt(multiplexer_3_out), .MEM_RegWrite(ex_mem_1_regwrite_2), .MEM_WriteReg_V(ex_mem_1_rd_2),
    .EX_WriteReg_V(id_ex_1_rd_2), .BranchTaken(BranchTaken), .Stall(stall), .PC_EN(\气泡_重定向处理逻辑_1_pc_en ),
    .IF_ID_EN(\气泡_重定向处理逻辑_1_if_id_en ), .IF_ID_CLR(if_id_1_p5), .ID_EX_CLR(Flush),
    .EX_MemToReg(id_ex_1_memtoreg_2), .EX_RegWrite(id_ex_1_regwrite_2), .RsFoward(ID_RsFoward),
    .RtFoward(ID_RtFoward));  // open: Flush, LoadUse
  Multiplexer #(.select(1), .width(32), .disabled("Z"), .enable("false")) multiplexer_17 (
    .in0(multiplexer_16_out), .in1(ex_mem_1_uimm_2), .out(multiplexer_17_out), .sel(ex_mem_1_auipc_2));
  not not_9 (not_9_out, halt);
  ME_WB me_wb_1 (
    .RegWrite(ex_mem_1_regwrite_2), .MemToReg(ex_mem_1_memtoreg_2), .AluResult(multiplexer_17_out),
    .RD(mips_ram_1_dataout), .rd_2(ex_mem_1_rd_2), .RegWrite_2(RegWrite), .MemToReg_2(me_wb_1_memtoreg_2),
    .AluResult_2(me_wb_1_aluresult_2), .RD_3(me_wb_1_rd_3), .rd_4(me_wb_1_rd_4), .CLK(CLK),
    .ShouldHalt(ex_mem_1_shouldhalt_2), .ShouldHalt_2(me_wb_1_shouldhalt_2), .Ecall(ex_mem_1_ecall_2),
    .Ecall_2(me_wb_1_ecall_2), .PC(M_PC), .PC_2(WB_PC), .IR(MEM_IR), .IR_2(WB_IR), .En(not_9_out));
  or or_15 (CSIR1, IR1, IRA);
  Multiplexer #(.select(1), .width(32), .disabled("Z"), .enable("false")) multiplexer_18 (
    .in0(me_wb_1_aluresult_2), .in1(me_wb_1_rd_3), .out(RDin), .sel(me_wb_1_memtoreg_2));
  or or_16 (CSIR2, IR2, IRB);
  or or_17 (CSIR3, IR3, IRC);
  and and_13 (and_13_out, ~halt, CLK);  // AND_Gate
  and and_14 (and_14_out, ~halt, CLK);  // AND_Gate
  D_Flip_Flop #(.trigger("falling"), .Pre_Clr_Positions("ABOVE_BELOW"), .NegatePresetClear("false"), .enable("true"), .NewFFLayout("true")) d_ff_5 (
    .clk(CLK), .D(me_wb_1_shouldhalt_2), .Q(halt), .en(me_wb_1_ecall_2), .reset(Go));  // open: Qn, preset
  Counter #(.width(16), .max('hffff), .ongoal("wrap"), .trigger("rising"), .behavior("new")) counter_2 (
    .count(Branch), .Q(\条件分支成功数 ), .clk(and_13_out), .clr(RST));  // open: load, D, carry, preset, down
  Counter #(.width(16), .max('hffff), .ongoal("wrap"), .trigger("rising"), .behavior("new")) counter_3 (
    .count(Flush), .Q(\插入气泡数 ), .clk(and_14_out), .clr(RST));  // open: load, D, carry, preset, down
  Counter #(.width(16), .max('hffff), .ongoal("wrap"), .trigger("rising"), .behavior("new")) counter_4 (
    .count(JJump), .Q(\无条件分支数 ), .clk(and_15_out), .clr(RST));  // open: load, D, carry, preset, down
  and and_15 (and_15_out, ~halt, CLK);  // AND_Gate
  Counter #(.width(16), .max('hffff), .ongoal("wrap"), .trigger("rising"), .behavior("new")) counter_5 (
    .count(CLK), .Q(\总周期数 ), .clk(and_16_out), .clr(RST));  // open: load, D, carry, preset, down
  and and_16 (and_16_out, ~halt, CLK);  // AND_Gate
  Counter #(.width(16), .max('hffff), .ongoal("wrap"), .trigger("rising"), .behavior("new")) counter_6 (
    .count(stall), .Q(\LoadUse次数 ), .clk(and_17_out), .clr(RST));  // open: load, D, carry, preset, down
  and and_17 (and_17_out, ~halt, CLK);  // AND_Gate

  // Other names for the same wires on the sheet: MEM_PC[31:0] = M_PC; PC[31:0] = IF_PC

  // Notes on the sheet:
  //   中断源
  //   时空图监测，可删除
  //   中断等待指示
  //   数码管输出
  //   指令探针
  //   指令存储器
  //   contents of rom_1 (hex, n*v repeats v):
  //   7d000113 100413 1f41993 41f9d993 433 c00913 800b13 140413 f47413 800293 100313 499993 89e9b3 1300533
  //   2200893 73 406282b3 fe0294e3 140413 f00f93 1f47433 1c41413 800293 100313 49d993 89e9b3 1300533
  //   2200893 73 406282b3 fe0294e3 1c45413 406b0b33 b0463 f95ff06f 2b3 fff2c293 1029293 fff2e293 500533
  //   2200893 73 f5dff06f 1112023 410113 a12023 410113 812023 410113 1312023 410113 1412023 410113 1512023
  //   410113 1612023 410113 100b13 300a13 100a93 1600433 441413 14469b3 1300533 2200893 73 fe0416e3
  //   415a0a33 fe0a10e3 ffc10113 12b03 ffc10113 12a83 ffc10113 12a03 ffc10113 12983 ffc10113 12403
  //   ffc10113 12503 ffc10113 12883 200073 1112023 410113 a12023 410113 812023 410113 1312023 410113
  //   1412023 410113 1512023 410113 1612023 410113 200b13 300a13 100a93 1600433 441413 14469b3 1300533
  //   2200893 73 fe0416e3 415a0a33 fe0a10e3 ffc10113 12b03 ffc10113 12a83 ffc10113 12a03 ffc10113 12983
  //   ffc10113 12403 ffc10113 12503 ffc10113 12883 200073 1112023 410113 a12023 410113 812023 410113
  //   1312023 410113 1412023 410113 1512023 410113 1612023 410113 300b13 300a13 100a93 1600433 441413
  //   14469b3 1300533 2200893 73 fe0416e3 415a0a33 fe0a10e3 ffc10113 12b03 ffc10113 12a83 ffc10113 12a03
  //   ffc10113 12983 ffc10113 12403 ffc10113 12503 ffc10113 12883 200073
  //   指令字
  //   JAL
  //   JALR
  //   Beq
  //   Bne
  //   MemToReg
  //   MemWrite
  //   AluOP
  //   AluSrcB
  //   RegWrite
  //   Reset 
  //   Reset 
  //   Reset 
  //   控制位
  //   流水调试日志用
  //   暂停节拍，不能为0
  //   戳工具置1进入计数暂停模式，ctrl+k时钟自动运行到对应节拍暂停
  //   ctrl+k关闭时钟连续运行，将控制位置零，进入单步调试模式调试
  //   可计数暂停的时钟源
  //   为方便自动评测，需要输出流水线各段保存的PC值，注意是PC不是PC+4，另外ID段寄存器写入信息，Mem段内存写入信息也要输出
  //   单级中断测试信号模拟器
  //   数据存储器
endmodule

module BTB (
  input  J_Branch,
  input  EX_Branch,
  input  EX_BranchTaken,
  input  CLK,
  input  [31:0] EX_BranchAddr,
  input  [31:0] EX_PC,
  input  [31:0] PC,
  output PredictJump,
  output [31:0] JumpAddr
);

  wire and_17_out, and_18_out, and_19_out, and_20_out, and_21_out, and_22_out, and_23_out, and_24_out,
       and_33_out, and_34_out, and_35_out, and_36_out, and_37_out, and_38_out, and_39_out, and_40_out,
       comparator_1_eq, comparator_2_eq, comparator_3_eq, comparator_4_eq, comparator_5_eq, comparator_6_eq,
       comparator_7_eq, comparator_8_eq, comparator_9_eq, comparator_10_eq, comparator_11_eq,
       comparator_12_eq, comparator_13_eq, comparator_14_eq, comparator_15_eq, comparator_16_eq,
       demultiplexer_1_out0, demultiplexer_1_out1, demultiplexer_1_out2, demultiplexer_1_out3,
       demultiplexer_1_out4, demultiplexer_1_out5, demultiplexer_1_out6, demultiplexer_1_out7,
       demultiplexer_2_out0, demultiplexer_2_out1, demultiplexer_2_out2, demultiplexer_2_out3,
       demultiplexer_2_out4, demultiplexer_2_out5, demultiplexer_2_out6, demultiplexer_2_out7, H0, H1, H2,
       H3, H4, H5, H6, H7, history_1_predict, history_2_predict, history_3_predict, history_4_predict,
       history_5_predict, history_6_predict, history_7_predict, history_8_predict, not_1_out, not_2_out,
       not_3_out, not_4_out, not_5_out, not_6_out, not_7_out, not_8_out, not_9_out, not_10_out, or_1_out,
       or_2_out, or_3_out, or_4_out, or_5_out, or_6_out, or_7_out, or_8_out, or_9_out, priority_encoder_1_gs,
       R0, R1, R2, R3, R4, R5, R6, R7, V0, V1, V2, V3, V4, V5, V6, V7, W0, W1, W2, W3, W4, W5, W6, W7;
  wire [2:0] max_with_id_1_id, max_with_id_2_id, max_with_id_3_id, max_with_id_4_id, max_with_id_5_id,
       max_with_id_6_id, max_with_id_7_id, multiplexer_1_out, priority_encoder_1_out;
  wire [15:0] max_with_id_1_val, max_with_id_2_val, max_with_id_3_val, max_with_id_4_val, max_with_id_5_val,
       max_with_id_6_val, T0, T1, T2, T3, T4, T5, T6, T7;
  wire [31:0] P0, P1, P2, P3, P4, P5, P6, P7;

  MAX_WITH_ID max_with_id_1 (
    .Val1(T0), .Val2(T1), .Id1(3'b000), .Id2(3'b001), .Val(max_with_id_1_val), .Id(max_with_id_1_id));
  MAX_WITH_ID max_with_id_2 (
    .Val1(T2), .Val2(T3), .Id1(3'b010), .Id2(3'b011), .Val(max_with_id_2_val), .Id(max_with_id_2_id));
  MAX_WITH_ID max_with_id_3 (
    .Val1(T4), .Val2(T5), .Id1(3'b100), .Id2(3'b101), .Val(max_with_id_3_val), .Id(max_with_id_3_id));
  MAX_WITH_ID max_with_id_4 (
    .Val1(T6), .Val2(T7), .Id1(3'b110), .Id2(3'b111), .Val(max_with_id_4_val), .Id(max_with_id_4_id));
  JumpReg J0 (
    .Write(W0), .Valid(V0), .EX_PC(EX_PC), .PC(P0), .Time(T0), .EX_BranchAddr(EX_BranchAddr),
    .JumpAddr(JumpAddr), .CLK(CLK), .Hit(H0));
  JumpReg J2 (
    .Write(W2), .Valid(V2), .EX_PC(EX_PC), .PC(P2), .Time(T2), .EX_BranchAddr(EX_BranchAddr),
    .JumpAddr(JumpAddr), .CLK(CLK), .Hit(H2));
  JumpReg J4 (
    .Write(W4), .Valid(V4), .EX_PC(EX_PC), .PC(P4), .Time(T4), .EX_BranchAddr(EX_BranchAddr),
    .JumpAddr(JumpAddr), .CLK(CLK), .Hit(H4));
  JumpReg J6 (
    .Write(W6), .Valid(V6), .EX_PC(EX_PC), .PC(P6), .Time(T6), .EX_BranchAddr(EX_BranchAddr),
    .JumpAddr(JumpAddr), .CLK(CLK), .Hit(H6));
  not not_1 (not_1_out, V0);
  not not_2 (not_2_out, V1);
  not not_3 (not_3_out, V2);
  not not_4 (not_4_out, V3);
  not not_5 (not_5_out, V4);
  not not_6 (not_6_out, V5);
  not not_7 (not_7_out, V6);
  not not_8 (not_8_out, V7);
  MAX_WITH_ID max_with_id_5 (
    .Val1(max_with_id_1_val), .Val2(max_with_id_2_val), .Id1(max_with_id_1_id), .Id2(max_with_id_2_id),
    .Val(max_with_id_5_val), .Id(max_with_id_5_id));
  MAX_WITH_ID max_with_id_6 (
    .Val1(max_with_id_3_val), .Val2(max_with_id_4_val), .Id1(max_with_id_3_id), .Id2(max_with_id_4_id),
    .Val(max_with_id_6_val), .Id(max_with_id_6_id));
  Multiplexer #(.select(1), .width(3), .disabled("Z"), .enable("false")) multiplexer_1 (
    .in0(3'b000), .in1(priority_encoder_1_out), .out(multiplexer_1_out), .sel(priority_encoder_1_gs));
  Priority_Encoder #(.select(3), .disabled("Z")) priority_encoder_1 (
    .in0(not_1_out), .in1(not_2_out), .in2(not_3_out), .in3(not_4_out), .in4(not_5_out), .in5(not_6_out),
    .in6(not_7_out), .in7(not_8_out), .out(priority_encoder_1_out), .gs(priority_encoder_1_gs));  // open: en_out, en_in
  MAX_WITH_ID max_with_id_7 (
    .Val1(max_with_id_5_val), .Val2(max_with_id_6_val), .Id1(max_with_id_5_id), .Id2(max_with_id_6_id),
    .Id(max_with_id_7_id));  // open: Val
  Demultiplexer #(.select(3), .width(1), .tristate("false"), .disabled("Z"), .enable("false")) demultiplexer_1 (
    .out0(demultiplexer_1_out0), .out1(demultiplexer_1_out1), .out2(demultiplexer_1_out2),
    .out3(demultiplexer_1_out3), .out4(demultiplexer_1_out4), .out5(demultiplexer_1_out5),
    .out6(demultiplexer_1_out6), .out7(demultiplexer_1_out7), .in(priority_encoder_1_gs),
    .sel(multiplexer_1_out));
  Demultiplexer #(.select(3), .width(1), .tristate("false"), .disabled("Z"), .enable("false")) demultiplexer_2 (
    .out0(demultiplexer_2_out0), .out1(demultiplexer_2_out1), .out2(demultiplexer_2_out2),
    .out3(demultiplexer_2_out3), .out4(demultiplexer_2_out4), .out5(demultiplexer_2_out5),
    .out6(demultiplexer_2_out6), .out7(demultiplexer_2_out7), .in(not_9_out), .sel(max_with_id_7_id));
  not not_9 (not_9_out, priority_encoder_1_gs);
  JumpReg J1 (
    .Write(W1), .Valid(V1), .EX_PC(EX_PC), .PC(P1), .Time(T1), .EX_BranchAddr(EX_BranchAddr),
    .JumpAddr(JumpAddr), .CLK(CLK), .Hit(H1));
  JumpReg J3 (
    .Write(W3), .Valid(V3), .EX_PC(EX_PC), .PC(P3), .Time(T3), .EX_BranchAddr(EX_BranchAddr),
    .JumpAddr(JumpAddr), .CLK(CLK), .Hit(H3));
  JumpReg J5 (
    .Write(W5), .Valid(V5), .EX_PC(EX_PC), .PC(P5), .Time(T5), .EX_BranchAddr(EX_BranchAddr),
    .JumpAddr(JumpAddr), .CLK(CLK), .Hit(H5));
  JumpReg J7 (
    .Write(W7), .Valid(V7), .EX_PC(EX_PC), .PC(P7), .Time(T7), .EX_BranchAddr(EX_BranchAddr),
    .JumpAddr(JumpAddr), .CLK(CLK), .Hit(H7));
  Comparator #(.width(32), .mode("unsigned")) comparator_1 (.a(EX_PC), .b(P0), .eq(comparator_1_eq));  // open: gt, lt
  Comparator #(.width(32), .mode("unsigned")) comparator_2 (.a(P0), .b(PC), .eq(comparator_2_eq));  // open: gt, lt
  Comparator #(.width(32), .mode("unsigned")) comparator_3 (.a(EX_PC), .b(P2), .eq(comparator_3_eq));  // open: gt, lt
  Comparator #(.width(32), .mode("unsigned")) comparator_4 (.a(P2), .b(PC), .eq(comparator_4_eq));  // open: gt, lt
  Comparator #(.width(32), .mode("unsigned")) comparator_5 (.a(EX_PC), .b(P4), .eq(comparator_5_eq));  // open: gt, lt
  Comparator #(.width(32), .mode("unsigned")) comparator_6 (.a(P4), .b(PC), .eq(comparator_6_eq));  // open: gt, lt
  Comparator #(.width(32), .mode("unsigned")) comparator_7 (.a(EX_PC), .b(P6), .eq(comparator_7_eq));  // open: gt, lt
  Comparator #(.width(32), .mode("unsigned")) comparator_8 (.a(P6), .b(PC), .eq(comparator_8_eq));  // open: gt, lt
  or or_1 (or_1_out, R0, R1, R2, R3, R4, R5, R6, R7);
  or or_2 (or_2_out, demultiplexer_1_out0, demultiplexer_2_out0);
  or or_3 (or_3_out, demultiplexer_1_out1, demultiplexer_2_out1);
  or or_4 (or_4_out, demultiplexer_1_out2, demultiplexer_2_out2);
  or or_5 (or_5_out, demultiplexer_1_out3, demultiplexer_2_out3);
  or or_6 (or_6_out, demultiplexer_1_out4, demultiplexer_2_out4);
  or or_7 (or_7_out, demultiplexer_1_out5, demultiplexer_2_out5);
  or or_8 (or_8_out, demultiplexer_1_out6, demultiplexer_2_out6);
  or or_9 (or_9_out, demultiplexer_1_out7, demultiplexer_2_out7);
  and and_1 (R0, comparator_1_eq, V0);
  and and_2 (H0, V0, comparator_2_eq);
  and and_3 (R2, comparator_3_eq, V2);
  and and_4 (H2, V2, comparator_4_eq);
  and and_5 (R4, comparator_5_eq, V4);
  and and_6 (H4, V4, comparator_6_eq);
  and and_7 (R6, comparator_7_eq, V6);
  and and_8 (H6, V6, comparator_8_eq);
  not not_10 (not_10_out, or_1_out);
  and and_9 (W0, or_2_out, EX_Branch, not_10_out);
  and and_10 (W1, or_3_out, EX_Branch, not_10_out);
  and and_11 (W2, or_4_out, EX_Branch, not_10_out);
  and and_12 (W3, or_5_out, EX_Branch, not_10_out);
  and and_13 (W4, or_6_out, EX_Branch, not_10_out);
  and and_14 (W5, or_7_out, EX_Branch, not_10_out);
  and and_15 (W6, or_8_out, EX_Branch, not_10_out);
  and and_16 (W7, or_9_out, EX_Branch, not_10_out);
  Comparator #(.width(32), .mode("unsigned")) comparator_9 (.a(EX_PC), .b(P1), .eq(comparator_9_eq));  // open: gt, lt
  Comparator #(.width(32), .mode("unsigned")) comparator_10 (.a(P1), .b(PC), .eq(comparator_10_eq));  // open: gt, lt
  Comparator #(.width(32), .mode("unsigned")) comparator_11 (.a(EX_PC), .b(P3), .eq(comparator_11_eq));  // open: gt, lt
  Comparator #(.width(32), .mode("unsigned")) comparator_12 (.a(P3), .b(PC), .eq(comparator_12_eq));  // open: gt, lt
  Comparator #(.width(32), .mode("unsigned")) comparator_13 (.a(EX_PC), .b(P5), .eq(comparator_13_eq));  // open: gt, lt
  Comparator #(.width(32), .mode("unsigned")) comparator_14 (.a(P5), .b(PC), .eq(comparator_14_eq));  // open: gt, lt
  Comparator #(.width(32), .mode("unsigned")) comparator_15 (.a(EX_PC), .b(P7), .eq(comparator_15_eq));  // open: gt, lt
  Comparator #(.width(32), .mode("unsigned")) comparator_16 (.a(P7), .b(PC), .eq(comparator_16_eq));  // open: gt, lt
  and and_17 (and_17_out, EX_Branch, R0);
  and and_18 (and_18_out, EX_Branch, R1);
  and and_19 (and_19_out, EX_Branch, R2);
  and and_20 (and_20_out, EX_Branch, R3);
  and and_21 (and_21_out, EX_Branch, R4);
  and and_22 (and_22_out, EX_Branch, R5);
  and and_23 (and_23_out, EX_Branch, R6);
  and and_24 (and_24_out, EX_Branch, R7);
  and and_25 (R1, comparator_9_eq, V1);
  and and_26 (H1, V1, comparator_10_eq);
  and and_27 (R3, comparator_11_eq, V3);
  and and_28 (H3, V3, comparator_12_eq);
  and and_29 (R5, comparator_13_eq, V5);
  and and_30 (H5, V5, comparator_14_eq);
  and and_31 (R7, comparator_15_eq, V7);
  and and_32 (H7, V7, comparator_16_eq);
  History history_1 (
    .BranchTaken(EX_BranchTaken), .Predict(history_1_predict), .En(and_17_out), .CLK(CLK), .J_Branch(J_Branch));
  History history_2 (
    .BranchTaken(EX_BranchTaken), .Predict(history_2_predict), .En(and_18_out), .CLK(CLK), .J_Branch(J_Branch));
  History history_3 (
    .BranchTaken(EX_BranchTaken), .Predict(history_3_predict), .En(and_19_out), .CLK(CLK), .J_Branch(J_Branch));
  History history_4 (
    .BranchTaken(EX_BranchTaken), .Predict(history_4_predict), .En(and_20_out), .CLK(CLK), .J_Branch(J_Branch));
  History history_5 (
    .BranchTaken(EX_BranchTaken), .Predict(history_5_predict), .En(and_21_out), .CLK(CLK), .J_Branch(J_Branch));
  History history_6 (
    .BranchTaken(EX_BranchTaken), .Predict(history_6_predict), .En(and_22_out), .CLK(CLK), .J_Branch(J_Branch));
  History history_7 (
    .BranchTaken(EX_BranchTaken), .Predict(history_7_predict), .En(and_23_out), .CLK(CLK), .J_Branch(J_Branch));
  History history_8 (
    .BranchTaken(EX_BranchTaken), .Predict(history_8_predict), .En(and_24_out), .CLK(CLK), .J_Branch(J_Branch));
  and and_33 (and_33_out, history_1_predict, H0);
  and and_34 (and_34_out, history_2_predict, H1);
  and and_35 (and_35_out, history_3_predict, H2);
  and and_36 (and_36_out, history_4_predict, H3);
  and and_37 (and_37_out, history_5_predict, H4);
  and and_38 (and_38_out, history_6_predict, H5);
  and and_39 (and_39_out, history_7_predict, H6);
  and and_40 (and_40_out, history_8_predict, H7);
  or or_10 (PredictJump, and_33_out, and_34_out, and_35_out, and_36_out, and_37_out, and_38_out, and_39_out, and_40_out);

  // Other names for the same wires on the sheet: EX_J_Branch = J_Branch
endmodule

module JumpReg (
  input  [31:0] EX_PC,
  input  [31:0] EX_BranchAddr,
  input  Write,
  input  CLK,
  input  Hit,
  output [15:0] Time,
  output [31:0] JumpAddr,
  output [31:0] PC,
  output Valid
);

  wire d_ff_1_q, or_1_out;
  wire [31:0] register_3_q;

  Register #(.width(1), .trigger("rising"), .Select("low")) register_1 (
    .D(1'b1), .en(Write), .Q(Valid), .clk(CLK));  // open: clr
  Register #(.width(32), .trigger("rising"), .Select("low")) register_2 (
    .D(EX_PC), .en(Write), .Q(PC), .clk(CLK));  // open: clr
  Counter #(.width(16), .max('hffff), .ongoal("wrap"), .trigger("rising"), .behavior("new")) counter_1 (
    .Q(Time), .clk(CLK), .clr(d_ff_1_q));  // open: load, D, count, carry, preset, down
  D_Flip_Flop #(.trigger("rising"), .Pre_Clr_Positions("ABOVE_BELOW"), .NegatePresetClear("false"), .enable("false"), .NewFFLayout("false")) d_ff_1 (
    .clk(CLK), .D(or_1_out), .Q(d_ff_1_q));  // open: Qn, preset, reset
  or or_1 (or_1_out, Write, Hit);
  Register #(.width(32), .trigger("rising"), .Select("low")) register_3 (
    .D(EX_BranchAddr), .en(Write), .Q(register_3_q), .clk(CLK));  // open: clr
  assign JumpAddr = Hit ? register_3_q : 32'bz;  // Controlled_Buffer controlled_buffer_1
endmodule

module MAX_WITH_ID (
  input  [15:0] Val1,
  input  [15:0] Val2,
  input  [2:0] Id1,
  input  [2:0] Id2,
  output [2:0] Id,
  output [15:0] Val
);

  wire comparator_1_lt;

  Multiplexer #(.select(1), .width(16), .disabled("Z"), .enable("false")) multiplexer_1 (
    .in0(Val1), .in1(Val2), .out(Val), .sel(comparator_1_lt));
  Comparator #(.width(16), .mode("unsigned")) comparator_1 (.a(Val1), .b(Val2), .lt(comparator_1_lt));  // open: gt, eq
  Multiplexer #(.select(1), .width(3), .disabled("Z"), .enable("false")) multiplexer_2 (
    .in0(Id1), .in1(Id2), .out(Id), .sel(comparator_1_lt));
endmodule

module History (
  input  BranchTaken,
  input  En,
  input  J_Branch,
  input  CLK,
  output Predict
);

  wire and_1_out, and_2_out, and_3_out, and_4_out, and_5_out, and_6_out, not_1_out, not_2_out;
  wire [0:0] register_1_q;
  wire [1:0] multiplexer_1_out, or_2_out;

  and and_1 (and_1_out, register_1_q[0], BranchTaken);
  and and_2 (and_2_out, Predict, BranchTaken);
  and and_3 (and_3_out, Predict, register_1_q[0]);
  not not_1 (not_1_out, register_1_q[0]);
  not not_2 (not_2_out, register_1_q[0]);
  or or_1 (or_2_out[1], and_1_out, and_2_out, and_3_out);
  and and_4 (and_4_out, not_1_out, BranchTaken);
  and and_5 (and_5_out, Predict, not_2_out);
  or or_2 (or_2_out[0], and_4_out, and_5_out, and_6_out);
  and and_6 (and_6_out, Predict, BranchTaken);
  Multiplexer #(.select(1), .width(2), .disabled("Z"), .enable("false")) multiplexer_1 (
    .in0(or_2_out), .in1(2'b10), .out(multiplexer_1_out), .sel(J_Branch));
  Register #(.width(2), .trigger("rising"), .Select("low")) register_1 (
    .D(multiplexer_1_out), .en(En), .Q({Predict, register_1_q[0]}), .clk(CLK));  // open: clr
endmodule

module \气泡重定向动态分支预测  (
  output RegWrite,
  output MemWrite,
  output [31:0] IF_PC,
  output [31:0] ID_PC,
  output [31:0] EX_PC,
  output [31:0] M_PC,
  output [31:0] WB_PC,
  output [31:0] RDin,
  output [31:0] MDin,
  output [31:0] LedData
);

  wire alu_1_out_6, and_1_out, and_2_out, and_4_out, and_5_out, and_6_out, and_7_out, and_8_out, and_9_out,
       and_10_out, and_11_out, Auipc, Beq, Bge, Bne, Branch, BranchTaken, btb_1_predictjump, Byte, CLK,
       clock_1_out, comparator_2_eq, comparator_2_lt, comparator_3_eq, comparator_4_eq, comparator_5_eq,
       d_ff_1_q, Ecall, Equ, EX_Branch, ex_mem_1_auipc_2, ex_mem_1_byte_2, ex_mem_1_ecall_2,
       ex_mem_1_jal_jalr_2, ex_mem_1_less_2, ex_mem_1_memtoreg_2, ex_mem_1_regwrite_2, ex_mem_1_shouldhalt_2,
       ex_mem_1_slt_2, EX_PredictErr, EX_PredictJump, Flush, Geq, Go, halt, id_ex_1_alusrc_2,
       id_ex_1_auipc_2, id_ex_1_beq_2, id_ex_1_bge_2, id_ex_1_bne_2, id_ex_1_byte_2, id_ex_1_ecall_2,
       id_ex_1_jal_2, id_ex_1_jalr_2, id_ex_1_memtoreg_2, id_ex_1_memwrite_2, id_ex_1_regwrite_2,
       if_id_1_predictjump_2, IR1, IR2, IR3, Jal, Jalr, JJump, me_wb_1_ecall_2, me_wb_1_memtoreg_2,
       me_wb_1_shouldhalt_2, nand_1_out, nand_2_out, not_1_out, not_2_out, not_3_out, not_4_out, not_5_out,
       not_6_out, not_7_out, not_8_out, or_1_out, or_3_out, riscv_probe_3_p1, RST, stall, Uret, W1, W2, W3,
       \单周期硬布线控制器_1_alu_src , \单周期硬布线控制器_1_memtoreg , \单周期硬布线控制器_1_memwrite , \单周期硬布线控制器_1_regwrite ,
       \单周期硬布线控制器_1_rsused , \单周期硬布线控制器_1_rtused , \单周期硬布线控制器_1_s_type , \气泡_重定向处理逻辑_1_if_id_clr ,
       \气泡_重定向处理逻辑_1_if_id_en , \气泡_重定向处理逻辑_1_pc_en ;
  wire [1:0] EX_RsFoward, EX_RtFoward, ID_RsFoward, ID_RtFoward, multiplexer_13_out;
  wire [3:0] id_ex_1_aluop_2, \单周期硬布线控制器_1_alu_op ;
  wire [4:0] ex_mem_1_rd_2, id_ex_1_rd_2, me_wb_1_rd_4, multiplexer_3_out, multiplexer_4_out;
  wire [12:0] CNT_num;
  wire [15:0] \LoadUse次数 , \总周期数 , \插入气泡数 , \无条件分支数 , \条件分支成功数 ;
  wire [31:0] adder_1_out, adder_2_out, adder_3_out, adder_4_out, adder_5_out, adder_6_out, alu_1_result,
       and_3_out, bit_extender_1_out, bit_extender_2_out, bit_extender_3_out, bit_extender_4_out,
       bit_extender_5_out, bit_extender_6_out, btb_1_jumpaddr, EX_IR, ex_mem_1_aluresult_2, ex_mem_1_uimm_2,
       EX_RE_RS, EX_RE_RT, EX_RS, EX_RT, id_ex_1_bimm_2, id_ex_1_imm_2, id_ex_1_jimm_2, id_ex_1_uimm_2,
       ID_IR, IF_IR, me_wb_1_aluresult_2, me_wb_1_rd_3, MEM_IR, mips_ram_1_dataout, multiplexer_1_out,
       multiplexer_2_out, multiplexer_5_out, multiplexer_6_out, multiplexer_7_out, multiplexer_8_out,
       multiplexer_9_out, multiplexer_10_out, multiplexer_14_out, multiplexer_15_out, multiplexer_16_out,
       regifile_1_r1, regifile_1_r2, shifter_1_out, shifter_2_out, shifter_3_out, WB_IR;

  Button \u_总复位  (.out(RST));
  Button _1 (.out(IR1));
  Button _2 (.out(IR2));
  Button _3 (.out(IR3));
  // Probe on \总周期数 
  // Probe on \总周期数 
  Button \u_继续运行  (.out(Go));
  LED #(.active("true")) led_1 (.in(W1));
  LED #(.active("true")) led_2 (.in(W2));
  LED #(.active("true")) led_3 (.in(W3));
  not not_1 (not_1_out, halt);
  and and_1 (and_1_out, not_1_out, \气泡_重定向处理逻辑_1_pc_en );
  Multiplexer #(.select(1), .width(32), .disabled("Z"), .enable("false")) multiplexer_1 (
    .in0(multiplexer_2_out), .in1(multiplexer_5_out), .out(multiplexer_1_out), .sel(EX_PredictErr));
  Hex_Digit_Display hex_digit_display_1 (.value(LedData[31:28]));  // open: dp
  // Probe on IF_PC[19:0]
  // RiscV_Probe riscv_probe_1: pin names not known; wires that end beside it: IF_IR
  Register #(.width(32), .trigger("rising"), .Select("low")) PC (
    .D(multiplexer_1_out), .en(and_1_out), .Q(IF_PC), .clk(CLK), .clr(riscv_probe_3_p1));
  Hex_Digit_Display hex_digit_display_2 (.value(LedData[27:24]));  // open: dp
  Hex_Digit_Display hex_digit_display_3 (.value(LedData[23:20]));  // open: dp
  // Probe on ID_PC[19:0]
  // RiscV_Probe riscv_probe_2: pin names not known; wires that end beside it: ID_IR
  Hex_Digit_Display hex_digit_display_4 (.value(LedData[15:12]));  // open: dp
  Hex_Digit_Display hex_digit_display_5 (.value(LedData[19:16]));  // open: dp
  // RiscV_Probe riscv_probe_3: pin names not known; wires that end beside it: riscv_probe_3_p1, RST, IF_IR, IF_IR
  Multiplexer #(.select(1), .width(32), .disabled("Z"), .enable("false")) multiplexer_2 (
    .in0(adder_1_out), .in1(btb_1_jumpaddr), .out(multiplexer_2_out), .sel(btb_1_predictjump));
  Adder #(.width(32)) adder_1 (.a(IF_PC), .b(32'h4), .out(adder_1_out));  // open: cin, cout
  BTB btb_1 (
    .EX_Branch(EX_Branch), .EX_BranchTaken(BranchTaken), .CLK(CLK), .EX_BranchAddr(multiplexer_5_out),
    .EX_PC(EX_PC), .PC(IF_PC), .PredictJump(btb_1_predictjump), .JumpAddr(btb_1_jumpaddr), .J_Branch(JJump));
  Hex_Digit_Display hex_digit_display_6 (.value(LedData[7:4]));  // open: dp
  Hex_Digit_Display hex_digit_display_7 (.value(LedData[11:8]));  // open: dp
  // Probe on EX_PC[19:0]
  // RiscV_Probe riscv_probe_4: pin names not known; wires that end beside it: EX_IR
  not not_2 (not_2_out, halt);
  and and_2 (and_2_out, not_2_out, \气泡_重定向处理逻辑_1_if_id_en );
  ROM #(.addrWidth(10), .dataWidth(32), .Select("high")) rom_1 (.addr(IF_PC[11:2]), .data(IF_IR));
  Hex_Digit_Display hex_digit_display_8 (.value(LedData[3:0]));  // open: dp
  IF_ID if_id_1 (
    .IR(IF_IR), .PC(IF_PC), .IR_2(ID_IR), .PC_2(ID_PC), .CLK(CLK), .Flush(\气泡_重定向处理逻辑_1_if_id_clr ),
    .En(and_2_out), .PredictJump_2(if_id_1_predictjump_2), .PredictJump(btb_1_predictjump));
  // Probe on \总周期数 
  // Probe on M_PC[19:0]
  // RiscV_Probe riscv_probe_5: pin names not known; wires that end beside it: MEM_IR
  // Probe on \总周期数 
  // Probe on \无条件分支数 
  // Probe on \条件分支成功数 
  // Probe on \插入气泡数 
  // Probe on \LoadUse次数 
  \单周期硬布线控制器  \u_单周期硬布线控制器_1  (
    .Funct({ID_IR[30], ID_IR[25], ID_IR[14:12]}), .OP(ID_IR[6:2]), .ALU_OP(\单周期硬布线控制器_1_alu_op ),
    .MemToReg(\单周期硬布线控制器_1_memtoreg ), .MemWrite(\单周期硬布线控制器_1_memwrite ), .ALU_SRC(\单周期硬布线控制器_1_alu_src ),
    .RegWrite(\单周期硬布线控制器_1_regwrite ), .ecall(Ecall), .S_type(\单周期硬布线控制器_1_s_type ), .Jalr(Jalr), .Beq(Beq),
    .JAL(Jal), .Bne(Bne), .in_3(ID_IR[21]), .uret(Uret), .Auipc(Auipc), .Byte(Byte), .BGE(Bge),
    .RsUsed(\单周期硬布线控制器_1_rsused ), .RtUsed(\单周期硬布线控制器_1_rtused ));  // open: CSRRSI, CSRRCI
  Multiplexer #(.select(1), .width(5), .disabled("Z"), .enable("false")) multiplexer_3 (
    .in0(ID_IR[19:15]), .in1(5'b10001), .out(multiplexer_3_out), .sel(Ecall));
  // Probe on multiplexer_3_out
  Multiplexer #(.select(1), .width(5), .disabled("Z"), .enable("false")) multiplexer_4 (
    .in0(ID_IR[24:20]), .in1(5'b01010), .out(multiplexer_4_out), .sel(Ecall));
  // Probe on multiplexer_4_out
  assign bit_extender_1_out = {{20{ID_IR[31]}}, ID_IR[31:20]};  // Bit_Extender bit_extender_1
  assign bit_extender_2_out = {{20{ID_IR[31]}}, {ID_IR[31:25], ID_IR[11:7]}};  // Bit_Extender bit_extender_2
  Multiplexer #(.select(1), .width(32), .disabled("Z"), .enable("false")) multiplexer_5 (
    .in0(adder_5_out), .in1(multiplexer_9_out), .out(multiplexer_5_out), .sel(BranchTaken));
  // Probe on IF_PC[11:0]
  // Probe on WB_PC[19:0]
  // RiscV_Probe riscv_probe_6: pin names not known; wires that end beside it: WB_IR
  Multiplexer #(.select(1), .width(32), .disabled("Z"), .enable("false")) multiplexer_6 (
    .in0(bit_extender_1_out), .in1(bit_extender_2_out), .out(multiplexer_6_out), .sel(\单周期硬布线控制器_1_s_type ));
  assign bit_extender_3_out = {{20{ID_IR[31]}}, {ID_IR[31], ID_IR[7], ID_IR[30:25], ID_IR[11:8]}};  // Bit_Extender bit_extender_3
  assign bit_extender_4_out = {{12{ID_IR[31]}}, {ID_IR[31], ID_IR[19:12], ID_IR[20], ID_IR[30:21]}};  // Bit_Extender bit_extender_4
  assign bit_extender_5_out = {{12{ID_IR[31]}}, ID_IR[31:12]};  // Bit_Extender bit_extender_5
  Shifter #(.width(32), .shift("ll")) shifter_1 (.in(bit_extender_5_out), .\dist (5'b01100), .out(shifter_1_out));
  // Probe on EX_PC[11:0]
  // Probe on ID_PC[11:0]
  not not_3 (not_3_out, CLK);
  Regifile regifile_1 (
    .Din(RDin), .Clk(not_3_out), .R1(regifile_1_r1), .R2(regifile_1_r2), .WE(RegWrite), .W_num(me_wb_1_rd_4),
    .R1_num(multiplexer_3_out), .R2_num(multiplexer_4_out));
  Shifter #(.width(32), .shift("ll")) shifter_2 (.in(bit_extender_3_out), .\dist (5'b00001), .out(shifter_2_out));
  Shifter #(.width(32), .shift("ll")) shifter_3 (.in(bit_extender_4_out), .\dist (5'b00001), .out(shifter_3_out));
  Adder #(.width(32)) adder_2 (.a(shifter_1_out), .b(ID_PC), .out(adder_2_out));  // open: cin, cout
  Comparator #(.width(32), .mode("unsigned")) comparator_1 (
    .a({32{1'b1}}), .b(multiplexer_9_out), .gt(BranchTaken));  // open: eq, lt
  // Probe on M_PC[11:0]
  D_Flip_Flop #(.trigger("high"), .Pre_Clr_Positions("LEGACY"), .NegatePresetClear("false"), .enable("true"), .NewFFLayout("false")) d_ff_1 (.Q(d_ff_1_q));  // open: clk, D, Qn, preset, en, reset
  // Probe on 13'h16
  Adder #(.width(32)) adder_3 (.a(shifter_2_out), .b(ID_PC), .out(adder_3_out));  // open: cin, cout
  Adder #(.width(32)) adder_4 (.a(ID_PC), .b(shifter_3_out), .out(adder_4_out));  // open: cin, cout
  // Probe on WB_PC[11:0]
  Comparator #(.width(13), .mode("twosComplement")) comparator_2 (
    .a(CNT_num), .b(13'h16), .eq(comparator_2_eq), .lt(comparator_2_lt));  // open: gt
  Clock #(.highDuration(1), .lowDuration(1)) clock_1 (.out(clock_1_out));
  not not_4 (not_4_out, halt);
  ID_EX id_ex_1 (
    .RegWrite(\单周期硬布线控制器_1_regwrite ), .R1(regifile_1_r1), .R2(regifile_1_r2), .rd(ID_IR[11:7]),
    .Imm(multiplexer_6_out), .PC(ID_PC), .RegWrite_2(id_ex_1_regwrite_2), .R1_2(EX_RS), .R2_2(EX_RT),
    .rd_2(id_ex_1_rd_2), .Imm_2(id_ex_1_imm_2), .PC_2(EX_PC), .CLK(CLK), .MemToReg(\单周期硬布线控制器_1_memtoreg ),
    .MemToReg_2(id_ex_1_memtoreg_2), .MemWrite(\单周期硬布线控制器_1_memwrite ), .MemWrite_2(id_ex_1_memwrite_2),
    .AluOP(\单周期硬布线控制器_1_alu_op ), .AluOP_2(id_ex_1_aluop_2), .Bne(Bne), .Bne_2(id_ex_1_bne_2),
    .AluSrc(\单周期硬布线控制器_1_alu_src ), .AluSrc_2(id_ex_1_alusrc_2), .Beq(Beq), .Beq_2(id_ex_1_beq_2), .Bge(Bge),
    .Bge_2(id_ex_1_bge_2), .Auipc(Auipc), .Auipc_2(id_ex_1_auipc_2), .Byte(Byte), .Byte_2(id_ex_1_byte_2),
    .Jalr(Jalr), .Jalr_2(id_ex_1_jalr_2), .Jal(Jal), .Jal_2(id_ex_1_jal_2), .BImm(adder_3_out),
    .BImm_2(id_ex_1_bimm_2), .JImm(adder_4_out), .JImm_2(id_ex_1_jimm_2), .UImm(adder_2_out),
    .UImm_2(id_ex_1_uimm_2), .Ecall(Ecall), .Ecall_2(id_ex_1_ecall_2), .IR(ID_IR), .IR_2(EX_IR),
    .Flush(Flush), .En(not_4_out), .RsFoward(ID_RsFoward), .RsFoward_2(EX_RsFoward), .RtFoward(ID_RtFoward),
    .RtFoward_2(EX_RtFoward), .PredictJump(if_id_1_predictjump_2), .PredictJump_2(EX_PredictJump));  // open: Uert, Uert_2
  nand nand_1 (nand_1_out, d_ff_1_q, comparator_2_eq);
  Counter #(.width(13), .max('h1fff), .ongoal("stay"), .trigger("rising"), .behavior("old")) counter_1 (
    .count(comparator_2_lt), .Q(CNT_num), .clk(clock_1_out));  // open: load, D, carry, clr, preset
  or or_1 (or_1_out, id_ex_1_jalr_2, id_ex_1_jal_2);
  Adder #(.width(32)) adder_5 (.a(EX_PC), .b(32'h4), .out(adder_5_out));  // open: cin, cout
  xor xor_1 (EX_PredictErr, EX_PredictJump, BranchTaken);
  assign CLK = nand_1_out ? clock_1_out : 1'bz;  // Controlled_Buffer controlled_buffer_1
  Multiplexer #(.select(1), .width(32), .disabled("Z"), .enable("false")) multiplexer_7 (
    .in0({32{1'b1}}), .in1(and_3_out), .out(multiplexer_7_out), .sel(id_ex_1_jalr_2));
  Pull_Resistor #(.pull(1)) pull_resistor_1 (.node(CLK));
  Multiplexer #(.select(1), .width(32), .disabled("Z"), .enable("false")) multiplexer_8 (
    .in0(multiplexer_7_out), .in1(id_ex_1_bimm_2), .out(multiplexer_8_out), .sel(Branch));
  Multiplexer #(.select(1), .width(32), .disabled("Z"), .enable("false")) multiplexer_9 (
    .in0(multiplexer_8_out), .in1(id_ex_1_jimm_2), .out(multiplexer_9_out), .sel(id_ex_1_jal_2));
  Comparator #(.width(4), .mode("unsigned")) comparator_3 (
    .a(id_ex_1_aluop_2), .b(4'b1100), .eq(comparator_3_eq));  // open: gt, lt
  Comparator #(.width(4), .mode("unsigned")) comparator_4 (
    .a(id_ex_1_aluop_2), .b(4'b1011), .eq(comparator_4_eq));  // open: gt, lt
  Comparator #(.width(32), .mode("twosComplement")) comparator_5 (
    .a(EX_RE_RS), .b(32'h22), .eq(comparator_5_eq));  // open: gt, lt
  nand nand_2 (nand_2_out, comparator_5_eq, id_ex_1_ecall_2);
  Multiplexer #(.select(1), .width(32), .disabled("Z"), .enable("false")) multiplexer_10 (
    .in0(EX_RE_RT), .in1(id_ex_1_imm_2), .out(multiplexer_10_out), .sel(id_ex_1_alusrc_2));
  not not_5 (not_5_out, Equ);
  or or_2 (JJump, id_ex_1_jalr_2, id_ex_1_jal_2);
  or or_3 (or_3_out, comparator_3_eq, comparator_4_eq);
  ALU alu_1 (
    .X(EX_RE_RS), .Y(multiplexer_10_out), .AluOP(id_ex_1_aluop_2), .Equal(Equ), .Result(alu_1_result),
    .out_4(Geq), .out_6(alu_1_out_6));  // open: Result_2
  assign and_3_out = 32'hfffe & alu_1_result;  // AND_Gate and_3, 32 bits wide
  and and_4 (and_4_out, id_ex_1_beq_2, Equ);
  and and_5 (and_5_out, id_ex_1_bne_2, not_5_out);
  and and_6 (and_6_out, id_ex_1_bge_2, Geq);
  or or_4 (Branch, and_6_out, and_5_out, and_4_out);
  or or_5 (EX_Branch, Branch, id_ex_1_jal_2, id_ex_1_jalr_2);
  Multiplexer #(.select(2), .width(32), .disabled("Z"), .enable("false")) multiplexer_11 (
    .in0(EX_RS), .in1(RDin), .in2(multiplexer_16_out), .out(EX_RE_RS), .sel(EX_RsFoward));  // open: in3
  Multiplexer #(.select(2), .width(32), .disabled("Z"), .enable("false")) multiplexer_12 (
    .in0(EX_RT), .in1(RDin), .in2(multiplexer_16_out), .out(EX_RE_RT), .sel(EX_RtFoward));  // open: in3
  Register #(.width(32), .trigger("rising"), .Select("low")) register_1 (
    .D(EX_RE_RT), .en(not_6_out), .Q(LedData), .clk(CLK));  // open: clr
  not not_6 (not_6_out, nand_2_out);
  not not_7 (not_7_out, halt);
  EX_MEM ex_mem_1 (
    .AluResult(alu_1_result), .WriteData(EX_RE_RT), .rd(id_ex_1_rd_2), .AluResult_2(ex_mem_1_aluresult_2),
    .WriteData_2(MDin), .rd_2(ex_mem_1_rd_2), .CLK(CLK), .RegWrite(id_ex_1_regwrite_2),
    .RegWrite_2(ex_mem_1_regwrite_2), .MemToReg(id_ex_1_memtoreg_2), .MemToReg_2(ex_mem_1_memtoreg_2),
    .MemWrite(id_ex_1_memwrite_2), .MemWrite_2(MemWrite), .Byte(id_ex_1_byte_2), .Byte_2(ex_mem_1_byte_2),
    .Ecall(id_ex_1_ecall_2), .Ecall_2(ex_mem_1_ecall_2), .ShouldHalt(nand_2_out),
    .ShouldHalt_2(ex_mem_1_shouldhalt_2), .Auipc(id_ex_1_auipc_2), .Auipc_2(ex_mem_1_auipc_2),
    .Less(alu_1_out_6), .Less_2(ex_mem_1_less_2), .Slt(or_3_out), .Slt_2(ex_mem_1_slt_2),
    .Jal_Jalr(or_1_out), .Jal_Jalr_2(ex_mem_1_jal_jalr_2), .PC(EX_PC), .PC_2(M_PC), .UImm(id_ex_1_uimm_2),
    .UImm_2(ex_mem_1_uimm_2), .IR(EX_IR), .IR_2(MEM_IR), .En(not_7_out), .Flush(1'b0));  // open: Uert_2, Uert
  assign bit_extender_6_out = {{31{1'b0}}, ex_mem_1_less_2};  // Bit_Extender bit_extender_6
  MIPS_RAM mips_ram_1 (
    .\字节地址 (ex_mem_1_aluresult_2[11:0]), .Din(MDin), .DataOut(mips_ram_1_dataout), .CLK(CLK), .WE(MemWrite),
    .Mode(multiplexer_13_out));
  Multiplexer #(.select(1), .width(2), .disabled("Z"), .enable("false")) multiplexer_13 (
    .in0(2'b00), .in1(2'b01), .out(multiplexer_13_out), .sel(ex_mem_1_byte_2));
  Multiplexer #(.select(1), .width(32), .disabled("Z"), .enable("false")) multiplexer_14 (
    .in0(ex_mem_1_aluresult_2), .in1(bit_extender_6_out), .out(multiplexer_14_out), .sel(ex_mem_1_slt_2));
  Adder #(.width(32)) adder_6 (.a(M_PC), .b(32'h4), .out(adder_6_out));  // open: cin, cout
  Multiplexer #(.select(1), .width(32), .disabled("Z"), .enable("false")) multiplexer_15 (
    .in0(multiplexer_14_out), .in1(adder_6_out), .out(multiplexer_15_out), .sel(ex_mem_1_jal_jalr_2));
  \气泡_重定向处理逻辑  \u_气泡_重定向处理逻辑_1  (
    .RsUsed(\单周期硬布线控制器_1_rsused ), .rs(multiplexer_3_out), .RtUsed(\单周期硬布线控制器_1_rtused ),
    .rt(multiplexer_4_out), .MEM_RegWrite(ex_mem_1_regwrite_2), .MEM_WriteReg_V(ex_mem_1_rd_2),
    .EX_WriteReg_V(id_ex_1_rd_2), .BranchTaken(EX_PredictErr), .Stall(stall), .PC_EN(\气泡_重定向处理逻辑_1_pc_en ),
    .IF_ID_EN(\气泡_重定向处理逻辑_1_if_id_en ), .IF_ID_CLR(\气泡_重定向处理逻辑_1_if_id_clr ), .ID_EX_CLR(Flush),
    .EX_MemToReg(id_ex_1_memtoreg_2), .EX_RegWrite(id_ex_1_regwrite_2), .RsFoward(ID_RsFoward),
    .RtFoward(ID_RtFoward));  // open: Flush, LoadUse
  Multiplexer #(.select(1), .width(32), .disabled("Z"), .enable("false")) multiplexer_16 (
    .in0(multiplexer_15_out), .in1(ex_mem_1_uimm_2), .out(multiplexer_16_out), .sel(ex_mem_1_auipc_2));
  not not_8 (not_8_out, halt);
  ME_WB me_wb_1 (
    .RegWrite(ex_mem_1_regwrite_2), .MemToReg(ex_mem_1_memtoreg_2), .AluResult(multiplexer_16_out),
    .RD(mips_ram_1_dataout), .rd_2(ex_mem_1_rd_2), .RegWrite_2(RegWrite), .MemToReg_2(me_wb_1_memtoreg_2),
    .AluResult_2(me_wb_1_aluresult_2), .RD_3(me_wb_1_rd_3), .rd_4(me_wb_1_rd_4), .CLK(CLK),
    .ShouldHalt(ex_mem_1_shouldhalt_2), .ShouldHalt_2(me_wb_1_shouldhalt_2), .Ecall(ex_mem_1_ecall_2),
    .Ecall_2(me_wb_1_ecall_2), .PC(M_PC), .PC_2(WB_PC), .IR(MEM_IR), .IR_2(WB_IR), .En(not_8_out));
  Multiplexer #(.select(1), .width(32), .disabled("Z"), .enable("false")) multiplexer_17 (
    .in0(me_wb_1_aluresult_2), .in1(me_wb_1_rd_3), .out(RDin), .sel(me_wb_1_memtoreg_2));
  D_Flip_Flop #(.trigger("falling"), .Pre_Clr_Positions("ABOVE_BELOW"), .NegatePresetClear("false"), .enable("true"), .NewFFLayout("true")) d_ff_2 (
    .clk(CLK), .D(me_wb_1_shouldhalt_2), .Q(halt), .en(me_wb_1_ecall_2), .reset(Go));  // open: Qn, preset
  Counter #(.width(16), .max('hffff), .ongoal("wrap"), .trigger("rising"), .behavior("new")) counter_2 (
    .count(Branch), .Q(\条件分支成功数 ), .clk(and_7_out), .clr(RST));  // open: load, D, carry, preset, down
  and and_7 (and_7_out, ~halt, CLK);  // AND_Gate
  Counter #(.width(16), .max('hffff), .ongoal("wrap"), .trigger("rising"), .behavior("new")) counter_3 (
    .count(Flush), .Q(\插入气泡数 ), .clk(and_8_out), .clr(RST));  // open: load, D, carry, preset, down
  and and_8 (and_8_out, ~halt, CLK);  // AND_Gate
  Counter #(.width(16), .max('hffff), .ongoal("wrap"), .trigger("rising"), .behavior("new")) counter_4 (
    .count(JJump), .Q(\无条件分支数 ), .clk(and_9_out), .clr(RST));  // open: load, D, carry, preset, down
  and and_9 (and_9_out, ~halt, CLK);  // AND_Gate
  Counter #(.width(16), .max('hffff), .ongoal("wrap"), .trigger("rising"), .behavior("new")) counter_5 (
    .count(CLK), .Q(\总周期数 ), .clk(and_10_out), .clr(RST));  // open: load, D, carry, preset, down
  and and_10 (and_10_out, ~halt, CLK);  // AND_Gate
  and and_11 (and_11_out, ~halt, CLK);  // AND_Gate
  Counter #(.width(16), .max('hffff), .ongoal("wrap"), .trigger("rising"), .behavior("new")) counter_6 (
    .count(stall), .Q(\LoadUse次数 ), .clk(and_11_out), .clr(RST));  // open: load, D, carry, preset, down

  // Other names for the same wires on the sheet: MEM_PC[31:0] = M_PC; PC[31:0] = IF_PC

  // Notes on the sheet:
  //   中断源
  //   时空图监测，可删除
  //   中断等待指示
  //   数码管输出
  //   指令探针
  //   指令存储器
  //   contents of rom_1 (hex, n*v repeats v):
  //   100493 100006f 100493 200913 300993 100006f 100493 200913 300993 100006f 100493 200913 300993
  //   100006f 100493 200913 300993 3ec000ef 100413 100493 1f49493 900533 2200893 73 24d493 48463 fedff06f
  //   900533 2200893 73 100493 249493 900533 2200893 73 48463 fedff06f 100493 1f49493 900533 2200893 73
  //   4034d493 900533 2200893 73 4044d493 900533 2200893 73 4044d493 900533 2200893 73 4044d493 900533
  //   2200893 73 4044d493 900533 2200893 73 4044d493 900533 2200893 73 4044d493 900533 2200893 73 4044d493
  //   900533 2200893 73 100413 1f41993 41f9d993 433 c00913 300b13 140413 f47413 800293 100313 499993
  //   89e9b3 1300533 2200893 73 406282b3 fe0294e3 140413 f00f93 1f47433 1c41413 800293 100313 49d993
  //   89e9b3 1300533 2200893 73 406282b3 fe0294e3 1c45413 406b0b33 b0463 f95ff06f 2b3 fff2c293 829293
  //   ff2e293 500533 2200893 73 fff00413 493 84a023 140413 448493 84a023 140413 448493 84a023 140413
  //   448493 84a023 140413 448493 84a023 140413 448493 84a023 140413 448493 84a023 140413 448493 84a023
  //   140413 448493 84a023 140413 448493 84a023 140413 448493 84a023 140413 448493 84a023 140413 448493
  //   84a023 140413 448493 84a023 140413 448493 84a023 140413 448493 84a023 140413 448493 140413 433
  //   3c00493 42983 4aa03 149a2b3 28663 134a023 1442023 ffc48493 fe9412e3 800533 2200893 73 440413 3c00493
  //   fc9416e3 3200893 73 fff00293 7700493 849493 7748493 900533 2200893 73 1000e13 54c4b3 900533 2200893
  //   73 fffe0e13 fe0e16e3 a00893 73 13 430497 900533 2200893 73 430497 900533 2200893 73 430497 900533
  //   2200893 73 430497 900533 2200893 73 430497 900533 2200893 73 430497 900533 2200893 73 430497 900533
  //   2200893 73 430497 900533 2200893 73 a00893 73 313 2000e13 493 100913 930023 900533 2200893 73
  //   12484b3 130313 fffe0e13 fe0e12e3 800e13 313 32483 900533 2200893 73 430313 fffe0e13 fe0e14e3 a00893
  //   73 f00493 900533 2200893 73 fff48493 fe04d8e3 a00893 73 a00893 73 413 140413 800533 2200893 73
  //   240413 800533 2200893 73 340413 800533 2200893 73 440413 800533 2200893 73 540413 800533 2200893 73
  //   640413 800533 2200893 73 740413 800533 2200893 73 840413 800533 2200893 2200893 73 8067
  //   指令字
  //   JAL
  //   JALR
  //   Beq
  //   Bne
  //   MemToReg
  //   MemWrite
  //   AluOP
  //   AluSrcB
  //   RegWrite
  //   控制位
  //   流水调试日志用
  //   暂停节拍，不能为0
  //   戳工具置1进入计数暂停模式，ctrl+k时钟自动运行到对应节拍暂停
  //   ctrl+k关闭时钟连续运行，将控制位置零，进入单步调试模式调试
  //   可计数暂停的时钟源
  //   为方便自动评测，需要输出流水线各段保存的PC值，注意是PC不是PC+4，另外ID段寄存器写入信息，Mem段内存写入信息也要输出
  //   数据存储器
endmodule
